// Logisim project seq.circ as structural Verilog: 17 circuits, main circuit test
module byHand_TET_RAM (
  input  [13:0] TET,
  input  [13:0] Octaves,
  input  Reset
);

  wire and_1_out, clock_1_out, comparator_1_eq, comparator_2_eq, comparator_3_lt, comparator_4_gt, not_1_out,
       or_1_out;
  wire [13:0] adder_1_out, adder_2_out, adder_3_out, multiplexer_1_out, multiplier_1_out, multiplier_2_out,
       register_1_q, register_2_q, register_3_q, rom_1_data, subtractor_1_out;

  Register #(.width(14)) register_1 (.D(adder_1_out), .en(1'b1), .clk(clock_1_out), .Q(register_1_q), .clr(or_1_out));
  Adder #(.width(14)) adder_1 (.a(register_1_q), .b({14{1'b0}}), .out(adder_1_out), .cin(1'b1));  // open: cout
  or or_1 (or_1_out, Reset, comparator_2_eq);
  Subtractor #(.width(14)) subtractor_1 (.a(TET), .b({14{1'b0}}), .out(subtractor_1_out), .bin(1'b1));  // open: bout
  Comparator #(.mode("unsigned"), .width(14)) comparator_1 (
    .a(subtractor_1_out), .b(register_1_q), .eq(comparator_1_eq));  // open: gt, lt
  Comparator #(.mode("unsigned"), .width(14)) comparator_2 (
    .a(TET), .b(register_1_q), .eq(comparator_2_eq));  // open: gt, lt
  ROM #(.addrWidth(14), .dataWidth(14)) rom_1 (.addr(register_1_q), .data(rom_1_data));
  Adder #(.width(14)) adder_2 (
    .a(register_3_q), .b({14{1'b0}}), .out(adder_2_out), .cin(comparator_1_eq));  // open: cout
  Clock clock_1 (.out(clock_1_out));
  Register #(.width(14)) register_2 (.D(adder_3_out), .en(1'b1), .clk(clock_1_out), .Q(register_2_q), .clr(Reset));
  Adder #(.width(14)) adder_3 (.a(register_2_q), .b({14{1'b0}}), .out(adder_3_out), .cin(1'b1));  // open: cout
  Register #(.width(14)) register_3 (.D(adder_2_out), .en(1'b1), .clk(clock_1_out), .Q(register_3_q), .clr(Reset));
  Comparator #(.width(14)) comparator_3 (.a(register_3_q), .b(Octaves), .lt(comparator_3_lt));  // open: gt, eq
  Multiplier #(.width(14)) multiplier_1 (.a(14'h2), .b(register_3_q), .out(multiplier_1_out));  // open: cin, cout
  and and_1 (and_1_out, clock_1_out, comparator_3_lt);
  Multiplier #(.width(14)) multiplier_2 (
    .a(rom_1_data), .b(multiplexer_1_out), .out(multiplier_2_out));  // open: cin, cout
  Multiplexer #(.width(14)) multiplexer_1 (
    .in0(14'h1), .in1(multiplier_1_out), .out(multiplexer_1_out), .sel(not_1_out));
  not not_1 (not_1_out, comparator_4_gt);
  Comparator #(.width(14)) comparator_4 (.a(14'h1), .b(register_3_q), .gt(comparator_4_gt));  // open: eq, lt
  RAM #(.addrWidth(14), .dataWidth(14), .\type ("nonvolatile")) ram_1 (
    .addr(register_2_q), .we(1'b1), .clk(and_1_out), .din(multiplier_2_out));  // open: oe, dout

  // Notes on the sheet:
  //   contents of rom_1 (hex, n*v repeats v):
  //   37 3a 3e 41 45 49 4e 52 57 5c 62 68
  //   "Octaver"
endmodule

module test (
  input  [13:0] in_1,
  input  in_2,
  input  in_3,
  input  [6:0] in_4,
  input  [13:0] in_5,
  input  in_6,
  input  [13:0] in_7,
  input  in_8,
  input  in_9,
  input  [6:0] in_10,
  input  [13:0] in_11,
  input  [13:0] in_12,
  input  [13:0] in_13,
  input  [13:0] in_14,
  input  in_15,
  input  in_16,
  input  [6:0] in_17,
  output [13:0] out_18
);

  wire clock_1_out, clock_2_out, clock_3_out;
  wire [13:0] adder_1_out, adder_2_out, adder_3_out, random_1_out, register_1_q, register_2_q, register_3_q,
       register_4_q, rom_1_data, rom_2_data, rom_3_data, subtractor_1_out;

  Clock clock_1 (.out(clock_1_out));
  Clock clock_2 (.out(clock_2_out));
  Adder #(.width(14)) adder_1 (.a(register_2_q), .b(in_14), .out(adder_1_out));  // open: cin, cout
  Random #(.width(14)) random_1 (.next(clock_2_out), .clk(clock_2_out), .out(random_1_out));  // open: clr
  Adder #(.width(14)) adder_2 (.a(register_3_q), .b(in_1), .out(adder_2_out));  // open: cin, cout
  Register #(.width(14)) register_1 (.D(adder_3_out), .en(1'b1), .clk(clock_2_out), .Q(register_1_q), .clr(in_8));
  Adder #(.width(14)) adder_3 (.a(register_1_q), .b(in_7), .out(adder_3_out));  // open: cin, cout
  Register #(.width(14)) register_2 (.D(adder_1_out), .en(1'b1), .clk(1'b1), .Q(register_2_q), .clr(in_15));
  Register #(.width(14)) register_3 (.D(adder_2_out), .en(1'b1), .clk(clock_1_out), .Q(register_3_q), .clr(in_2));
  ROM #(.addrWidth(14), .dataWidth(14)) rom_1 (.addr(register_3_q), .data(rom_1_data));
  ROM #(.addrWidth(14), .dataWidth(14)) rom_2 (.addr(register_1_q), .data(rom_2_data));
  ROM #(.addrWidth(14), .dataWidth(14)) rom_3 (.addr(register_2_q), .data(rom_3_data));
  // Buzzer buzzer_1: pin names not known; wires that end beside it: rom_1_data, in_3, in_4
  // Buzzer buzzer_2: pin names not known; wires that end beside it: rom_2_data, in_9, in_10
  // Buzzer buzzer_3: pin names not known; wires that end beside it: rom_3_data, in_16, in_17
  Clock clock_3 (.out(clock_3_out));
  Subtractor #(.width(14)) subtractor_1 (.a(register_4_q), .b(in_5), .out(subtractor_1_out));  // open: bin, bout
  Register #(.width(14)) register_4 (.D(subtractor_1_out), .en(1'b1), .clk(clock_3_out), .Q(register_4_q), .clr(in_6));
  Divider #(.width(14)) divider_1 (.a(in_11), .b(in_12), .rem(out_18));  // open: out, upper
  Comparator #(.mode("unsigned"), .width(14)) comparator_1 (.a(in_13), .b(out_18));  // open: gt, eq, lt

  // Notes on the sheet:
  //   contents of rom_1 (hex, n*v repeats v):
  //   37 38 39 39 3a 3b 3c 3d 3e 3f 40 40 41 42 43 44 45 46 47 48 49 4a 4c 4d 4e 4f 50 51 52 54 55 56 57
  //   59 5a 5b 5c 5e 5f 61 62 63 65 66 68 69 6b 6c 6e 70 71 73 75 76 78 7a 7b 7d 7f 81 83 85 87 89 8b 8d
  //   8f 91 93 95 97 99 9c 9e a0 a2 a5 a7 aa ac af b1 b4 b6 b9 bc be c1 c4 c7 ca cd d0 d3 d6 d9 dc df e2
  //   e6 e9 ec f0 f3 f7 fb fe 102 106 109 10d 111 115 119 11d 121 126 12a 12e 133 137 13c 140 145 14a 14e
  //   153 158 15d 162 167 16d 172 177 17d 182 188 18e 193 199 19f 1a5 1ab 1b2
  //   contents of rom_2 (hex, n*v repeats v):
  //   37 3a 3e 41 45 49 4e 52 57 5c 62 68 6e 75 7b 83 8b 93 9c a5 af b9 c4 d0 dc e9 f7 106 115 126 137 14a
  //   15d 172 188 19f 1b8 1d2 1ee 20b 22a 24b 26e 293 2ba 2e4 310 33f 370 3a4 3dc 417 455 497 4dd 527 575
  //   5c8 620 67d 6e0 749 7b8 82d 8a9 92d 9b9 a4d aea b90 c40 cfa dc0 e91 f6f 105a 1153 125b 1372 149a
  //   15d4 1720 1880 19f5 1b80 1d23 1ede 20b4 22a6 24b5 26e4 2934 2ba7 2e40 3100 33ea
  //   contents of rom_3 (hex, n*v repeats v):
  //   37 3a 3e 41 45 49 4e 52 57 5c 62 68 6e 75 7b 83 8b 93 9c a5 af b9 c4 d0 dc e9 f7 106 115 126 137 14a
  //   15d 172 188 19f 1b8 1d2 1ee 20b 22a 24b 26e 293 2ba 2e4 310 33f 370 3a4 3dc 417 455 497 4dd 527 575
  //   5c8 620 67d 6e0 749 7b8 82d 8a9 92d 9b9 a4d aea b90 c40 cfa dc0 e91 f6f 105a 1153 125b 1372 149a
  //   15d4 1720 1880 19f5 1b80 1d23 1ede 20b4 22a6 24b5 26e4 2934 2ba7 2e40 3100 33ea
  //   12TET
  //   24TET
endmodule

module byHand_Rand (
  input  [5:0] in_1
);

  wire clock_1_out, comparator_1_lt;
  wire [5:0] demultiplexer_1_out0, demultiplexer_1_out1, multiplexer_1_out, random_1_out, subtractor_1_out;

  Clock clock_1 (.out(clock_1_out));
  Random #(.width(6)) random_1 (.clk(clock_1_out), .out(random_1_out));  // open: clr, next
  Comparator #(.mode("unsigned"), .width(6)) comparator_1 (
    .a(in_1), .b(random_1_out), .lt(comparator_1_lt));  // open: gt, eq
  Demultiplexer #(.width(6)) demultiplexer_1 (
    .out0(demultiplexer_1_out0), .out1(demultiplexer_1_out1), .in(random_1_out), .sel(comparator_1_lt));
  Subtractor #(.width(6)) subtractor_1 (.a(demultiplexer_1_out1), .b(in_1), .out(subtractor_1_out));  // open: bin, bout
  Multiplexer #(.width(6)) multiplexer_1 (
    .in0(demultiplexer_1_out0), .in1(subtractor_1_out), .out(multiplexer_1_out), .sel(comparator_1_lt));
  ROM #(.addrWidth(6), .dataWidth(14)) rom_1 (.addr(multiplexer_1_out));  // open: data
  Divider divider_1 ();  // open: a, b, out, upper, rem
  Adder adder_1 ();  // open: a, b, out, cin, cout
  RAM #(.addrWidth(6), .dataWidth(14)) ram_1 ();  // open: addr, we, oe, clk, din, dout

  // Notes on the sheet:
  //   TET * Octaves
  //   contents of rom_1 (hex, n*v repeats v):
  //   dc e9 f7 106 115 126 137 14a 15d 172 188 19f 1b8 1d2 1ee 20b 22a 24b 26e 293 2ba 2e4 310 33f 370 3a4
  //   3dc 417 455 497 4dd 527 575 5c8 620 67d 6e0 749 7b8 82d 8a9 92d 9b9 a4d aea b90 c40 cfa
endmodule

module Synth (
  input  in_1,
  input  in_2,
  input  [6:0] in_3,
  input  [1:0] in_4
);

  wire button_1_out, button_2_out, buzzer_1_p3, demultiplexer_1_out0, demultiplexer_1_out1,
       demultiplexer_1_out2, demultiplexer_1_out3, demultiplexer_2_out0, demultiplexer_2_out1,
       demultiplexer_2_out2, demultiplexer_2_out3, xor_1_out, xor_2_out;
  wire [1:0] buzzer_2_p1;
  wire [6:0] slider_1_out;
  wire [13:0] rom_1_data, rom_2_data;

  Button button_1 (.out(button_1_out));
  xor xor_1 (xor_1_out, in_2, button_1_out);
  Demultiplexer #(.select(2)) demultiplexer_1 (
    .out0(demultiplexer_1_out0), .out1(demultiplexer_1_out1), .out2(demultiplexer_1_out2),
    .out3(demultiplexer_1_out3), .in(xor_1_out), .sel(buzzer_2_p1));
  ROM #(.addrWidth(2), .dataWidth(14)) rom_1 (.addr(2'b00), .data(rom_1_data));
  // Buzzer #(.waveform("Square")) buzzer_1: pin names not known; wires that end beside it: rom_1_data, demultiplexer_1_out1, buzzer_1_p3
  // Buzzer buzzer_2: pin names not known; wires that end beside it: buzzer_2_p1, buzzer_2_p1, buzzer_2_p1, rom_1_data, demultiplexer_1_out0, buzzer_1_p3
  // Buzzer #(.waveform("Noise")) buzzer_3: pin names not known; wires that end beside it: rom_1_data, demultiplexer_1_out3, buzzer_1_p3, buzzer_1_p3, buzzer_1_p3, buzzer_1_p3
  // Buzzer #(.waveform("Triangle")) buzzer_4: pin names not known; wires that end beside it: rom_1_data, demultiplexer_1_out2, buzzer_1_p3
  Slider #(.width(7)) slider_1 (.out(slider_1_out));
  Button button_2 (.out(button_2_out));
  xor xor_2 (xor_2_out, in_1, button_2_out);
  Demultiplexer #(.select(2)) demultiplexer_2 (
    .out0(demultiplexer_2_out0), .out1(demultiplexer_2_out1), .out2(demultiplexer_2_out2),
    .out3(demultiplexer_2_out3), .in(xor_2_out), .sel(in_4));
  ROM #(.addrWidth(7), .dataWidth(14)) rom_2 (.addr(slider_1_out), .data(rom_2_data));
  // Buzzer buzzer_5: pin names not known; wires that end beside it: rom_2_data, demultiplexer_2_out0, in_3
  // Buzzer #(.waveform("Triangle")) buzzer_6: pin names not known; wires that end beside it: rom_2_data, demultiplexer_2_out2, in_3
  // Buzzer #(.waveform("Square")) buzzer_7: pin names not known; wires that end beside it: rom_2_data, demultiplexer_2_out1, in_3
  // Buzzer #(.waveform("Noise")) buzzer_8: pin names not known; wires that end beside it: rom_2_data, demultiplexer_2_out3, in_3

  // Notes on the sheet:
  //   contents of rom_1 (hex, n*v repeats v):
  //   37
  //   contents of rom_2 (hex, n*v repeats v):
  //   37 3a 3e 41 45 49 4e 52 57 5c 62 68 6e 75 7b 83 8b 93 9c a5 af b9 c4 d0 dc e9 f7 106 115 126 137 14a
  //   15d 172 188 19f 1b8 1d2 1ee 20b 22a 24b 26e 293 2ba 2e4 310 33f 370 3a4 3dc 417 455 497 4dd 527 575
  //   5c8 620 67d 6e0 749 7b8 82d 8a9 92d 9b9 a4d aea b90 c40 cfa dc0 e91 f6f 105a 1153 125b 1372 149a
  //   15d4 1720 1880 19f5 1b80 1d23 1ede 20b4 22a6 24b5 26e4 2934 2ba7 2e40 3100 33ea
endmodule
module Synth_12TET_8_Octaves (
  input  [1:0] Waveform,
  input  [6:0] Volume,
  input  A0,
  input  in_4,
  input  in_5,
  input  in_6,
  input  in_7,
  input  in_8,
  input  in_9,
  input  in_10,
  input  in_11,
  input  in_12,
  input  in_13,
  input  in_14,
  input  A1,
  input  in_16,
  input  in_17,
  input  in_18,
  input  in_19,
  input  in_20,
  input  in_21,
  input  in_22,
  input  in_23,
  input  in_24,
  input  in_25,
  input  in_26,
  input  A2,
  input  in_28,
  input  in_29,
  input  in_30,
  input  in_31,
  input  in_32,
  input  in_33,
  input  in_34,
  input  in_35,
  input  in_36,
  input  in_37,
  input  in_38,
  input  A3,
  input  in_40,
  input  in_41,
  input  in_42,
  input  in_43,
  input  in_44,
  input  in_45,
  input  in_46,
  input  in_47,
  input  in_48,
  input  in_49,
  input  in_50,
  input  A4,
  input  in_52,
  input  in_53,
  input  in_54,
  input  in_55,
  input  in_56,
  input  in_57,
  input  in_58,
  input  in_59,
  input  in_60,
  input  in_61,
  input  in_62,
  input  A5,
  input  in_64,
  input  in_65,
  input  in_66,
  input  in_67,
  input  in_68,
  input  in_69,
  input  in_70,
  input  in_71,
  input  in_72,
  input  in_73,
  input  in_74,
  input  A6,
  input  in_76,
  input  in_77,
  input  in_78,
  input  in_79,
  input  in_80,
  input  in_81,
  input  in_82,
  input  in_83,
  input  in_84,
  input  in_85,
  input  in_86,
  input  A7,
  input  in_88,
  input  in_89,
  input  in_90,
  input  in_91,
  input  in_92,
  input  in_93,
  input  in_94,
  input  in_95,
  input  in_96,
  input  in_97,
  input  in_98,
  input  A8,
  input  in_100,
  input  in_101,
  input  in_102,
  input  in_103,
  input  in_104,
  input  in_105,
  input  in_106,
  input  in_107,
  input  in_108,
  input  in_109,
  input  in_110
);

  wire button_1_out, button_2_out, button_3_out, button_4_out, button_5_out, button_6_out, button_7_out,
       button_8_out, button_9_out, button_10_out, button_11_out, button_12_out, button_13_out, button_14_out,
       button_15_out, button_16_out, button_17_out, button_18_out, button_19_out, button_20_out,
       button_21_out, button_22_out, button_23_out, button_24_out, button_25_out, button_26_out,
       button_27_out, button_28_out, button_29_out, button_30_out, button_31_out, button_32_out,
       button_33_out, button_34_out, button_35_out, button_36_out, button_37_out, button_38_out,
       button_39_out, button_40_out, button_41_out, button_42_out, button_43_out, button_44_out,
       button_45_out, button_46_out, button_47_out, button_48_out, button_49_out, button_50_out,
       button_51_out, button_52_out, button_53_out, button_54_out, button_55_out, button_56_out,
       button_57_out, button_58_out, button_59_out, button_60_out, button_61_out, button_62_out,
       button_63_out, button_64_out, button_65_out, button_66_out, button_67_out, button_68_out,
       button_69_out, button_70_out, button_71_out, button_72_out, button_73_out, button_74_out,
       button_75_out, button_76_out, button_77_out, button_78_out, button_79_out, button_80_out,
       button_81_out, button_82_out, button_83_out, button_84_out, button_85_out, button_86_out,
       button_87_out, button_88_out, button_89_out, button_90_out, button_91_out, button_92_out,
       button_93_out, button_94_out, button_95_out, button_96_out, button_97_out, button_98_out,
       button_99_out, button_100_out, button_101_out, button_102_out, button_103_out, button_104_out,
       button_105_out, button_106_out, button_107_out, button_108_out, demultiplexer_1_out0,
       demultiplexer_1_out1, demultiplexer_1_out2, demultiplexer_1_out3, demultiplexer_2_out0,
       demultiplexer_2_out1, demultiplexer_2_out2, demultiplexer_2_out3, demultiplexer_3_out0,
       demultiplexer_3_out1, demultiplexer_3_out2, demultiplexer_3_out3, demultiplexer_4_out0,
       demultiplexer_4_out1, demultiplexer_4_out2, demultiplexer_4_out3, demultiplexer_5_out0,
       demultiplexer_5_out1, demultiplexer_5_out2, demultiplexer_5_out3, demultiplexer_6_out0,
       demultiplexer_6_out1, demultiplexer_6_out2, demultiplexer_6_out3, demultiplexer_7_out0,
       demultiplexer_7_out1, demultiplexer_7_out2, demultiplexer_7_out3, demultiplexer_8_out0,
       demultiplexer_8_out1, demultiplexer_8_out2, demultiplexer_8_out3, demultiplexer_9_out0,
       demultiplexer_9_out1, demultiplexer_9_out2, demultiplexer_9_out3, demultiplexer_10_out0,
       demultiplexer_10_out1, demultiplexer_10_out2, demultiplexer_10_out3, demultiplexer_11_out0,
       demultiplexer_11_out1, demultiplexer_11_out2, demultiplexer_11_out3, demultiplexer_12_out0,
       demultiplexer_12_out1, demultiplexer_12_out2, demultiplexer_12_out3, demultiplexer_13_out0,
       demultiplexer_13_out1, demultiplexer_13_out2, demultiplexer_13_out3, demultiplexer_14_out0,
       demultiplexer_14_out1, demultiplexer_14_out2, demultiplexer_14_out3, demultiplexer_15_out0,
       demultiplexer_15_out1, demultiplexer_15_out2, demultiplexer_15_out3, demultiplexer_16_out0,
       demultiplexer_16_out1, demultiplexer_16_out2, demultiplexer_16_out3, demultiplexer_17_out0,
       demultiplexer_17_out1, demultiplexer_17_out2, demultiplexer_17_out3, demultiplexer_18_out0,
       demultiplexer_18_out1, demultiplexer_18_out2, demultiplexer_18_out3, demultiplexer_19_out0,
       demultiplexer_19_out1, demultiplexer_19_out2, demultiplexer_19_out3, demultiplexer_20_out0,
       demultiplexer_20_out1, demultiplexer_20_out2, demultiplexer_20_out3, demultiplexer_21_out0,
       demultiplexer_21_out1, demultiplexer_21_out2, demultiplexer_21_out3, demultiplexer_22_out0,
       demultiplexer_22_out1, demultiplexer_22_out2, demultiplexer_22_out3, demultiplexer_23_out0,
       demultiplexer_23_out1, demultiplexer_23_out2, demultiplexer_23_out3, demultiplexer_24_out0,
       demultiplexer_24_out1, demultiplexer_24_out2, demultiplexer_24_out3, demultiplexer_25_out0,
       demultiplexer_25_out1, demultiplexer_25_out2, demultiplexer_25_out3, demultiplexer_26_out0,
       demultiplexer_26_out1, demultiplexer_26_out2, demultiplexer_26_out3, demultiplexer_27_out0,
       demultiplexer_27_out1, demultiplexer_27_out2, demultiplexer_27_out3, demultiplexer_28_out0,
       demultiplexer_28_out1, demultiplexer_28_out2, demultiplexer_28_out3, demultiplexer_29_out0,
       demultiplexer_29_out1, demultiplexer_29_out2, demultiplexer_29_out3, demultiplexer_30_out0,
       demultiplexer_30_out1, demultiplexer_30_out2, demultiplexer_30_out3, demultiplexer_31_out0,
       demultiplexer_31_out1, demultiplexer_31_out2, demultiplexer_31_out3, demultiplexer_32_out0,
       demultiplexer_32_out1, demultiplexer_32_out2, demultiplexer_32_out3, demultiplexer_33_out0,
       demultiplexer_33_out1, demultiplexer_33_out2, demultiplexer_33_out3, demultiplexer_34_out0,
       demultiplexer_34_out1, demultiplexer_34_out2, demultiplexer_34_out3, demultiplexer_35_out0,
       demultiplexer_35_out1, demultiplexer_35_out2, demultiplexer_35_out3, demultiplexer_36_out0,
       demultiplexer_36_out1, demultiplexer_36_out2, demultiplexer_36_out3, demultiplexer_37_out0,
       demultiplexer_37_out1, demultiplexer_37_out2, demultiplexer_37_out3, demultiplexer_38_out0,
       demultiplexer_38_out1, demultiplexer_38_out2, demultiplexer_38_out3, demultiplexer_39_out0,
       demultiplexer_39_out1, demultiplexer_39_out2, demultiplexer_39_out3, demultiplexer_40_out0,
       demultiplexer_40_out1, demultiplexer_40_out2, demultiplexer_40_out3, demultiplexer_41_out0,
       demultiplexer_41_out1, demultiplexer_41_out2, demultiplexer_41_out3, demultiplexer_42_out0,
       demultiplexer_42_out1, demultiplexer_42_out2, demultiplexer_42_out3, demultiplexer_43_out0,
       demultiplexer_43_out1, demultiplexer_43_out2, demultiplexer_43_out3, demultiplexer_44_out0,
       demultiplexer_44_out1, demultiplexer_44_out2, demultiplexer_44_out3, demultiplexer_45_out0,
       demultiplexer_45_out1, demultiplexer_45_out2, demultiplexer_45_out3, demultiplexer_46_out0,
       demultiplexer_46_out1, demultiplexer_46_out2, demultiplexer_46_out3, demultiplexer_47_out0,
       demultiplexer_47_out1, demultiplexer_47_out2, demultiplexer_47_out3, demultiplexer_48_out0,
       demultiplexer_48_out1, demultiplexer_48_out2, demultiplexer_48_out3, demultiplexer_49_out0,
       demultiplexer_49_out1, demultiplexer_49_out2, demultiplexer_49_out3, demultiplexer_50_out0,
       demultiplexer_50_out1, demultiplexer_50_out2, demultiplexer_50_out3, demultiplexer_51_out0,
       demultiplexer_51_out1, demultiplexer_51_out2, demultiplexer_51_out3, demultiplexer_52_out0,
       demultiplexer_52_out1, demultiplexer_52_out2, demultiplexer_52_out3, demultiplexer_53_out0,
       demultiplexer_53_out1, demultiplexer_53_out2, demultiplexer_53_out3, demultiplexer_54_out0,
       demultiplexer_54_out1, demultiplexer_54_out2, demultiplexer_54_out3, demultiplexer_55_out0,
       demultiplexer_55_out1, demultiplexer_55_out2, demultiplexer_55_out3, demultiplexer_56_out0,
       demultiplexer_56_out1, demultiplexer_56_out2, demultiplexer_56_out3, demultiplexer_57_out0,
       demultiplexer_57_out1, demultiplexer_57_out2, demultiplexer_57_out3, demultiplexer_58_out0,
       demultiplexer_58_out1, demultiplexer_58_out2, demultiplexer_58_out3, demultiplexer_59_out0,
       demultiplexer_59_out1, demultiplexer_59_out2, demultiplexer_59_out3, demultiplexer_60_out0,
       demultiplexer_60_out1, demultiplexer_60_out2, demultiplexer_60_out3, demultiplexer_61_out0,
       demultiplexer_61_out1, demultiplexer_61_out2, demultiplexer_61_out3, demultiplexer_62_out0,
       demultiplexer_62_out1, demultiplexer_62_out2, demultiplexer_62_out3, demultiplexer_63_out0,
       demultiplexer_63_out1, demultiplexer_63_out2, demultiplexer_63_out3, demultiplexer_64_out0,
       demultiplexer_64_out1, demultiplexer_64_out2, demultiplexer_64_out3, demultiplexer_65_out0,
       demultiplexer_65_out1, demultiplexer_65_out2, demultiplexer_65_out3, demultiplexer_66_out0,
       demultiplexer_66_out1, demultiplexer_66_out2, demultiplexer_66_out3, demultiplexer_67_out0,
       demultiplexer_67_out1, demultiplexer_67_out2, demultiplexer_67_out3, demultiplexer_68_out0,
       demultiplexer_68_out1, demultiplexer_68_out2, demultiplexer_68_out3, demultiplexer_69_out0,
       demultiplexer_69_out1, demultiplexer_69_out2, demultiplexer_69_out3, demultiplexer_70_out0,
       demultiplexer_70_out1, demultiplexer_70_out2, demultiplexer_70_out3, demultiplexer_71_out0,
       demultiplexer_71_out1, demultiplexer_71_out2, demultiplexer_71_out3, demultiplexer_72_out0,
       demultiplexer_72_out1, demultiplexer_72_out2, demultiplexer_72_out3, demultiplexer_73_out0,
       demultiplexer_73_out1, demultiplexer_73_out2, demultiplexer_73_out3, demultiplexer_74_out0,
       demultiplexer_74_out1, demultiplexer_74_out2, demultiplexer_74_out3, demultiplexer_75_out0,
       demultiplexer_75_out1, demultiplexer_75_out2, demultiplexer_75_out3, demultiplexer_76_out0,
       demultiplexer_76_out1, demultiplexer_76_out2, demultiplexer_76_out3, demultiplexer_77_out0,
       demultiplexer_77_out1, demultiplexer_77_out2, demultiplexer_77_out3, demultiplexer_78_out0,
       demultiplexer_78_out1, demultiplexer_78_out2, demultiplexer_78_out3, demultiplexer_79_out0,
       demultiplexer_79_out1, demultiplexer_79_out2, demultiplexer_79_out3, demultiplexer_80_out0,
       demultiplexer_80_out1, demultiplexer_80_out2, demultiplexer_80_out3, demultiplexer_81_out0,
       demultiplexer_81_out1, demultiplexer_81_out2, demultiplexer_81_out3, demultiplexer_82_out0,
       demultiplexer_82_out1, demultiplexer_82_out2, demultiplexer_82_out3, demultiplexer_83_out0,
       demultiplexer_83_out1, demultiplexer_83_out2, demultiplexer_83_out3, demultiplexer_84_out0,
       demultiplexer_84_out1, demultiplexer_84_out2, demultiplexer_84_out3, demultiplexer_85_out0,
       demultiplexer_85_out1, demultiplexer_85_out2, demultiplexer_85_out3, demultiplexer_86_out0,
       demultiplexer_86_out1, demultiplexer_86_out2, demultiplexer_86_out3, demultiplexer_87_out0,
       demultiplexer_87_out1, demultiplexer_87_out2, demultiplexer_87_out3, demultiplexer_88_out0,
       demultiplexer_88_out1, demultiplexer_88_out2, demultiplexer_88_out3, demultiplexer_89_out0,
       demultiplexer_89_out1, demultiplexer_89_out2, demultiplexer_89_out3, demultiplexer_90_out0,
       demultiplexer_90_out1, demultiplexer_90_out2, demultiplexer_90_out3, demultiplexer_91_out0,
       demultiplexer_91_out1, demultiplexer_91_out2, demultiplexer_91_out3, demultiplexer_92_out0,
       demultiplexer_92_out1, demultiplexer_92_out2, demultiplexer_92_out3, demultiplexer_93_out0,
       demultiplexer_93_out1, demultiplexer_93_out2, demultiplexer_93_out3, demultiplexer_94_out0,
       demultiplexer_94_out1, demultiplexer_94_out2, demultiplexer_94_out3, demultiplexer_95_out0,
       demultiplexer_95_out1, demultiplexer_95_out2, demultiplexer_95_out3, demultiplexer_96_out0,
       demultiplexer_96_out1, demultiplexer_96_out2, demultiplexer_96_out3, demultiplexer_97_out0,
       demultiplexer_97_out1, demultiplexer_97_out2, demultiplexer_97_out3, demultiplexer_98_out0,
       demultiplexer_98_out1, demultiplexer_98_out2, demultiplexer_98_out3, demultiplexer_99_out0,
       demultiplexer_99_out1, demultiplexer_99_out2, demultiplexer_99_out3, demultiplexer_100_out0,
       demultiplexer_100_out1, demultiplexer_100_out2, demultiplexer_100_out3, demultiplexer_101_out0,
       demultiplexer_101_out1, demultiplexer_101_out2, demultiplexer_101_out3, demultiplexer_102_out0,
       demultiplexer_102_out1, demultiplexer_102_out2, demultiplexer_102_out3, demultiplexer_103_out0,
       demultiplexer_103_out1, demultiplexer_103_out2, demultiplexer_103_out3, demultiplexer_104_out0,
       demultiplexer_104_out1, demultiplexer_104_out2, demultiplexer_104_out3, demultiplexer_105_out0,
       demultiplexer_105_out1, demultiplexer_105_out2, demultiplexer_105_out3, demultiplexer_106_out0,
       demultiplexer_106_out1, demultiplexer_106_out2, demultiplexer_106_out3, demultiplexer_107_out0,
       demultiplexer_107_out1, demultiplexer_107_out2, demultiplexer_107_out3, demultiplexer_108_out0,
       demultiplexer_108_out1, demultiplexer_108_out2, demultiplexer_108_out3, xor_1_out, xor_2_out,
       xor_3_out, xor_4_out, xor_5_out, xor_6_out, xor_7_out, xor_8_out, xor_9_out, xor_10_out, xor_11_out,
       xor_12_out, xor_13_out, xor_14_out, xor_15_out, xor_16_out, xor_17_out, xor_18_out, xor_19_out,
       xor_20_out, xor_21_out, xor_22_out, xor_23_out, xor_24_out, xor_25_out, xor_26_out, xor_27_out,
       xor_28_out, xor_29_out, xor_30_out, xor_31_out, xor_32_out, xor_33_out, xor_34_out, xor_35_out,
       xor_36_out, xor_37_out, xor_38_out, xor_39_out, xor_40_out, xor_41_out, xor_42_out, xor_43_out,
       xor_44_out, xor_45_out, xor_46_out, xor_47_out, xor_48_out, xor_49_out, xor_50_out, xor_51_out,
       xor_52_out, xor_53_out, xor_54_out, xor_55_out, xor_56_out, xor_57_out, xor_58_out, xor_59_out,
       xor_60_out, xor_61_out, xor_62_out, xor_63_out, xor_64_out, xor_65_out, xor_66_out, xor_67_out,
       xor_68_out, xor_69_out, xor_70_out, xor_71_out, xor_72_out, xor_73_out, xor_74_out, xor_75_out,
       xor_76_out, xor_77_out, xor_78_out, xor_79_out, xor_80_out, xor_81_out, xor_82_out, xor_83_out,
       xor_84_out, xor_85_out, xor_86_out, xor_87_out, xor_88_out, xor_89_out, xor_90_out, xor_91_out,
       xor_92_out, xor_93_out, xor_94_out, xor_95_out, xor_96_out, xor_97_out, xor_98_out, xor_99_out,
       xor_100_out, xor_101_out, xor_102_out, xor_103_out, xor_104_out, xor_105_out, xor_106_out,
       xor_107_out, xor_108_out;
  wire [13:0] rom_1_data, rom_2_data, rom_3_data, rom_4_data, rom_5_data, rom_6_data, rom_7_data, rom_8_data,
       rom_9_data, rom_10_data, rom_11_data, rom_12_data, rom_13_data, rom_14_data, rom_15_data, rom_16_data,
       rom_17_data, rom_18_data, rom_19_data, rom_20_data, rom_21_data, rom_22_data, rom_23_data,
       rom_24_data, rom_25_data, rom_26_data, rom_27_data, rom_28_data, rom_29_data, rom_30_data,
       rom_31_data, rom_32_data, rom_33_data, rom_34_data, rom_35_data, rom_36_data, rom_37_data,
       rom_38_data, rom_39_data, rom_40_data, rom_41_data, rom_42_data, rom_43_data, rom_44_data,
       rom_45_data, rom_46_data, rom_47_data, rom_48_data, rom_49_data, rom_50_data, rom_51_data,
       rom_52_data, rom_53_data, rom_54_data, rom_55_data, rom_56_data, rom_57_data, rom_58_data,
       rom_59_data, rom_60_data, rom_61_data, rom_62_data, rom_63_data, rom_64_data, rom_65_data,
       rom_66_data, rom_67_data, rom_68_data, rom_69_data, rom_70_data, rom_71_data, rom_72_data,
       rom_73_data, rom_74_data, rom_75_data, rom_76_data, rom_77_data, rom_78_data, rom_79_data,
       rom_80_data, rom_81_data, rom_82_data, rom_83_data, rom_84_data, rom_85_data, rom_86_data,
       rom_87_data, rom_88_data, rom_89_data, rom_90_data, rom_91_data, rom_92_data, rom_93_data,
       rom_94_data, rom_95_data, rom_96_data, rom_97_data, rom_98_data, rom_99_data, rom_100_data,
       rom_101_data, rom_102_data, rom_103_data, rom_104_data, rom_105_data, rom_106_data, rom_107_data,
       rom_108_data;

  Button button_1 (.out(button_1_out));
  xor xor_1 (xor_1_out, A0, button_1_out);
  Demultiplexer #(.select(2)) demultiplexer_1 (
    .out0(demultiplexer_1_out0), .out1(demultiplexer_1_out1), .out2(demultiplexer_1_out2),
    .out3(demultiplexer_1_out3), .in(xor_1_out), .sel(Waveform));
  ROM #(.addrWidth(2), .dataWidth(14)) rom_1 (.addr(2'b00), .data(rom_1_data));
  Button button_2 (.out(button_2_out));
  xor xor_2 (xor_2_out, A1, button_2_out);
  Demultiplexer #(.select(2)) demultiplexer_2 (
    .out0(demultiplexer_2_out0), .out1(demultiplexer_2_out1), .out2(demultiplexer_2_out2),
    .out3(demultiplexer_2_out3), .in(xor_2_out), .sel(Waveform));
  ROM #(.addrWidth(2), .dataWidth(14)) rom_2 (.addr(2'b00), .data(rom_2_data));
  Button button_3 (.out(button_3_out));
  xor xor_3 (xor_3_out, A2, button_3_out);
  Demultiplexer #(.select(2)) demultiplexer_3 (
    .out0(demultiplexer_3_out0), .out1(demultiplexer_3_out1), .out2(demultiplexer_3_out2),
    .out3(demultiplexer_3_out3), .in(xor_3_out), .sel(Waveform));
  ROM #(.addrWidth(2), .dataWidth(14)) rom_3 (.addr(2'b00), .data(rom_3_data));
  Button button_4 (.out(button_4_out));
  xor xor_4 (xor_4_out, A3, button_4_out);
  Demultiplexer #(.select(2)) demultiplexer_4 (
    .out0(demultiplexer_4_out0), .out1(demultiplexer_4_out1), .out2(demultiplexer_4_out2),
    .out3(demultiplexer_4_out3), .in(xor_4_out), .sel(Waveform));
  ROM #(.addrWidth(2), .dataWidth(14)) rom_4 (.addr(2'b00), .data(rom_4_data));
  Button button_5 (.out(button_5_out));
  xor xor_5 (xor_5_out, A4, button_5_out);
  Demultiplexer #(.select(2)) demultiplexer_5 (
    .out0(demultiplexer_5_out0), .out1(demultiplexer_5_out1), .out2(demultiplexer_5_out2),
    .out3(demultiplexer_5_out3), .in(xor_5_out), .sel(Waveform));
  ROM #(.addrWidth(2), .dataWidth(14)) rom_5 (.addr(2'b00), .data(rom_5_data));
  Button button_6 (.out(button_6_out));
  xor xor_6 (xor_6_out, A5, button_6_out);
  Demultiplexer #(.select(2)) demultiplexer_6 (
    .out0(demultiplexer_6_out0), .out1(demultiplexer_6_out1), .out2(demultiplexer_6_out2),
    .out3(demultiplexer_6_out3), .in(xor_6_out), .sel(Waveform));
  ROM #(.addrWidth(2), .dataWidth(14)) rom_6 (.addr(2'b00), .data(rom_6_data));
  Button button_7 (.out(button_7_out));
  xor xor_7 (xor_7_out, A6, button_7_out);
  Demultiplexer #(.select(2)) demultiplexer_7 (
    .out0(demultiplexer_7_out0), .out1(demultiplexer_7_out1), .out2(demultiplexer_7_out2),
    .out3(demultiplexer_7_out3), .in(xor_7_out), .sel(Waveform));
  ROM #(.addrWidth(2), .dataWidth(14)) rom_7 (.addr(2'b00), .data(rom_7_data));
  Button button_8 (.out(button_8_out));
  xor xor_8 (xor_8_out, A7, button_8_out);
  Demultiplexer #(.select(2)) demultiplexer_8 (
    .out0(demultiplexer_8_out0), .out1(demultiplexer_8_out1), .out2(demultiplexer_8_out2),
    .out3(demultiplexer_8_out3), .in(xor_8_out), .sel(Waveform));
  ROM #(.addrWidth(2), .dataWidth(14)) rom_8 (.addr(2'b00), .data(rom_8_data));
  Button button_9 (.out(button_9_out));
  xor xor_9 (xor_9_out, A8, button_9_out);
  Demultiplexer #(.select(2)) demultiplexer_9 (
    .out0(demultiplexer_9_out0), .out1(demultiplexer_9_out1), .out2(demultiplexer_9_out2),
    .out3(demultiplexer_9_out3), .in(xor_9_out), .sel(Waveform));
  ROM #(.addrWidth(2), .dataWidth(14)) rom_9 (.addr(2'b00), .data(rom_9_data));
  // Buzzer #(.waveform("Square")) buzzer_1: pin names not known; wires that end beside it: rom_1_data, demultiplexer_1_out1, Volume
  // Buzzer buzzer_2: pin names not known; wires that end beside it: rom_1_data, demultiplexer_1_out0, Volume
  // Buzzer #(.waveform("Square")) buzzer_3: pin names not known; wires that end beside it: rom_2_data, demultiplexer_2_out1, Volume
  // Buzzer buzzer_4: pin names not known; wires that end beside it: rom_2_data, demultiplexer_2_out0, Volume
  // Buzzer #(.waveform("Square")) buzzer_5: pin names not known; wires that end beside it: rom_3_data, demultiplexer_3_out1, Volume
  // Buzzer buzzer_6: pin names not known; wires that end beside it: rom_3_data, demultiplexer_3_out0, Volume
  // Buzzer #(.waveform("Square")) buzzer_7: pin names not known; wires that end beside it: rom_4_data, demultiplexer_4_out1, Volume
  // Buzzer buzzer_8: pin names not known; wires that end beside it: rom_4_data, demultiplexer_4_out0, Volume
  // Buzzer #(.waveform("Square")) buzzer_9: pin names not known; wires that end beside it: rom_5_data, demultiplexer_5_out1, Volume
  // Buzzer buzzer_10: pin names not known; wires that end beside it: rom_5_data, demultiplexer_5_out0, Volume
  // Buzzer #(.waveform("Square")) buzzer_11: pin names not known; wires that end beside it: rom_6_data, demultiplexer_6_out1, Volume
  // Buzzer buzzer_12: pin names not known; wires that end beside it: rom_6_data, demultiplexer_6_out0, Volume
  // Buzzer #(.waveform("Square")) buzzer_13: pin names not known; wires that end beside it: rom_7_data, demultiplexer_7_out1, Volume
  // Buzzer buzzer_14: pin names not known; wires that end beside it: rom_7_data, demultiplexer_7_out0, Volume
  // Buzzer #(.waveform("Square")) buzzer_15: pin names not known; wires that end beside it: rom_8_data, demultiplexer_8_out1, Volume
  // Buzzer buzzer_16: pin names not known; wires that end beside it: rom_8_data, demultiplexer_8_out0, Volume
  // Buzzer #(.waveform("Square")) buzzer_17: pin names not known; wires that end beside it: rom_9_data, demultiplexer_9_out1, Volume
  // Buzzer buzzer_18: pin names not known; wires that end beside it: rom_9_data, demultiplexer_9_out0, Volume
  // Buzzer #(.waveform("Sawtooth")) buzzer_19: pin names not known; wires that end beside it: rom_1_data, demultiplexer_1_out3, Volume
  // Buzzer #(.waveform("Triangle")) buzzer_20: pin names not known; wires that end beside it: rom_1_data, demultiplexer_1_out2, Volume
  // Buzzer #(.waveform("Sawtooth")) buzzer_21: pin names not known; wires that end beside it: rom_2_data, demultiplexer_2_out3, Volume
  // Buzzer #(.waveform("Triangle")) buzzer_22: pin names not known; wires that end beside it: rom_2_data, demultiplexer_2_out2, Volume
  // Buzzer #(.waveform("Sawtooth")) buzzer_23: pin names not known; wires that end beside it: rom_3_data, demultiplexer_3_out3, Volume
  // Buzzer #(.waveform("Triangle")) buzzer_24: pin names not known; wires that end beside it: rom_3_data, demultiplexer_3_out2, Volume
  // Buzzer #(.waveform("Sawtooth")) buzzer_25: pin names not known; wires that end beside it: rom_4_data, demultiplexer_4_out3, Volume
  // Buzzer #(.waveform("Triangle")) buzzer_26: pin names not known; wires that end beside it: rom_4_data, demultiplexer_4_out2, Volume
  // Buzzer #(.waveform("Sawtooth")) buzzer_27: pin names not known; wires that end beside it: rom_5_data, demultiplexer_5_out3, Volume
  // Buzzer #(.waveform("Triangle")) buzzer_28: pin names not known; wires that end beside it: rom_5_data, demultiplexer_5_out2, Volume
  // Buzzer #(.waveform("Sawtooth")) buzzer_29: pin names not known; wires that end beside it: rom_6_data, demultiplexer_6_out3, Volume
  // Buzzer #(.waveform("Triangle")) buzzer_30: pin names not known; wires that end beside it: rom_6_data, demultiplexer_6_out2, Volume
  // Buzzer #(.waveform("Sawtooth")) buzzer_31: pin names not known; wires that end beside it: rom_7_data, demultiplexer_7_out3, Volume
  // Buzzer #(.waveform("Triangle")) buzzer_32: pin names not known; wires that end beside it: rom_7_data, demultiplexer_7_out2, Volume
  // Buzzer #(.waveform("Sawtooth")) buzzer_33: pin names not known; wires that end beside it: rom_8_data, demultiplexer_8_out3, Volume
  // Buzzer #(.waveform("Triangle")) buzzer_34: pin names not known; wires that end beside it: rom_8_data, demultiplexer_8_out2, Volume
  // Buzzer #(.waveform("Sawtooth")) buzzer_35: pin names not known; wires that end beside it: rom_9_data, demultiplexer_9_out3, Volume
  // Buzzer #(.waveform("Triangle")) buzzer_36: pin names not known; wires that end beside it: rom_9_data, demultiplexer_9_out2, Volume
  Button button_10 (.out(button_10_out));
  xor xor_10 (xor_10_out, in_4, button_10_out);
  Demultiplexer #(.select(2)) demultiplexer_10 (
    .out0(demultiplexer_10_out0), .out1(demultiplexer_10_out1), .out2(demultiplexer_10_out2),
    .out3(demultiplexer_10_out3), .in(xor_10_out), .sel(Waveform));
  ROM #(.addrWidth(2), .dataWidth(14)) rom_10 (.addr(2'b00), .data(rom_10_data));
  Button button_11 (.out(button_11_out));
  xor xor_11 (xor_11_out, in_16, button_11_out);
  Demultiplexer #(.select(2)) demultiplexer_11 (
    .out0(demultiplexer_11_out0), .out1(demultiplexer_11_out1), .out2(demultiplexer_11_out2),
    .out3(demultiplexer_11_out3), .in(xor_11_out), .sel(Waveform));
  ROM #(.addrWidth(2), .dataWidth(14)) rom_11 (.addr(2'b00), .data(rom_11_data));
  Button button_12 (.out(button_12_out));
  xor xor_12 (xor_12_out, in_28, button_12_out);
  Demultiplexer #(.select(2)) demultiplexer_12 (
    .out0(demultiplexer_12_out0), .out1(demultiplexer_12_out1), .out2(demultiplexer_12_out2),
    .out3(demultiplexer_12_out3), .in(xor_12_out), .sel(Waveform));
  ROM #(.addrWidth(2), .dataWidth(14)) rom_12 (.addr(2'b00), .data(rom_12_data));
  Button button_13 (.out(button_13_out));
  xor xor_13 (xor_13_out, in_40, button_13_out);
  Demultiplexer #(.select(2)) demultiplexer_13 (
    .out0(demultiplexer_13_out0), .out1(demultiplexer_13_out1), .out2(demultiplexer_13_out2),
    .out3(demultiplexer_13_out3), .in(xor_13_out), .sel(Waveform));
  ROM #(.addrWidth(2), .dataWidth(14)) rom_13 (.addr(2'b00), .data(rom_13_data));
  Button button_14 (.out(button_14_out));
  xor xor_14 (xor_14_out, in_52, button_14_out);
  Demultiplexer #(.select(2)) demultiplexer_14 (
    .out0(demultiplexer_14_out0), .out1(demultiplexer_14_out1), .out2(demultiplexer_14_out2),
    .out3(demultiplexer_14_out3), .in(xor_14_out), .sel(Waveform));
  ROM #(.addrWidth(2), .dataWidth(14)) rom_14 (.addr(2'b00), .data(rom_14_data));
  Button button_15 (.out(button_15_out));
  xor xor_15 (xor_15_out, in_64, button_15_out);
  Demultiplexer #(.select(2)) demultiplexer_15 (
    .out0(demultiplexer_15_out0), .out1(demultiplexer_15_out1), .out2(demultiplexer_15_out2),
    .out3(demultiplexer_15_out3), .in(xor_15_out), .sel(Waveform));
  ROM #(.addrWidth(2), .dataWidth(14)) rom_15 (.addr(2'b00), .data(rom_15_data));
  Button button_16 (.out(button_16_out));
  xor xor_16 (xor_16_out, in_76, button_16_out);
  Demultiplexer #(.select(2)) demultiplexer_16 (
    .out0(demultiplexer_16_out0), .out1(demultiplexer_16_out1), .out2(demultiplexer_16_out2),
    .out3(demultiplexer_16_out3), .in(xor_16_out), .sel(Waveform));
  ROM #(.addrWidth(2), .dataWidth(14)) rom_16 (.addr(2'b00), .data(rom_16_data));
  Button button_17 (.out(button_17_out));
  xor xor_17 (xor_17_out, in_88, button_17_out);
  Demultiplexer #(.select(2)) demultiplexer_17 (
    .out0(demultiplexer_17_out0), .out1(demultiplexer_17_out1), .out2(demultiplexer_17_out2),
    .out3(demultiplexer_17_out3), .in(xor_17_out), .sel(Waveform));
  ROM #(.addrWidth(2), .dataWidth(14)) rom_17 (.addr(2'b00), .data(rom_17_data));
  Button button_18 (.out(button_18_out));
  xor xor_18 (xor_18_out, in_100, button_18_out);
  Demultiplexer #(.select(2)) demultiplexer_18 (
    .out0(demultiplexer_18_out0), .out1(demultiplexer_18_out1), .out2(demultiplexer_18_out2),
    .out3(demultiplexer_18_out3), .in(xor_18_out), .sel(Waveform));
  ROM #(.addrWidth(2), .dataWidth(14)) rom_18 (.addr(2'b00), .data(rom_18_data));
  // Buzzer buzzer_37: pin names not known; wires that end beside it: rom_10_data, demultiplexer_10_out0, Volume
  // Buzzer buzzer_38: pin names not known; wires that end beside it: rom_11_data, demultiplexer_11_out0, Volume
  // Buzzer buzzer_39: pin names not known; wires that end beside it: rom_12_data, demultiplexer_12_out0, Volume
  // Buzzer buzzer_40: pin names not known; wires that end beside it: rom_13_data, demultiplexer_13_out0, Volume
  // Buzzer buzzer_41: pin names not known; wires that end beside it: rom_14_data, demultiplexer_14_out0, Volume
  // Buzzer buzzer_42: pin names not known; wires that end beside it: rom_15_data, demultiplexer_15_out0, Volume
  // Buzzer buzzer_43: pin names not known; wires that end beside it: rom_16_data, demultiplexer_16_out0, Volume
  // Buzzer buzzer_44: pin names not known; wires that end beside it: rom_17_data, demultiplexer_17_out0, Volume
  // Buzzer buzzer_45: pin names not known; wires that end beside it: rom_18_data, demultiplexer_18_out0, Volume
  // Buzzer #(.waveform("Triangle")) buzzer_46: pin names not known; wires that end beside it: rom_10_data, demultiplexer_10_out2, Volume
  // Buzzer #(.waveform("Square")) buzzer_47: pin names not known; wires that end beside it: rom_10_data, demultiplexer_10_out1, Volume
  // Buzzer #(.waveform("Triangle")) buzzer_48: pin names not known; wires that end beside it: rom_11_data, demultiplexer_11_out2, Volume
  // Buzzer #(.waveform("Square")) buzzer_49: pin names not known; wires that end beside it: rom_11_data, demultiplexer_11_out1, Volume
  // Buzzer #(.waveform("Triangle")) buzzer_50: pin names not known; wires that end beside it: rom_12_data, demultiplexer_12_out2, Volume
  // Buzzer #(.waveform("Square")) buzzer_51: pin names not known; wires that end beside it: rom_12_data, demultiplexer_12_out1, Volume
  // Buzzer #(.waveform("Triangle")) buzzer_52: pin names not known; wires that end beside it: rom_13_data, demultiplexer_13_out2, Volume
  // Buzzer #(.waveform("Square")) buzzer_53: pin names not known; wires that end beside it: rom_13_data, demultiplexer_13_out1, Volume
  // Buzzer #(.waveform("Triangle")) buzzer_54: pin names not known; wires that end beside it: rom_14_data, demultiplexer_14_out2, Volume
  // Buzzer #(.waveform("Square")) buzzer_55: pin names not known; wires that end beside it: rom_14_data, demultiplexer_14_out1, Volume
  // Buzzer #(.waveform("Triangle")) buzzer_56: pin names not known; wires that end beside it: rom_15_data, demultiplexer_15_out2, Volume
  // Buzzer #(.waveform("Square")) buzzer_57: pin names not known; wires that end beside it: rom_15_data, demultiplexer_15_out1, Volume
  // Buzzer #(.waveform("Triangle")) buzzer_58: pin names not known; wires that end beside it: rom_16_data, demultiplexer_16_out2, Volume
  // Buzzer #(.waveform("Square")) buzzer_59: pin names not known; wires that end beside it: rom_16_data, demultiplexer_16_out1, Volume
  // Buzzer #(.waveform("Triangle")) buzzer_60: pin names not known; wires that end beside it: rom_17_data, demultiplexer_17_out2, Volume
  // Buzzer #(.waveform("Square")) buzzer_61: pin names not known; wires that end beside it: rom_17_data, demultiplexer_17_out1, Volume
  // Buzzer #(.waveform("Triangle")) buzzer_62: pin names not known; wires that end beside it: rom_18_data, demultiplexer_18_out2, Volume
  // Buzzer #(.waveform("Square")) buzzer_63: pin names not known; wires that end beside it: rom_18_data, demultiplexer_18_out1, Volume
  // Buzzer #(.waveform("Sawtooth")) buzzer_64: pin names not known; wires that end beside it: rom_10_data, demultiplexer_10_out3, Volume
  // Buzzer #(.waveform("Sawtooth")) buzzer_65: pin names not known; wires that end beside it: rom_11_data, demultiplexer_11_out3, Volume
  // Buzzer #(.waveform("Sawtooth")) buzzer_66: pin names not known; wires that end beside it: rom_12_data, demultiplexer_12_out3, Volume
  // Buzzer #(.waveform("Sawtooth")) buzzer_67: pin names not known; wires that end beside it: rom_13_data, demultiplexer_13_out3, Volume
  // Buzzer #(.waveform("Sawtooth")) buzzer_68: pin names not known; wires that end beside it: rom_14_data, demultiplexer_14_out3, Volume
  // Buzzer #(.waveform("Sawtooth")) buzzer_69: pin names not known; wires that end beside it: rom_15_data, demultiplexer_15_out3, Volume
  // Buzzer #(.waveform("Sawtooth")) buzzer_70: pin names not known; wires that end beside it: rom_16_data, demultiplexer_16_out3, Volume
  // Buzzer #(.waveform("Sawtooth")) buzzer_71: pin names not known; wires that end beside it: rom_17_data, demultiplexer_17_out3, Volume
  // Buzzer #(.waveform("Sawtooth")) buzzer_72: pin names not known; wires that end beside it: rom_18_data, demultiplexer_18_out3, Volume
  Button button_19 (.out(button_19_out));
  xor xor_19 (xor_19_out, in_5, button_19_out);
  Demultiplexer #(.select(2)) demultiplexer_19 (
    .out0(demultiplexer_19_out0), .out1(demultiplexer_19_out1), .out2(demultiplexer_19_out2),
    .out3(demultiplexer_19_out3), .in(xor_19_out), .sel(Waveform));
  ROM #(.addrWidth(2), .dataWidth(14)) rom_19 (.addr(2'b00), .data(rom_19_data));
  Button button_20 (.out(button_20_out));
  xor xor_20 (xor_20_out, in_17, button_20_out);
  Demultiplexer #(.select(2)) demultiplexer_20 (
    .out0(demultiplexer_20_out0), .out1(demultiplexer_20_out1), .out2(demultiplexer_20_out2),
    .out3(demultiplexer_20_out3), .in(xor_20_out), .sel(Waveform));
  ROM #(.addrWidth(2), .dataWidth(14)) rom_20 (.addr(2'b00), .data(rom_20_data));
  Button button_21 (.out(button_21_out));
  xor xor_21 (xor_21_out, in_29, button_21_out);
  Demultiplexer #(.select(2)) demultiplexer_21 (
    .out0(demultiplexer_21_out0), .out1(demultiplexer_21_out1), .out2(demultiplexer_21_out2),
    .out3(demultiplexer_21_out3), .in(xor_21_out), .sel(Waveform));
  ROM #(.addrWidth(2), .dataWidth(14)) rom_21 (.addr(2'b00), .data(rom_21_data));
  Button button_22 (.out(button_22_out));
  xor xor_22 (xor_22_out, in_41, button_22_out);
  Demultiplexer #(.select(2)) demultiplexer_22 (
    .out0(demultiplexer_22_out0), .out1(demultiplexer_22_out1), .out2(demultiplexer_22_out2),
    .out3(demultiplexer_22_out3), .in(xor_22_out), .sel(Waveform));
  ROM #(.addrWidth(2), .dataWidth(14)) rom_22 (.addr(2'b00), .data(rom_22_data));
  Button button_23 (.out(button_23_out));
  xor xor_23 (xor_23_out, in_53, button_23_out);
  Demultiplexer #(.select(2)) demultiplexer_23 (
    .out0(demultiplexer_23_out0), .out1(demultiplexer_23_out1), .out2(demultiplexer_23_out2),
    .out3(demultiplexer_23_out3), .in(xor_23_out), .sel(Waveform));
  ROM #(.addrWidth(2), .dataWidth(14)) rom_23 (.addr(2'b00), .data(rom_23_data));
  Button button_24 (.out(button_24_out));
  xor xor_24 (xor_24_out, in_65, button_24_out);
  Demultiplexer #(.select(2)) demultiplexer_24 (
    .out0(demultiplexer_24_out0), .out1(demultiplexer_24_out1), .out2(demultiplexer_24_out2),
    .out3(demultiplexer_24_out3), .in(xor_24_out), .sel(Waveform));
  ROM #(.addrWidth(2), .dataWidth(14)) rom_24 (.addr(2'b00), .data(rom_24_data));
  Button button_25 (.out(button_25_out));
  xor xor_25 (xor_25_out, in_77, button_25_out);
  Demultiplexer #(.select(2)) demultiplexer_25 (
    .out0(demultiplexer_25_out0), .out1(demultiplexer_25_out1), .out2(demultiplexer_25_out2),
    .out3(demultiplexer_25_out3), .in(xor_25_out), .sel(Waveform));
  ROM #(.addrWidth(2), .dataWidth(14)) rom_25 (.addr(2'b00), .data(rom_25_data));
  Button button_26 (.out(button_26_out));
  xor xor_26 (xor_26_out, in_89, button_26_out);
  Demultiplexer #(.select(2)) demultiplexer_26 (
    .out0(demultiplexer_26_out0), .out1(demultiplexer_26_out1), .out2(demultiplexer_26_out2),
    .out3(demultiplexer_26_out3), .in(xor_26_out), .sel(Waveform));
  ROM #(.addrWidth(2), .dataWidth(14)) rom_26 (.addr(2'b00), .data(rom_26_data));
  Button button_27 (.out(button_27_out));
  xor xor_27 (xor_27_out, in_101, button_27_out);
  Demultiplexer #(.select(2)) demultiplexer_27 (
    .out0(demultiplexer_27_out0), .out1(demultiplexer_27_out1), .out2(demultiplexer_27_out2),
    .out3(demultiplexer_27_out3), .in(xor_27_out), .sel(Waveform));
  ROM #(.addrWidth(2), .dataWidth(14)) rom_27 (.addr(2'b00), .data(rom_27_data));
  // Buzzer #(.waveform("Square")) buzzer_73: pin names not known; wires that end beside it: rom_19_data, demultiplexer_19_out1, Volume
  // Buzzer buzzer_74: pin names not known; wires that end beside it: rom_19_data, demultiplexer_19_out0, Volume
  // Buzzer #(.waveform("Square")) buzzer_75: pin names not known; wires that end beside it: rom_20_data, demultiplexer_20_out1, Volume
  // Buzzer buzzer_76: pin names not known; wires that end beside it: rom_20_data, demultiplexer_20_out0, Volume
  // Buzzer #(.waveform("Square")) buzzer_77: pin names not known; wires that end beside it: rom_21_data, demultiplexer_21_out1, Volume
  // Buzzer buzzer_78: pin names not known; wires that end beside it: rom_21_data, demultiplexer_21_out0, Volume
  // Buzzer #(.waveform("Square")) buzzer_79: pin names not known; wires that end beside it: rom_22_data, demultiplexer_22_out1, Volume
  // Buzzer buzzer_80: pin names not known; wires that end beside it: rom_22_data, demultiplexer_22_out0, Volume
  // Buzzer #(.waveform("Square")) buzzer_81: pin names not known; wires that end beside it: rom_23_data, demultiplexer_23_out1, Volume
  // Buzzer buzzer_82: pin names not known; wires that end beside it: rom_23_data, demultiplexer_23_out0, Volume
  // Buzzer #(.waveform("Square")) buzzer_83: pin names not known; wires that end beside it: rom_24_data, demultiplexer_24_out1, Volume
  // Buzzer buzzer_84: pin names not known; wires that end beside it: rom_24_data, demultiplexer_24_out0, Volume
  // Buzzer #(.waveform("Square")) buzzer_85: pin names not known; wires that end beside it: rom_25_data, demultiplexer_25_out1, Volume
  // Buzzer buzzer_86: pin names not known; wires that end beside it: rom_25_data, demultiplexer_25_out0, Volume
  // Buzzer #(.waveform("Square")) buzzer_87: pin names not known; wires that end beside it: rom_26_data, demultiplexer_26_out1, Volume
  // Buzzer buzzer_88: pin names not known; wires that end beside it: rom_26_data, demultiplexer_26_out0, Volume
  // Buzzer #(.waveform("Square")) buzzer_89: pin names not known; wires that end beside it: rom_27_data, demultiplexer_27_out1, Volume
  // Buzzer buzzer_90: pin names not known; wires that end beside it: rom_27_data, demultiplexer_27_out0, Volume
  // Buzzer #(.waveform("Sawtooth")) buzzer_91: pin names not known; wires that end beside it: rom_19_data, demultiplexer_19_out3, Volume
  // Buzzer #(.waveform("Triangle")) buzzer_92: pin names not known; wires that end beside it: rom_19_data, demultiplexer_19_out2, Volume
  // Buzzer #(.waveform("Sawtooth")) buzzer_93: pin names not known; wires that end beside it: rom_20_data, demultiplexer_20_out3, Volume
  // Buzzer #(.waveform("Triangle")) buzzer_94: pin names not known; wires that end beside it: rom_20_data, demultiplexer_20_out2, Volume
  // Buzzer #(.waveform("Sawtooth")) buzzer_95: pin names not known; wires that end beside it: rom_21_data, demultiplexer_21_out3, Volume
  // Buzzer #(.waveform("Triangle")) buzzer_96: pin names not known; wires that end beside it: rom_21_data, demultiplexer_21_out2, Volume
  // Buzzer #(.waveform("Sawtooth")) buzzer_97: pin names not known; wires that end beside it: rom_22_data, demultiplexer_22_out3, Volume
  // Buzzer #(.waveform("Triangle")) buzzer_98: pin names not known; wires that end beside it: rom_22_data, demultiplexer_22_out2, Volume
  // Buzzer #(.waveform("Sawtooth")) buzzer_99: pin names not known; wires that end beside it: rom_23_data, demultiplexer_23_out3, Volume
  // Buzzer #(.waveform("Triangle")) buzzer_100: pin names not known; wires that end beside it: rom_23_data, demultiplexer_23_out2, Volume
  // Buzzer #(.waveform("Sawtooth")) buzzer_101: pin names not known; wires that end beside it: rom_24_data, demultiplexer_24_out3, Volume
  // Buzzer #(.waveform("Triangle")) buzzer_102: pin names not known; wires that end beside it: rom_24_data, demultiplexer_24_out2, Volume
  // Buzzer #(.waveform("Sawtooth")) buzzer_103: pin names not known; wires that end beside it: rom_25_data, demultiplexer_25_out3, Volume
  // Buzzer #(.waveform("Triangle")) buzzer_104: pin names not known; wires that end beside it: rom_25_data, demultiplexer_25_out2, Volume
  // Buzzer #(.waveform("Sawtooth")) buzzer_105: pin names not known; wires that end beside it: rom_26_data, demultiplexer_26_out3, Volume
  // Buzzer #(.waveform("Triangle")) buzzer_106: pin names not known; wires that end beside it: rom_26_data, demultiplexer_26_out2, Volume
  // Buzzer #(.waveform("Sawtooth")) buzzer_107: pin names not known; wires that end beside it: rom_27_data, demultiplexer_27_out3, Volume
  // Buzzer #(.waveform("Triangle")) buzzer_108: pin names not known; wires that end beside it: rom_27_data, demultiplexer_27_out2, Volume
  Button button_28 (.out(button_28_out));
  xor xor_28 (xor_28_out, in_6, button_28_out);
  Demultiplexer #(.select(2)) demultiplexer_28 (
    .out0(demultiplexer_28_out0), .out1(demultiplexer_28_out1), .out2(demultiplexer_28_out2),
    .out3(demultiplexer_28_out3), .in(xor_28_out), .sel(Waveform));
  ROM #(.addrWidth(2), .dataWidth(14)) rom_28 (.addr(2'b00), .data(rom_28_data));
  Button button_29 (.out(button_29_out));
  xor xor_29 (xor_29_out, in_18, button_29_out);
  Demultiplexer #(.select(2)) demultiplexer_29 (
    .out0(demultiplexer_29_out0), .out1(demultiplexer_29_out1), .out2(demultiplexer_29_out2),
    .out3(demultiplexer_29_out3), .in(xor_29_out), .sel(Waveform));
  ROM #(.addrWidth(2), .dataWidth(14)) rom_29 (.addr(2'b00), .data(rom_29_data));
  Button button_30 (.out(button_30_out));
  xor xor_30 (xor_30_out, in_30, button_30_out);
  Demultiplexer #(.select(2)) demultiplexer_30 (
    .out0(demultiplexer_30_out0), .out1(demultiplexer_30_out1), .out2(demultiplexer_30_out2),
    .out3(demultiplexer_30_out3), .in(xor_30_out), .sel(Waveform));
  ROM #(.addrWidth(2), .dataWidth(14)) rom_30 (.addr(2'b00), .data(rom_30_data));
  Button button_31 (.out(button_31_out));
  xor xor_31 (xor_31_out, in_42, button_31_out);
  Demultiplexer #(.select(2)) demultiplexer_31 (
    .out0(demultiplexer_31_out0), .out1(demultiplexer_31_out1), .out2(demultiplexer_31_out2),
    .out3(demultiplexer_31_out3), .in(xor_31_out), .sel(Waveform));
  ROM #(.addrWidth(2), .dataWidth(14)) rom_31 (.addr(2'b00), .data(rom_31_data));
  Button button_32 (.out(button_32_out));
  xor xor_32 (xor_32_out, in_54, button_32_out);
  Demultiplexer #(.select(2)) demultiplexer_32 (
    .out0(demultiplexer_32_out0), .out1(demultiplexer_32_out1), .out2(demultiplexer_32_out2),
    .out3(demultiplexer_32_out3), .in(xor_32_out), .sel(Waveform));
  ROM #(.addrWidth(2), .dataWidth(14)) rom_32 (.addr(2'b00), .data(rom_32_data));
  Button button_33 (.out(button_33_out));
  xor xor_33 (xor_33_out, in_66, button_33_out);
  Demultiplexer #(.select(2)) demultiplexer_33 (
    .out0(demultiplexer_33_out0), .out1(demultiplexer_33_out1), .out2(demultiplexer_33_out2),
    .out3(demultiplexer_33_out3), .in(xor_33_out), .sel(Waveform));
  ROM #(.addrWidth(2), .dataWidth(14)) rom_33 (.addr(2'b00), .data(rom_33_data));
  Button button_34 (.out(button_34_out));
  xor xor_34 (xor_34_out, in_78, button_34_out);
  Demultiplexer #(.select(2)) demultiplexer_34 (
    .out0(demultiplexer_34_out0), .out1(demultiplexer_34_out1), .out2(demultiplexer_34_out2),
    .out3(demultiplexer_34_out3), .in(xor_34_out), .sel(Waveform));
  ROM #(.addrWidth(2), .dataWidth(14)) rom_34 (.addr(2'b00), .data(rom_34_data));
  Button button_35 (.out(button_35_out));
  xor xor_35 (xor_35_out, in_90, button_35_out);
  Demultiplexer #(.select(2)) demultiplexer_35 (
    .out0(demultiplexer_35_out0), .out1(demultiplexer_35_out1), .out2(demultiplexer_35_out2),
    .out3(demultiplexer_35_out3), .in(xor_35_out), .sel(Waveform));
  ROM #(.addrWidth(2), .dataWidth(14)) rom_35 (.addr(2'b00), .data(rom_35_data));
  Button button_36 (.out(button_36_out));
  xor xor_36 (xor_36_out, in_102, button_36_out);
  Demultiplexer #(.select(2)) demultiplexer_36 (
    .out0(demultiplexer_36_out0), .out1(demultiplexer_36_out1), .out2(demultiplexer_36_out2),
    .out3(demultiplexer_36_out3), .in(xor_36_out), .sel(Waveform));
  ROM #(.addrWidth(2), .dataWidth(14)) rom_36 (.addr(2'b00), .data(rom_36_data));
  // Buzzer buzzer_109: pin names not known; wires that end beside it: rom_28_data, demultiplexer_28_out0, Volume
  // Buzzer buzzer_110: pin names not known; wires that end beside it: rom_29_data, demultiplexer_29_out0, Volume
  // Buzzer buzzer_111: pin names not known; wires that end beside it: rom_30_data, demultiplexer_30_out0, Volume
  // Buzzer buzzer_112: pin names not known; wires that end beside it: rom_31_data, demultiplexer_31_out0, Volume
  // Buzzer buzzer_113: pin names not known; wires that end beside it: rom_32_data, demultiplexer_32_out0, Volume
  // Buzzer buzzer_114: pin names not known; wires that end beside it: rom_33_data, demultiplexer_33_out0, Volume
  // Buzzer buzzer_115: pin names not known; wires that end beside it: rom_34_data, demultiplexer_34_out0, Volume
  // Buzzer buzzer_116: pin names not known; wires that end beside it: rom_35_data, demultiplexer_35_out0, Volume
  // Buzzer buzzer_117: pin names not known; wires that end beside it: rom_36_data, demultiplexer_36_out0, Volume
  // Buzzer #(.waveform("Triangle")) buzzer_118: pin names not known; wires that end beside it: rom_28_data, demultiplexer_28_out2, Volume
  // Buzzer #(.waveform("Square")) buzzer_119: pin names not known; wires that end beside it: rom_28_data, demultiplexer_28_out1, Volume
  // Buzzer #(.waveform("Triangle")) buzzer_120: pin names not known; wires that end beside it: rom_29_data, demultiplexer_29_out2, Volume
  // Buzzer #(.waveform("Square")) buzzer_121: pin names not known; wires that end beside it: rom_29_data, demultiplexer_29_out1, Volume
  // Buzzer #(.waveform("Triangle")) buzzer_122: pin names not known; wires that end beside it: rom_30_data, demultiplexer_30_out2, Volume
  // Buzzer #(.waveform("Square")) buzzer_123: pin names not known; wires that end beside it: rom_30_data, demultiplexer_30_out1, Volume
  // Buzzer #(.waveform("Triangle")) buzzer_124: pin names not known; wires that end beside it: rom_31_data, demultiplexer_31_out2, Volume
  // Buzzer #(.waveform("Square")) buzzer_125: pin names not known; wires that end beside it: rom_31_data, demultiplexer_31_out1, Volume
  // Buzzer #(.waveform("Triangle")) buzzer_126: pin names not known; wires that end beside it: rom_32_data, demultiplexer_32_out2, Volume
  // Buzzer #(.waveform("Square")) buzzer_127: pin names not known; wires that end beside it: rom_32_data, demultiplexer_32_out1, Volume
  // Buzzer #(.waveform("Triangle")) buzzer_128: pin names not known; wires that end beside it: rom_33_data, demultiplexer_33_out2, Volume
  // Buzzer #(.waveform("Square")) buzzer_129: pin names not known; wires that end beside it: rom_33_data, demultiplexer_33_out1, Volume
  // Buzzer #(.waveform("Triangle")) buzzer_130: pin names not known; wires that end beside it: rom_34_data, demultiplexer_34_out2, Volume
  // Buzzer #(.waveform("Square")) buzzer_131: pin names not known; wires that end beside it: rom_34_data, demultiplexer_34_out1, Volume
  // Buzzer #(.waveform("Triangle")) buzzer_132: pin names not known; wires that end beside it: rom_35_data, demultiplexer_35_out2, Volume
  // Buzzer #(.waveform("Square")) buzzer_133: pin names not known; wires that end beside it: rom_35_data, demultiplexer_35_out1, Volume
  // Buzzer #(.waveform("Triangle")) buzzer_134: pin names not known; wires that end beside it: rom_36_data, demultiplexer_36_out2, Volume
  // Buzzer #(.waveform("Square")) buzzer_135: pin names not known; wires that end beside it: rom_36_data, demultiplexer_36_out1, Volume
  // Buzzer #(.waveform("Sawtooth")) buzzer_136: pin names not known; wires that end beside it: rom_28_data, demultiplexer_28_out3, Volume
  // Buzzer #(.waveform("Sawtooth")) buzzer_137: pin names not known; wires that end beside it: rom_29_data, demultiplexer_29_out3, Volume
  // Buzzer #(.waveform("Sawtooth")) buzzer_138: pin names not known; wires that end beside it: rom_30_data, demultiplexer_30_out3, Volume
  // Buzzer #(.waveform("Sawtooth")) buzzer_139: pin names not known; wires that end beside it: rom_31_data, demultiplexer_31_out3, Volume
  // Buzzer #(.waveform("Sawtooth")) buzzer_140: pin names not known; wires that end beside it: rom_32_data, demultiplexer_32_out3, Volume
  // Buzzer #(.waveform("Sawtooth")) buzzer_141: pin names not known; wires that end beside it: rom_33_data, demultiplexer_33_out3, Volume
  // Buzzer #(.waveform("Sawtooth")) buzzer_142: pin names not known; wires that end beside it: rom_34_data, demultiplexer_34_out3, Volume
  // Buzzer #(.waveform("Sawtooth")) buzzer_143: pin names not known; wires that end beside it: rom_35_data, demultiplexer_35_out3, Volume
  // Buzzer #(.waveform("Sawtooth")) buzzer_144: pin names not known; wires that end beside it: rom_36_data, demultiplexer_36_out3, Volume
  Button button_37 (.out(button_37_out));
  xor xor_37 (xor_37_out, in_7, button_37_out);
  Demultiplexer #(.select(2)) demultiplexer_37 (
    .out0(demultiplexer_37_out0), .out1(demultiplexer_37_out1), .out2(demultiplexer_37_out2),
    .out3(demultiplexer_37_out3), .in(xor_37_out), .sel(Waveform));
  ROM #(.addrWidth(2), .dataWidth(14)) rom_37 (.addr(2'b00), .data(rom_37_data));
  Button button_38 (.out(button_38_out));
  xor xor_38 (xor_38_out, in_19, button_38_out);
  Demultiplexer #(.select(2)) demultiplexer_38 (
    .out0(demultiplexer_38_out0), .out1(demultiplexer_38_out1), .out2(demultiplexer_38_out2),
    .out3(demultiplexer_38_out3), .in(xor_38_out), .sel(Waveform));
  ROM #(.addrWidth(2), .dataWidth(14)) rom_38 (.addr(2'b00), .data(rom_38_data));
  Button button_39 (.out(button_39_out));
  xor xor_39 (xor_39_out, in_31, button_39_out);
  Demultiplexer #(.select(2)) demultiplexer_39 (
    .out0(demultiplexer_39_out0), .out1(demultiplexer_39_out1), .out2(demultiplexer_39_out2),
    .out3(demultiplexer_39_out3), .in(xor_39_out), .sel(Waveform));
  ROM #(.addrWidth(2), .dataWidth(14)) rom_39 (.addr(2'b00), .data(rom_39_data));
  Button button_40 (.out(button_40_out));
  xor xor_40 (xor_40_out, in_43, button_40_out);
  Demultiplexer #(.select(2)) demultiplexer_40 (
    .out0(demultiplexer_40_out0), .out1(demultiplexer_40_out1), .out2(demultiplexer_40_out2),
    .out3(demultiplexer_40_out3), .in(xor_40_out), .sel(Waveform));
  ROM #(.addrWidth(2), .dataWidth(14)) rom_40 (.addr(2'b00), .data(rom_40_data));
  Button button_41 (.out(button_41_out));
  xor xor_41 (xor_41_out, in_55, button_41_out);
  Demultiplexer #(.select(2)) demultiplexer_41 (
    .out0(demultiplexer_41_out0), .out1(demultiplexer_41_out1), .out2(demultiplexer_41_out2),
    .out3(demultiplexer_41_out3), .in(xor_41_out), .sel(Waveform));
  ROM #(.addrWidth(2), .dataWidth(14)) rom_41 (.addr(2'b00), .data(rom_41_data));
  Button button_42 (.out(button_42_out));
  xor xor_42 (xor_42_out, in_67, button_42_out);
  Demultiplexer #(.select(2)) demultiplexer_42 (
    .out0(demultiplexer_42_out0), .out1(demultiplexer_42_out1), .out2(demultiplexer_42_out2),
    .out3(demultiplexer_42_out3), .in(xor_42_out), .sel(Waveform));
  ROM #(.addrWidth(2), .dataWidth(14)) rom_42 (.addr(2'b00), .data(rom_42_data));
  Button button_43 (.out(button_43_out));
  xor xor_43 (xor_43_out, in_79, button_43_out);
  Demultiplexer #(.select(2)) demultiplexer_43 (
    .out0(demultiplexer_43_out0), .out1(demultiplexer_43_out1), .out2(demultiplexer_43_out2),
    .out3(demultiplexer_43_out3), .in(xor_43_out), .sel(Waveform));
  ROM #(.addrWidth(2), .dataWidth(14)) rom_43 (.addr(2'b00), .data(rom_43_data));
  Button button_44 (.out(button_44_out));
  xor xor_44 (xor_44_out, in_91, button_44_out);
  Demultiplexer #(.select(2)) demultiplexer_44 (
    .out0(demultiplexer_44_out0), .out1(demultiplexer_44_out1), .out2(demultiplexer_44_out2),
    .out3(demultiplexer_44_out3), .in(xor_44_out), .sel(Waveform));
  ROM #(.addrWidth(2), .dataWidth(14)) rom_44 (.addr(2'b00), .data(rom_44_data));
  Button button_45 (.out(button_45_out));
  xor xor_45 (xor_45_out, in_103, button_45_out);
  Demultiplexer #(.select(2)) demultiplexer_45 (
    .out0(demultiplexer_45_out0), .out1(demultiplexer_45_out1), .out2(demultiplexer_45_out2),
    .out3(demultiplexer_45_out3), .in(xor_45_out), .sel(Waveform));
  ROM #(.addrWidth(2), .dataWidth(14)) rom_45 (.addr(2'b00), .data(rom_45_data));
  // Buzzer #(.waveform("Square")) buzzer_145: pin names not known; wires that end beside it: rom_37_data, demultiplexer_37_out1, Volume
  // Buzzer buzzer_146: pin names not known; wires that end beside it: rom_37_data, demultiplexer_37_out0, Volume
  // Buzzer #(.waveform("Square")) buzzer_147: pin names not known; wires that end beside it: rom_38_data, demultiplexer_38_out1, Volume
  // Buzzer buzzer_148: pin names not known; wires that end beside it: rom_38_data, demultiplexer_38_out0, Volume
  // Buzzer #(.waveform("Square")) buzzer_149: pin names not known; wires that end beside it: rom_39_data, demultiplexer_39_out1, Volume
  // Buzzer buzzer_150: pin names not known; wires that end beside it: rom_39_data, demultiplexer_39_out0, Volume
  // Buzzer #(.waveform("Square")) buzzer_151: pin names not known; wires that end beside it: rom_40_data, demultiplexer_40_out1, Volume
  // Buzzer buzzer_152: pin names not known; wires that end beside it: rom_40_data, demultiplexer_40_out0, Volume
  // Buzzer #(.waveform("Square")) buzzer_153: pin names not known; wires that end beside it: rom_41_data, demultiplexer_41_out1, Volume
  // Buzzer buzzer_154: pin names not known; wires that end beside it: rom_41_data, demultiplexer_41_out0, Volume
  // Buzzer #(.waveform("Square")) buzzer_155: pin names not known; wires that end beside it: rom_42_data, demultiplexer_42_out1, Volume
  // Buzzer buzzer_156: pin names not known; wires that end beside it: rom_42_data, demultiplexer_42_out0, Volume
  // Buzzer #(.waveform("Square")) buzzer_157: pin names not known; wires that end beside it: rom_43_data, demultiplexer_43_out1, Volume
  // Buzzer buzzer_158: pin names not known; wires that end beside it: rom_43_data, demultiplexer_43_out0, Volume
  // Buzzer #(.waveform("Square")) buzzer_159: pin names not known; wires that end beside it: rom_44_data, demultiplexer_44_out1, Volume
  // Buzzer buzzer_160: pin names not known; wires that end beside it: rom_44_data, demultiplexer_44_out0, Volume
  // Buzzer #(.waveform("Square")) buzzer_161: pin names not known; wires that end beside it: rom_45_data, demultiplexer_45_out1, Volume
  // Buzzer buzzer_162: pin names not known; wires that end beside it: rom_45_data, demultiplexer_45_out0, Volume
  // Buzzer #(.waveform("Sawtooth")) buzzer_163: pin names not known; wires that end beside it: rom_37_data, demultiplexer_37_out3, Volume
  // Buzzer #(.waveform("Triangle")) buzzer_164: pin names not known; wires that end beside it: rom_37_data, demultiplexer_37_out2, Volume
  // Buzzer #(.waveform("Sawtooth")) buzzer_165: pin names not known; wires that end beside it: rom_38_data, demultiplexer_38_out3, Volume
  // Buzzer #(.waveform("Triangle")) buzzer_166: pin names not known; wires that end beside it: rom_38_data, demultiplexer_38_out2, Volume
  // Buzzer #(.waveform("Sawtooth")) buzzer_167: pin names not known; wires that end beside it: rom_39_data, demultiplexer_39_out3, Volume
  // Buzzer #(.waveform("Triangle")) buzzer_168: pin names not known; wires that end beside it: rom_39_data, demultiplexer_39_out2, Volume
  // Buzzer #(.waveform("Sawtooth")) buzzer_169: pin names not known; wires that end beside it: rom_40_data, demultiplexer_40_out3, Volume
  // Buzzer #(.waveform("Triangle")) buzzer_170: pin names not known; wires that end beside it: rom_40_data, demultiplexer_40_out2, Volume
  // Buzzer #(.waveform("Sawtooth")) buzzer_171: pin names not known; wires that end beside it: rom_41_data, demultiplexer_41_out3, Volume
  // Buzzer #(.waveform("Triangle")) buzzer_172: pin names not known; wires that end beside it: rom_41_data, demultiplexer_41_out2, Volume
  // Buzzer #(.waveform("Sawtooth")) buzzer_173: pin names not known; wires that end beside it: rom_42_data, demultiplexer_42_out3, Volume
  // Buzzer #(.waveform("Triangle")) buzzer_174: pin names not known; wires that end beside it: rom_42_data, demultiplexer_42_out2, Volume
  // Buzzer #(.waveform("Sawtooth")) buzzer_175: pin names not known; wires that end beside it: rom_43_data, demultiplexer_43_out3, Volume
  // Buzzer #(.waveform("Triangle")) buzzer_176: pin names not known; wires that end beside it: rom_43_data, demultiplexer_43_out2, Volume
  // Buzzer #(.waveform("Sawtooth")) buzzer_177: pin names not known; wires that end beside it: rom_44_data, demultiplexer_44_out3, Volume
  // Buzzer #(.waveform("Triangle")) buzzer_178: pin names not known; wires that end beside it: rom_44_data, demultiplexer_44_out2, Volume
  // Buzzer #(.waveform("Sawtooth")) buzzer_179: pin names not known; wires that end beside it: rom_45_data, demultiplexer_45_out3, Volume
  // Buzzer #(.waveform("Triangle")) buzzer_180: pin names not known; wires that end beside it: rom_45_data, demultiplexer_45_out2, Volume
  Button button_46 (.out(button_46_out));
  xor xor_46 (xor_46_out, in_8, button_46_out);
  Demultiplexer #(.select(2)) demultiplexer_46 (
    .out0(demultiplexer_46_out0), .out1(demultiplexer_46_out1), .out2(demultiplexer_46_out2),
    .out3(demultiplexer_46_out3), .in(xor_46_out), .sel(Waveform));
  ROM #(.addrWidth(2), .dataWidth(14)) rom_46 (.addr(2'b00), .data(rom_46_data));
  Button button_47 (.out(button_47_out));
  xor xor_47 (xor_47_out, in_20, button_47_out);
  Demultiplexer #(.select(2)) demultiplexer_47 (
    .out0(demultiplexer_47_out0), .out1(demultiplexer_47_out1), .out2(demultiplexer_47_out2),
    .out3(demultiplexer_47_out3), .in(xor_47_out), .sel(Waveform));
  ROM #(.addrWidth(2), .dataWidth(14)) rom_47 (.addr(2'b00), .data(rom_47_data));
  Button button_48 (.out(button_48_out));
  xor xor_48 (xor_48_out, in_32, button_48_out);
  Demultiplexer #(.select(2)) demultiplexer_48 (
    .out0(demultiplexer_48_out0), .out1(demultiplexer_48_out1), .out2(demultiplexer_48_out2),
    .out3(demultiplexer_48_out3), .in(xor_48_out), .sel(Waveform));
  ROM #(.addrWidth(2), .dataWidth(14)) rom_48 (.addr(2'b00), .data(rom_48_data));
  Button button_49 (.out(button_49_out));
  xor xor_49 (xor_49_out, in_44, button_49_out);
  Demultiplexer #(.select(2)) demultiplexer_49 (
    .out0(demultiplexer_49_out0), .out1(demultiplexer_49_out1), .out2(demultiplexer_49_out2),
    .out3(demultiplexer_49_out3), .in(xor_49_out), .sel(Waveform));
  ROM #(.addrWidth(2), .dataWidth(14)) rom_49 (.addr(2'b00), .data(rom_49_data));
  Button button_50 (.out(button_50_out));
  xor xor_50 (xor_50_out, in_56, button_50_out);
  Demultiplexer #(.select(2)) demultiplexer_50 (
    .out0(demultiplexer_50_out0), .out1(demultiplexer_50_out1), .out2(demultiplexer_50_out2),
    .out3(demultiplexer_50_out3), .in(xor_50_out), .sel(Waveform));
  ROM #(.addrWidth(2), .dataWidth(14)) rom_50 (.addr(2'b00), .data(rom_50_data));
  Button button_51 (.out(button_51_out));
  xor xor_51 (xor_51_out, in_68, button_51_out);
  Demultiplexer #(.select(2)) demultiplexer_51 (
    .out0(demultiplexer_51_out0), .out1(demultiplexer_51_out1), .out2(demultiplexer_51_out2),
    .out3(demultiplexer_51_out3), .in(xor_51_out), .sel(Waveform));
  ROM #(.addrWidth(2), .dataWidth(14)) rom_51 (.addr(2'b00), .data(rom_51_data));
  Button button_52 (.out(button_52_out));
  xor xor_52 (xor_52_out, in_80, button_52_out);
  Demultiplexer #(.select(2)) demultiplexer_52 (
    .out0(demultiplexer_52_out0), .out1(demultiplexer_52_out1), .out2(demultiplexer_52_out2),
    .out3(demultiplexer_52_out3), .in(xor_52_out), .sel(Waveform));
  ROM #(.addrWidth(2), .dataWidth(14)) rom_52 (.addr(2'b00), .data(rom_52_data));
  Button button_53 (.out(button_53_out));
  xor xor_53 (xor_53_out, in_92, button_53_out);
  Demultiplexer #(.select(2)) demultiplexer_53 (
    .out0(demultiplexer_53_out0), .out1(demultiplexer_53_out1), .out2(demultiplexer_53_out2),
    .out3(demultiplexer_53_out3), .in(xor_53_out), .sel(Waveform));
  ROM #(.addrWidth(2), .dataWidth(14)) rom_53 (.addr(2'b00), .data(rom_53_data));
  Button button_54 (.out(button_54_out));
  xor xor_54 (xor_54_out, in_104, button_54_out);
  Demultiplexer #(.select(2)) demultiplexer_54 (
    .out0(demultiplexer_54_out0), .out1(demultiplexer_54_out1), .out2(demultiplexer_54_out2),
    .out3(demultiplexer_54_out3), .in(xor_54_out), .sel(Waveform));
  ROM #(.addrWidth(2), .dataWidth(14)) rom_54 (.addr(2'b00), .data(rom_54_data));
  // Buzzer buzzer_181: pin names not known; wires that end beside it: rom_46_data, demultiplexer_46_out0, Volume
  // Buzzer buzzer_182: pin names not known; wires that end beside it: rom_47_data, demultiplexer_47_out0, Volume
  // Buzzer buzzer_183: pin names not known; wires that end beside it: rom_48_data, demultiplexer_48_out0, Volume
  // Buzzer buzzer_184: pin names not known; wires that end beside it: rom_49_data, demultiplexer_49_out0, Volume
  // Buzzer buzzer_185: pin names not known; wires that end beside it: rom_50_data, demultiplexer_50_out0, Volume
  // Buzzer buzzer_186: pin names not known; wires that end beside it: rom_51_data, demultiplexer_51_out0, Volume
  // Buzzer buzzer_187: pin names not known; wires that end beside it: rom_52_data, demultiplexer_52_out0, Volume
  // Buzzer buzzer_188: pin names not known; wires that end beside it: rom_53_data, demultiplexer_53_out0, Volume
  // Buzzer buzzer_189: pin names not known; wires that end beside it: rom_54_data, demultiplexer_54_out0, Volume
  // Buzzer #(.waveform("Triangle")) buzzer_190: pin names not known; wires that end beside it: rom_46_data, demultiplexer_46_out2, Volume
  // Buzzer #(.waveform("Square")) buzzer_191: pin names not known; wires that end beside it: rom_46_data, demultiplexer_46_out1, Volume
  // Buzzer #(.waveform("Triangle")) buzzer_192: pin names not known; wires that end beside it: rom_47_data, demultiplexer_47_out2, Volume
  // Buzzer #(.waveform("Square")) buzzer_193: pin names not known; wires that end beside it: rom_47_data, demultiplexer_47_out1, Volume
  // Buzzer #(.waveform("Triangle")) buzzer_194: pin names not known; wires that end beside it: rom_48_data, demultiplexer_48_out2, Volume
  // Buzzer #(.waveform("Square")) buzzer_195: pin names not known; wires that end beside it: rom_48_data, demultiplexer_48_out1, Volume
  // Buzzer #(.waveform("Triangle")) buzzer_196: pin names not known; wires that end beside it: rom_49_data, demultiplexer_49_out2, Volume
  // Buzzer #(.waveform("Square")) buzzer_197: pin names not known; wires that end beside it: rom_49_data, demultiplexer_49_out1, Volume
  // Buzzer #(.waveform("Triangle")) buzzer_198: pin names not known; wires that end beside it: rom_50_data, demultiplexer_50_out2, Volume
  // Buzzer #(.waveform("Square")) buzzer_199: pin names not known; wires that end beside it: rom_50_data, demultiplexer_50_out1, Volume
  // Buzzer #(.waveform("Triangle")) buzzer_200: pin names not known; wires that end beside it: rom_51_data, demultiplexer_51_out2, Volume
  // Buzzer #(.waveform("Square")) buzzer_201: pin names not known; wires that end beside it: rom_51_data, demultiplexer_51_out1, Volume
  // Buzzer #(.waveform("Triangle")) buzzer_202: pin names not known; wires that end beside it: rom_52_data, demultiplexer_52_out2, Volume
  // Buzzer #(.waveform("Square")) buzzer_203: pin names not known; wires that end beside it: rom_52_data, demultiplexer_52_out1, Volume
  // Buzzer #(.waveform("Triangle")) buzzer_204: pin names not known; wires that end beside it: rom_53_data, demultiplexer_53_out2, Volume
  // Buzzer #(.waveform("Square")) buzzer_205: pin names not known; wires that end beside it: rom_53_data, demultiplexer_53_out1, Volume
  // Buzzer #(.waveform("Triangle")) buzzer_206: pin names not known; wires that end beside it: rom_54_data, demultiplexer_54_out2, Volume
  // Buzzer #(.waveform("Square")) buzzer_207: pin names not known; wires that end beside it: rom_54_data, demultiplexer_54_out1, Volume
  // Buzzer #(.waveform("Sawtooth")) buzzer_208: pin names not known; wires that end beside it: rom_46_data, demultiplexer_46_out3, Volume
  // Buzzer #(.waveform("Sawtooth")) buzzer_209: pin names not known; wires that end beside it: rom_47_data, demultiplexer_47_out3, Volume
  // Buzzer #(.waveform("Sawtooth")) buzzer_210: pin names not known; wires that end beside it: rom_48_data, demultiplexer_48_out3, Volume
  // Buzzer #(.waveform("Sawtooth")) buzzer_211: pin names not known; wires that end beside it: rom_49_data, demultiplexer_49_out3, Volume
  // Buzzer #(.waveform("Sawtooth")) buzzer_212: pin names not known; wires that end beside it: rom_50_data, demultiplexer_50_out3, Volume
  // Buzzer #(.waveform("Sawtooth")) buzzer_213: pin names not known; wires that end beside it: rom_51_data, demultiplexer_51_out3, Volume
  // Buzzer #(.waveform("Sawtooth")) buzzer_214: pin names not known; wires that end beside it: rom_52_data, demultiplexer_52_out3, Volume
  // Buzzer #(.waveform("Sawtooth")) buzzer_215: pin names not known; wires that end beside it: rom_53_data, demultiplexer_53_out3, Volume
  // Buzzer #(.waveform("Sawtooth")) buzzer_216: pin names not known; wires that end beside it: rom_54_data, demultiplexer_54_out3, Volume
  Button button_55 (.out(button_55_out));
  xor xor_55 (xor_55_out, in_9, button_55_out);
  Demultiplexer #(.select(2)) demultiplexer_55 (
    .out0(demultiplexer_55_out0), .out1(demultiplexer_55_out1), .out2(demultiplexer_55_out2),
    .out3(demultiplexer_55_out3), .in(xor_55_out), .sel(Waveform));
  ROM #(.addrWidth(2), .dataWidth(14)) rom_55 (.addr(2'b00), .data(rom_55_data));
  Button button_56 (.out(button_56_out));
  xor xor_56 (xor_56_out, in_21, button_56_out);
  Demultiplexer #(.select(2)) demultiplexer_56 (
    .out0(demultiplexer_56_out0), .out1(demultiplexer_56_out1), .out2(demultiplexer_56_out2),
    .out3(demultiplexer_56_out3), .in(xor_56_out), .sel(Waveform));
  ROM #(.addrWidth(2), .dataWidth(14)) rom_56 (.addr(2'b00), .data(rom_56_data));
  Button button_57 (.out(button_57_out));
  xor xor_57 (xor_57_out, in_33, button_57_out);
  Demultiplexer #(.select(2)) demultiplexer_57 (
    .out0(demultiplexer_57_out0), .out1(demultiplexer_57_out1), .out2(demultiplexer_57_out2),
    .out3(demultiplexer_57_out3), .in(xor_57_out), .sel(Waveform));
  ROM #(.addrWidth(2), .dataWidth(14)) rom_57 (.addr(2'b00), .data(rom_57_data));
  Button button_58 (.out(button_58_out));
  xor xor_58 (xor_58_out, in_45, button_58_out);
  Demultiplexer #(.select(2)) demultiplexer_58 (
    .out0(demultiplexer_58_out0), .out1(demultiplexer_58_out1), .out2(demultiplexer_58_out2),
    .out3(demultiplexer_58_out3), .in(xor_58_out), .sel(Waveform));
  ROM #(.addrWidth(2), .dataWidth(14)) rom_58 (.addr(2'b00), .data(rom_58_data));
  Button button_59 (.out(button_59_out));
  xor xor_59 (xor_59_out, in_57, button_59_out);
  Demultiplexer #(.select(2)) demultiplexer_59 (
    .out0(demultiplexer_59_out0), .out1(demultiplexer_59_out1), .out2(demultiplexer_59_out2),
    .out3(demultiplexer_59_out3), .in(xor_59_out), .sel(Waveform));
  ROM #(.addrWidth(2), .dataWidth(14)) rom_59 (.addr(2'b00), .data(rom_59_data));
  Button button_60 (.out(button_60_out));
  xor xor_60 (xor_60_out, in_69, button_60_out);
  Demultiplexer #(.select(2)) demultiplexer_60 (
    .out0(demultiplexer_60_out0), .out1(demultiplexer_60_out1), .out2(demultiplexer_60_out2),
    .out3(demultiplexer_60_out3), .in(xor_60_out), .sel(Waveform));
  ROM #(.addrWidth(2), .dataWidth(14)) rom_60 (.addr(2'b00), .data(rom_60_data));
  Button button_61 (.out(button_61_out));
  xor xor_61 (xor_61_out, in_81, button_61_out);
  Demultiplexer #(.select(2)) demultiplexer_61 (
    .out0(demultiplexer_61_out0), .out1(demultiplexer_61_out1), .out2(demultiplexer_61_out2),
    .out3(demultiplexer_61_out3), .in(xor_61_out), .sel(Waveform));
  ROM #(.addrWidth(2), .dataWidth(14)) rom_61 (.addr(2'b00), .data(rom_61_data));
  Button button_62 (.out(button_62_out));
  xor xor_62 (xor_62_out, in_93, button_62_out);
  Demultiplexer #(.select(2)) demultiplexer_62 (
    .out0(demultiplexer_62_out0), .out1(demultiplexer_62_out1), .out2(demultiplexer_62_out2),
    .out3(demultiplexer_62_out3), .in(xor_62_out), .sel(Waveform));
  ROM #(.addrWidth(2), .dataWidth(14)) rom_62 (.addr(2'b00), .data(rom_62_data));
  Button button_63 (.out(button_63_out));
  xor xor_63 (xor_63_out, in_105, button_63_out);
  Demultiplexer #(.select(2)) demultiplexer_63 (
    .out0(demultiplexer_63_out0), .out1(demultiplexer_63_out1), .out2(demultiplexer_63_out2),
    .out3(demultiplexer_63_out3), .in(xor_63_out), .sel(Waveform));
  ROM #(.addrWidth(2), .dataWidth(14)) rom_63 (.addr(2'b00), .data(rom_63_data));
  // Buzzer #(.waveform("Square")) buzzer_217: pin names not known; wires that end beside it: rom_55_data, demultiplexer_55_out1, Volume
  // Buzzer buzzer_218: pin names not known; wires that end beside it: rom_55_data, demultiplexer_55_out0, Volume
  // Buzzer #(.waveform("Square")) buzzer_219: pin names not known; wires that end beside it: rom_56_data, demultiplexer_56_out1, Volume
  // Buzzer buzzer_220: pin names not known; wires that end beside it: rom_56_data, demultiplexer_56_out0, Volume
  // Buzzer #(.waveform("Square")) buzzer_221: pin names not known; wires that end beside it: rom_57_data, demultiplexer_57_out1, Volume
  // Buzzer buzzer_222: pin names not known; wires that end beside it: rom_57_data, demultiplexer_57_out0, Volume
  // Buzzer #(.waveform("Square")) buzzer_223: pin names not known; wires that end beside it: rom_58_data, demultiplexer_58_out1, Volume
  // Buzzer buzzer_224: pin names not known; wires that end beside it: rom_58_data, demultiplexer_58_out0, Volume
  // Buzzer #(.waveform("Square")) buzzer_225: pin names not known; wires that end beside it: rom_59_data, demultiplexer_59_out1, Volume
  // Buzzer buzzer_226: pin names not known; wires that end beside it: rom_59_data, demultiplexer_59_out0, Volume
  // Buzzer #(.waveform("Square")) buzzer_227: pin names not known; wires that end beside it: rom_60_data, demultiplexer_60_out1, Volume
  // Buzzer buzzer_228: pin names not known; wires that end beside it: rom_60_data, demultiplexer_60_out0, Volume
  // Buzzer #(.waveform("Square")) buzzer_229: pin names not known; wires that end beside it: rom_61_data, demultiplexer_61_out1, Volume
  // Buzzer buzzer_230: pin names not known; wires that end beside it: rom_61_data, demultiplexer_61_out0, Volume
  // Buzzer #(.waveform("Square")) buzzer_231: pin names not known; wires that end beside it: rom_62_data, demultiplexer_62_out1, Volume
  // Buzzer buzzer_232: pin names not known; wires that end beside it: rom_62_data, demultiplexer_62_out0, Volume
  // Buzzer #(.waveform("Square")) buzzer_233: pin names not known; wires that end beside it: rom_63_data, demultiplexer_63_out1, Volume
  // Buzzer buzzer_234: pin names not known; wires that end beside it: rom_63_data, demultiplexer_63_out0, Volume
  // Buzzer #(.waveform("Sawtooth")) buzzer_235: pin names not known; wires that end beside it: rom_55_data, demultiplexer_55_out3, Volume
  // Buzzer #(.waveform("Triangle")) buzzer_236: pin names not known; wires that end beside it: rom_55_data, demultiplexer_55_out2, Volume
  // Buzzer #(.waveform("Sawtooth")) buzzer_237: pin names not known; wires that end beside it: rom_56_data, demultiplexer_56_out3, Volume
  // Buzzer #(.waveform("Triangle")) buzzer_238: pin names not known; wires that end beside it: rom_56_data, demultiplexer_56_out2, Volume
  // Buzzer #(.waveform("Sawtooth")) buzzer_239: pin names not known; wires that end beside it: rom_57_data, demultiplexer_57_out3, Volume
  // Buzzer #(.waveform("Triangle")) buzzer_240: pin names not known; wires that end beside it: rom_57_data, demultiplexer_57_out2, Volume
  // Buzzer #(.waveform("Sawtooth")) buzzer_241: pin names not known; wires that end beside it: rom_58_data, demultiplexer_58_out3, Volume
  // Buzzer #(.waveform("Triangle")) buzzer_242: pin names not known; wires that end beside it: rom_58_data, demultiplexer_58_out2, Volume
  // Buzzer #(.waveform("Sawtooth")) buzzer_243: pin names not known; wires that end beside it: rom_59_data, demultiplexer_59_out3, Volume
  // Buzzer #(.waveform("Triangle")) buzzer_244: pin names not known; wires that end beside it: rom_59_data, demultiplexer_59_out2, Volume
  // Buzzer #(.waveform("Sawtooth")) buzzer_245: pin names not known; wires that end beside it: rom_60_data, demultiplexer_60_out3, Volume
  // Buzzer #(.waveform("Triangle")) buzzer_246: pin names not known; wires that end beside it: rom_60_data, demultiplexer_60_out2, Volume
  // Buzzer #(.waveform("Sawtooth")) buzzer_247: pin names not known; wires that end beside it: rom_61_data, demultiplexer_61_out3, Volume
  // Buzzer #(.waveform("Triangle")) buzzer_248: pin names not known; wires that end beside it: rom_61_data, demultiplexer_61_out2, Volume
  // Buzzer #(.waveform("Sawtooth")) buzzer_249: pin names not known; wires that end beside it: rom_62_data, demultiplexer_62_out3, Volume
  // Buzzer #(.waveform("Triangle")) buzzer_250: pin names not known; wires that end beside it: rom_62_data, demultiplexer_62_out2, Volume
  // Buzzer #(.waveform("Sawtooth")) buzzer_251: pin names not known; wires that end beside it: rom_63_data, demultiplexer_63_out3, Volume
  // Buzzer #(.waveform("Triangle")) buzzer_252: pin names not known; wires that end beside it: rom_63_data, demultiplexer_63_out2, Volume
  Button button_64 (.out(button_64_out));
  xor xor_64 (xor_64_out, in_10, button_64_out);
  Demultiplexer #(.select(2)) demultiplexer_64 (
    .out0(demultiplexer_64_out0), .out1(demultiplexer_64_out1), .out2(demultiplexer_64_out2),
    .out3(demultiplexer_64_out3), .in(xor_64_out), .sel(Waveform));
  ROM #(.addrWidth(2), .dataWidth(14)) rom_64 (.addr(2'b00), .data(rom_64_data));
  Button button_65 (.out(button_65_out));
  xor xor_65 (xor_65_out, in_22, button_65_out);
  Demultiplexer #(.select(2)) demultiplexer_65 (
    .out0(demultiplexer_65_out0), .out1(demultiplexer_65_out1), .out2(demultiplexer_65_out2),
    .out3(demultiplexer_65_out3), .in(xor_65_out), .sel(Waveform));
  ROM #(.addrWidth(2), .dataWidth(14)) rom_65 (.addr(2'b00), .data(rom_65_data));
  Button button_66 (.out(button_66_out));
  xor xor_66 (xor_66_out, in_34, button_66_out);
  Demultiplexer #(.select(2)) demultiplexer_66 (
    .out0(demultiplexer_66_out0), .out1(demultiplexer_66_out1), .out2(demultiplexer_66_out2),
    .out3(demultiplexer_66_out3), .in(xor_66_out), .sel(Waveform));
  ROM #(.addrWidth(2), .dataWidth(14)) rom_66 (.addr(2'b00), .data(rom_66_data));
  Button button_67 (.out(button_67_out));
  xor xor_67 (xor_67_out, in_46, button_67_out);
  Demultiplexer #(.select(2)) demultiplexer_67 (
    .out0(demultiplexer_67_out0), .out1(demultiplexer_67_out1), .out2(demultiplexer_67_out2),
    .out3(demultiplexer_67_out3), .in(xor_67_out), .sel(Waveform));
  ROM #(.addrWidth(2), .dataWidth(14)) rom_67 (.addr(2'b00), .data(rom_67_data));
  Button button_68 (.out(button_68_out));
  xor xor_68 (xor_68_out, in_58, button_68_out);
  Demultiplexer #(.select(2)) demultiplexer_68 (
    .out0(demultiplexer_68_out0), .out1(demultiplexer_68_out1), .out2(demultiplexer_68_out2),
    .out3(demultiplexer_68_out3), .in(xor_68_out), .sel(Waveform));
  ROM #(.addrWidth(2), .dataWidth(14)) rom_68 (.addr(2'b00), .data(rom_68_data));
  Button button_69 (.out(button_69_out));
  xor xor_69 (xor_69_out, in_70, button_69_out);
  Demultiplexer #(.select(2)) demultiplexer_69 (
    .out0(demultiplexer_69_out0), .out1(demultiplexer_69_out1), .out2(demultiplexer_69_out2),
    .out3(demultiplexer_69_out3), .in(xor_69_out), .sel(Waveform));
  ROM #(.addrWidth(2), .dataWidth(14)) rom_69 (.addr(2'b00), .data(rom_69_data));
  Button button_70 (.out(button_70_out));
  xor xor_70 (xor_70_out, in_82, button_70_out);
  Demultiplexer #(.select(2)) demultiplexer_70 (
    .out0(demultiplexer_70_out0), .out1(demultiplexer_70_out1), .out2(demultiplexer_70_out2),
    .out3(demultiplexer_70_out3), .in(xor_70_out), .sel(Waveform));
  ROM #(.addrWidth(2), .dataWidth(14)) rom_70 (.addr(2'b00), .data(rom_70_data));
  Button button_71 (.out(button_71_out));
  xor xor_71 (xor_71_out, in_94, button_71_out);
  Demultiplexer #(.select(2)) demultiplexer_71 (
    .out0(demultiplexer_71_out0), .out1(demultiplexer_71_out1), .out2(demultiplexer_71_out2),
    .out3(demultiplexer_71_out3), .in(xor_71_out), .sel(Waveform));
  ROM #(.addrWidth(2), .dataWidth(14)) rom_71 (.addr(2'b00), .data(rom_71_data));
  Button button_72 (.out(button_72_out));
  xor xor_72 (xor_72_out, in_106, button_72_out);
  Demultiplexer #(.select(2)) demultiplexer_72 (
    .out0(demultiplexer_72_out0), .out1(demultiplexer_72_out1), .out2(demultiplexer_72_out2),
    .out3(demultiplexer_72_out3), .in(xor_72_out), .sel(Waveform));
  ROM #(.addrWidth(2), .dataWidth(14)) rom_72 (.addr(2'b00), .data(rom_72_data));
  // Buzzer buzzer_253: pin names not known; wires that end beside it: rom_64_data, demultiplexer_64_out0, Volume
  // Buzzer buzzer_254: pin names not known; wires that end beside it: rom_65_data, demultiplexer_65_out0, Volume
  // Buzzer buzzer_255: pin names not known; wires that end beside it: rom_66_data, demultiplexer_66_out0, Volume
  // Buzzer buzzer_256: pin names not known; wires that end beside it: rom_67_data, demultiplexer_67_out0, Volume
  // Buzzer buzzer_257: pin names not known; wires that end beside it: rom_68_data, demultiplexer_68_out0, Volume
  // Buzzer buzzer_258: pin names not known; wires that end beside it: rom_69_data, demultiplexer_69_out0, Volume
  // Buzzer buzzer_259: pin names not known; wires that end beside it: rom_70_data, demultiplexer_70_out0, Volume
  // Buzzer buzzer_260: pin names not known; wires that end beside it: rom_71_data, demultiplexer_71_out0, Volume
  // Buzzer buzzer_261: pin names not known; wires that end beside it: rom_72_data, demultiplexer_72_out0, Volume
  // Buzzer #(.waveform("Triangle")) buzzer_262: pin names not known; wires that end beside it: rom_64_data, demultiplexer_64_out2, Volume
  // Buzzer #(.waveform("Square")) buzzer_263: pin names not known; wires that end beside it: rom_64_data, demultiplexer_64_out1, Volume
  // Buzzer #(.waveform("Triangle")) buzzer_264: pin names not known; wires that end beside it: rom_65_data, demultiplexer_65_out2, Volume
  // Buzzer #(.waveform("Square")) buzzer_265: pin names not known; wires that end beside it: rom_65_data, demultiplexer_65_out1, Volume
  // Buzzer #(.waveform("Triangle")) buzzer_266: pin names not known; wires that end beside it: rom_66_data, demultiplexer_66_out2, Volume
  // Buzzer #(.waveform("Square")) buzzer_267: pin names not known; wires that end beside it: rom_66_data, demultiplexer_66_out1, Volume
  // Buzzer #(.waveform("Triangle")) buzzer_268: pin names not known; wires that end beside it: rom_67_data, demultiplexer_67_out2, Volume
  // Buzzer #(.waveform("Square")) buzzer_269: pin names not known; wires that end beside it: rom_67_data, demultiplexer_67_out1, Volume
  // Buzzer #(.waveform("Triangle")) buzzer_270: pin names not known; wires that end beside it: rom_68_data, demultiplexer_68_out2, Volume
  // Buzzer #(.waveform("Square")) buzzer_271: pin names not known; wires that end beside it: rom_68_data, demultiplexer_68_out1, Volume
  // Buzzer #(.waveform("Triangle")) buzzer_272: pin names not known; wires that end beside it: rom_69_data, demultiplexer_69_out2, Volume
  // Buzzer #(.waveform("Square")) buzzer_273: pin names not known; wires that end beside it: rom_69_data, demultiplexer_69_out1, Volume
  // Buzzer #(.waveform("Triangle")) buzzer_274: pin names not known; wires that end beside it: rom_70_data, demultiplexer_70_out2, Volume
  // Buzzer #(.waveform("Square")) buzzer_275: pin names not known; wires that end beside it: rom_70_data, demultiplexer_70_out1, Volume
  // Buzzer #(.waveform("Triangle")) buzzer_276: pin names not known; wires that end beside it: rom_71_data, demultiplexer_71_out2, Volume
  // Buzzer #(.waveform("Square")) buzzer_277: pin names not known; wires that end beside it: rom_71_data, demultiplexer_71_out1, Volume
  // Buzzer #(.waveform("Triangle")) buzzer_278: pin names not known; wires that end beside it: rom_72_data, demultiplexer_72_out2, Volume
  // Buzzer #(.waveform("Square")) buzzer_279: pin names not known; wires that end beside it: rom_72_data, demultiplexer_72_out1, Volume
  // Buzzer #(.waveform("Sawtooth")) buzzer_280: pin names not known; wires that end beside it: rom_64_data, demultiplexer_64_out3, Volume
  // Buzzer #(.waveform("Sawtooth")) buzzer_281: pin names not known; wires that end beside it: rom_65_data, demultiplexer_65_out3, Volume
  // Buzzer #(.waveform("Sawtooth")) buzzer_282: pin names not known; wires that end beside it: rom_66_data, demultiplexer_66_out3, Volume
  // Buzzer #(.waveform("Sawtooth")) buzzer_283: pin names not known; wires that end beside it: rom_67_data, demultiplexer_67_out3, Volume
  // Buzzer #(.waveform("Sawtooth")) buzzer_284: pin names not known; wires that end beside it: rom_68_data, demultiplexer_68_out3, Volume
  // Buzzer #(.waveform("Sawtooth")) buzzer_285: pin names not known; wires that end beside it: rom_69_data, demultiplexer_69_out3, Volume
  // Buzzer #(.waveform("Sawtooth")) buzzer_286: pin names not known; wires that end beside it: rom_70_data, demultiplexer_70_out3, Volume
  // Buzzer #(.waveform("Sawtooth")) buzzer_287: pin names not known; wires that end beside it: rom_71_data, demultiplexer_71_out3, Volume
  // Buzzer #(.waveform("Sawtooth")) buzzer_288: pin names not known; wires that end beside it: rom_72_data, demultiplexer_72_out3, Volume
  Button button_73 (.out(button_73_out));
  xor xor_73 (xor_73_out, in_11, button_73_out);
  Demultiplexer #(.select(2)) demultiplexer_73 (
    .out0(demultiplexer_73_out0), .out1(demultiplexer_73_out1), .out2(demultiplexer_73_out2),
    .out3(demultiplexer_73_out3), .in(xor_73_out), .sel(Waveform));
  ROM #(.addrWidth(2), .dataWidth(14)) rom_73 (.addr(2'b00), .data(rom_73_data));
  Button button_74 (.out(button_74_out));
  xor xor_74 (xor_74_out, in_23, button_74_out);
  Demultiplexer #(.select(2)) demultiplexer_74 (
    .out0(demultiplexer_74_out0), .out1(demultiplexer_74_out1), .out2(demultiplexer_74_out2),
    .out3(demultiplexer_74_out3), .in(xor_74_out), .sel(Waveform));
  ROM #(.addrWidth(2), .dataWidth(14)) rom_74 (.addr(2'b00), .data(rom_74_data));
  Button button_75 (.out(button_75_out));
  xor xor_75 (xor_75_out, in_35, button_75_out);
  Demultiplexer #(.select(2)) demultiplexer_75 (
    .out0(demultiplexer_75_out0), .out1(demultiplexer_75_out1), .out2(demultiplexer_75_out2),
    .out3(demultiplexer_75_out3), .in(xor_75_out), .sel(Waveform));
  ROM #(.addrWidth(2), .dataWidth(14)) rom_75 (.addr(2'b00), .data(rom_75_data));
  Button button_76 (.out(button_76_out));
  xor xor_76 (xor_76_out, in_47, button_76_out);
  Demultiplexer #(.select(2)) demultiplexer_76 (
    .out0(demultiplexer_76_out0), .out1(demultiplexer_76_out1), .out2(demultiplexer_76_out2),
    .out3(demultiplexer_76_out3), .in(xor_76_out), .sel(Waveform));
  ROM #(.addrWidth(2), .dataWidth(14)) rom_76 (.addr(2'b00), .data(rom_76_data));
  Button button_77 (.out(button_77_out));
  xor xor_77 (xor_77_out, in_59, button_77_out);
  Demultiplexer #(.select(2)) demultiplexer_77 (
    .out0(demultiplexer_77_out0), .out1(demultiplexer_77_out1), .out2(demultiplexer_77_out2),
    .out3(demultiplexer_77_out3), .in(xor_77_out), .sel(Waveform));
  ROM #(.addrWidth(2), .dataWidth(14)) rom_77 (.addr(2'b00), .data(rom_77_data));
  Button button_78 (.out(button_78_out));
  xor xor_78 (xor_78_out, in_71, button_78_out);
  Demultiplexer #(.select(2)) demultiplexer_78 (
    .out0(demultiplexer_78_out0), .out1(demultiplexer_78_out1), .out2(demultiplexer_78_out2),
    .out3(demultiplexer_78_out3), .in(xor_78_out), .sel(Waveform));
  ROM #(.addrWidth(2), .dataWidth(14)) rom_78 (.addr(2'b00), .data(rom_78_data));
  Button button_79 (.out(button_79_out));
  xor xor_79 (xor_79_out, in_83, button_79_out);
  Demultiplexer #(.select(2)) demultiplexer_79 (
    .out0(demultiplexer_79_out0), .out1(demultiplexer_79_out1), .out2(demultiplexer_79_out2),
    .out3(demultiplexer_79_out3), .in(xor_79_out), .sel(Waveform));
  ROM #(.addrWidth(2), .dataWidth(14)) rom_79 (.addr(2'b00), .data(rom_79_data));
  Button button_80 (.out(button_80_out));
  xor xor_80 (xor_80_out, in_95, button_80_out);
  Demultiplexer #(.select(2)) demultiplexer_80 (
    .out0(demultiplexer_80_out0), .out1(demultiplexer_80_out1), .out2(demultiplexer_80_out2),
    .out3(demultiplexer_80_out3), .in(xor_80_out), .sel(Waveform));
  ROM #(.addrWidth(2), .dataWidth(14)) rom_80 (.addr(2'b00), .data(rom_80_data));
  Button button_81 (.out(button_81_out));
  xor xor_81 (xor_81_out, in_107, button_81_out);
  Demultiplexer #(.select(2)) demultiplexer_81 (
    .out0(demultiplexer_81_out0), .out1(demultiplexer_81_out1), .out2(demultiplexer_81_out2),
    .out3(demultiplexer_81_out3), .in(xor_81_out), .sel(Waveform));
  ROM #(.addrWidth(2), .dataWidth(14)) rom_81 (.addr(2'b00), .data(rom_81_data));
  // Buzzer #(.waveform("Square")) buzzer_289: pin names not known; wires that end beside it: rom_73_data, demultiplexer_73_out1, Volume
  // Buzzer buzzer_290: pin names not known; wires that end beside it: rom_73_data, demultiplexer_73_out0, Volume
  // Buzzer #(.waveform("Square")) buzzer_291: pin names not known; wires that end beside it: rom_74_data, demultiplexer_74_out1, Volume
  // Buzzer buzzer_292: pin names not known; wires that end beside it: rom_74_data, demultiplexer_74_out0, Volume
  // Buzzer #(.waveform("Square")) buzzer_293: pin names not known; wires that end beside it: rom_75_data, demultiplexer_75_out1, Volume
  // Buzzer buzzer_294: pin names not known; wires that end beside it: rom_75_data, demultiplexer_75_out0, Volume
  // Buzzer #(.waveform("Square")) buzzer_295: pin names not known; wires that end beside it: rom_76_data, demultiplexer_76_out1, Volume
  // Buzzer buzzer_296: pin names not known; wires that end beside it: rom_76_data, demultiplexer_76_out0, Volume
  // Buzzer #(.waveform("Square")) buzzer_297: pin names not known; wires that end beside it: rom_77_data, demultiplexer_77_out1, Volume
  // Buzzer buzzer_298: pin names not known; wires that end beside it: rom_77_data, demultiplexer_77_out0, Volume
  // Buzzer #(.waveform("Square")) buzzer_299: pin names not known; wires that end beside it: rom_78_data, demultiplexer_78_out1, Volume
  // Buzzer buzzer_300: pin names not known; wires that end beside it: rom_78_data, demultiplexer_78_out0, Volume
  // Buzzer #(.waveform("Square")) buzzer_301: pin names not known; wires that end beside it: rom_79_data, demultiplexer_79_out1, Volume
  // Buzzer buzzer_302: pin names not known; wires that end beside it: rom_79_data, demultiplexer_79_out0, Volume
  // Buzzer #(.waveform("Square")) buzzer_303: pin names not known; wires that end beside it: rom_80_data, demultiplexer_80_out1, Volume
  // Buzzer buzzer_304: pin names not known; wires that end beside it: rom_80_data, demultiplexer_80_out0, Volume
  // Buzzer #(.waveform("Square")) buzzer_305: pin names not known; wires that end beside it: rom_81_data, demultiplexer_81_out1, Volume
  // Buzzer buzzer_306: pin names not known; wires that end beside it: rom_81_data, demultiplexer_81_out0, Volume
  // Buzzer #(.waveform("Sawtooth")) buzzer_307: pin names not known; wires that end beside it: rom_73_data, demultiplexer_73_out3, Volume
  // Buzzer #(.waveform("Triangle")) buzzer_308: pin names not known; wires that end beside it: rom_73_data, demultiplexer_73_out2, Volume
  // Buzzer #(.waveform("Sawtooth")) buzzer_309: pin names not known; wires that end beside it: rom_74_data, demultiplexer_74_out3, Volume
  // Buzzer #(.waveform("Triangle")) buzzer_310: pin names not known; wires that end beside it: rom_74_data, demultiplexer_74_out2, Volume
  // Buzzer #(.waveform("Sawtooth")) buzzer_311: pin names not known; wires that end beside it: rom_75_data, demultiplexer_75_out3, Volume
  // Buzzer #(.waveform("Triangle")) buzzer_312: pin names not known; wires that end beside it: rom_75_data, demultiplexer_75_out2, Volume
  // Buzzer #(.waveform("Sawtooth")) buzzer_313: pin names not known; wires that end beside it: rom_76_data, demultiplexer_76_out3, Volume
  // Buzzer #(.waveform("Triangle")) buzzer_314: pin names not known; wires that end beside it: rom_76_data, demultiplexer_76_out2, Volume
  // Buzzer #(.waveform("Sawtooth")) buzzer_315: pin names not known; wires that end beside it: rom_77_data, demultiplexer_77_out3, Volume
  // Buzzer #(.waveform("Triangle")) buzzer_316: pin names not known; wires that end beside it: rom_77_data, demultiplexer_77_out2, Volume
  // Buzzer #(.waveform("Sawtooth")) buzzer_317: pin names not known; wires that end beside it: rom_78_data, demultiplexer_78_out3, Volume
  // Buzzer #(.waveform("Triangle")) buzzer_318: pin names not known; wires that end beside it: rom_78_data, demultiplexer_78_out2, Volume
  // Buzzer #(.waveform("Sawtooth")) buzzer_319: pin names not known; wires that end beside it: rom_79_data, demultiplexer_79_out3, Volume
  // Buzzer #(.waveform("Triangle")) buzzer_320: pin names not known; wires that end beside it: rom_79_data, demultiplexer_79_out2, Volume
  // Buzzer #(.waveform("Sawtooth")) buzzer_321: pin names not known; wires that end beside it: rom_80_data, demultiplexer_80_out3, Volume
  // Buzzer #(.waveform("Triangle")) buzzer_322: pin names not known; wires that end beside it: rom_80_data, demultiplexer_80_out2, Volume
  // Buzzer #(.waveform("Sawtooth")) buzzer_323: pin names not known; wires that end beside it: rom_81_data, demultiplexer_81_out3, Volume
  // Buzzer #(.waveform("Triangle")) buzzer_324: pin names not known; wires that end beside it: rom_81_data, demultiplexer_81_out2, Volume
  Button button_82 (.out(button_82_out));
  xor xor_82 (xor_82_out, in_12, button_82_out);
  Demultiplexer #(.select(2)) demultiplexer_82 (
    .out0(demultiplexer_82_out0), .out1(demultiplexer_82_out1), .out2(demultiplexer_82_out2),
    .out3(demultiplexer_82_out3), .in(xor_82_out), .sel(Waveform));
  ROM #(.addrWidth(2), .dataWidth(14)) rom_82 (.addr(2'b00), .data(rom_82_data));
  Button button_83 (.out(button_83_out));
  xor xor_83 (xor_83_out, in_24, button_83_out);
  Demultiplexer #(.select(2)) demultiplexer_83 (
    .out0(demultiplexer_83_out0), .out1(demultiplexer_83_out1), .out2(demultiplexer_83_out2),
    .out3(demultiplexer_83_out3), .in(xor_83_out), .sel(Waveform));
  ROM #(.addrWidth(2), .dataWidth(14)) rom_83 (.addr(2'b00), .data(rom_83_data));
  Button button_84 (.out(button_84_out));
  xor xor_84 (xor_84_out, in_36, button_84_out);
  Demultiplexer #(.select(2)) demultiplexer_84 (
    .out0(demultiplexer_84_out0), .out1(demultiplexer_84_out1), .out2(demultiplexer_84_out2),
    .out3(demultiplexer_84_out3), .in(xor_84_out), .sel(Waveform));
  ROM #(.addrWidth(2), .dataWidth(14)) rom_84 (.addr(2'b00), .data(rom_84_data));
  Button button_85 (.out(button_85_out));
  xor xor_85 (xor_85_out, in_48, button_85_out);
  Demultiplexer #(.select(2)) demultiplexer_85 (
    .out0(demultiplexer_85_out0), .out1(demultiplexer_85_out1), .out2(demultiplexer_85_out2),
    .out3(demultiplexer_85_out3), .in(xor_85_out), .sel(Waveform));
  ROM #(.addrWidth(2), .dataWidth(14)) rom_85 (.addr(2'b00), .data(rom_85_data));
  Button button_86 (.out(button_86_out));
  xor xor_86 (xor_86_out, in_60, button_86_out);
  Demultiplexer #(.select(2)) demultiplexer_86 (
    .out0(demultiplexer_86_out0), .out1(demultiplexer_86_out1), .out2(demultiplexer_86_out2),
    .out3(demultiplexer_86_out3), .in(xor_86_out), .sel(Waveform));
  ROM #(.addrWidth(2), .dataWidth(14)) rom_86 (.addr(2'b00), .data(rom_86_data));
  Button button_87 (.out(button_87_out));
  xor xor_87 (xor_87_out, in_72, button_87_out);
  Demultiplexer #(.select(2)) demultiplexer_87 (
    .out0(demultiplexer_87_out0), .out1(demultiplexer_87_out1), .out2(demultiplexer_87_out2),
    .out3(demultiplexer_87_out3), .in(xor_87_out), .sel(Waveform));
  ROM #(.addrWidth(2), .dataWidth(14)) rom_87 (.addr(2'b00), .data(rom_87_data));
  Button button_88 (.out(button_88_out));
  xor xor_88 (xor_88_out, in_84, button_88_out);
  Demultiplexer #(.select(2)) demultiplexer_88 (
    .out0(demultiplexer_88_out0), .out1(demultiplexer_88_out1), .out2(demultiplexer_88_out2),
    .out3(demultiplexer_88_out3), .in(xor_88_out), .sel(Waveform));
  ROM #(.addrWidth(2), .dataWidth(14)) rom_88 (.addr(2'b00), .data(rom_88_data));
  Button button_89 (.out(button_89_out));
  xor xor_89 (xor_89_out, in_96, button_89_out);
  Demultiplexer #(.select(2)) demultiplexer_89 (
    .out0(demultiplexer_89_out0), .out1(demultiplexer_89_out1), .out2(demultiplexer_89_out2),
    .out3(demultiplexer_89_out3), .in(xor_89_out), .sel(Waveform));
  ROM #(.addrWidth(2), .dataWidth(14)) rom_89 (.addr(2'b00), .data(rom_89_data));
  Button button_90 (.out(button_90_out));
  xor xor_90 (xor_90_out, in_108, button_90_out);
  Demultiplexer #(.select(2)) demultiplexer_90 (
    .out0(demultiplexer_90_out0), .out1(demultiplexer_90_out1), .out2(demultiplexer_90_out2),
    .out3(demultiplexer_90_out3), .in(xor_90_out), .sel(Waveform));
  ROM #(.addrWidth(2), .dataWidth(14)) rom_90 (.addr(2'b00), .data(rom_90_data));
  // Buzzer buzzer_325: pin names not known; wires that end beside it: rom_82_data, demultiplexer_82_out0, Volume
  // Buzzer buzzer_326: pin names not known; wires that end beside it: rom_83_data, demultiplexer_83_out0, Volume
  // Buzzer buzzer_327: pin names not known; wires that end beside it: rom_84_data, demultiplexer_84_out0, Volume
  // Buzzer buzzer_328: pin names not known; wires that end beside it: rom_85_data, demultiplexer_85_out0, Volume
  // Buzzer buzzer_329: pin names not known; wires that end beside it: rom_86_data, demultiplexer_86_out0, Volume
  // Buzzer buzzer_330: pin names not known; wires that end beside it: rom_87_data, demultiplexer_87_out0, Volume
  // Buzzer buzzer_331: pin names not known; wires that end beside it: rom_88_data, demultiplexer_88_out0, Volume
  // Buzzer buzzer_332: pin names not known; wires that end beside it: rom_89_data, demultiplexer_89_out0, Volume
  // Buzzer buzzer_333: pin names not known; wires that end beside it: rom_90_data, demultiplexer_90_out0, Volume
  // Buzzer #(.waveform("Triangle")) buzzer_334: pin names not known; wires that end beside it: rom_82_data, demultiplexer_82_out2, Volume
  // Buzzer #(.waveform("Square")) buzzer_335: pin names not known; wires that end beside it: rom_82_data, demultiplexer_82_out1, Volume
  // Buzzer #(.waveform("Triangle")) buzzer_336: pin names not known; wires that end beside it: rom_83_data, demultiplexer_83_out2, Volume
  // Buzzer #(.waveform("Square")) buzzer_337: pin names not known; wires that end beside it: rom_83_data, demultiplexer_83_out1, Volume
  // Buzzer #(.waveform("Triangle")) buzzer_338: pin names not known; wires that end beside it: rom_84_data, demultiplexer_84_out2, Volume
  // Buzzer #(.waveform("Square")) buzzer_339: pin names not known; wires that end beside it: rom_84_data, demultiplexer_84_out1, Volume
  // Buzzer #(.waveform("Triangle")) buzzer_340: pin names not known; wires that end beside it: rom_85_data, demultiplexer_85_out2, Volume
  // Buzzer #(.waveform("Square")) buzzer_341: pin names not known; wires that end beside it: rom_85_data, demultiplexer_85_out1, Volume
  // Buzzer #(.waveform("Triangle")) buzzer_342: pin names not known; wires that end beside it: rom_86_data, demultiplexer_86_out2, Volume
  // Buzzer #(.waveform("Square")) buzzer_343: pin names not known; wires that end beside it: rom_86_data, demultiplexer_86_out1, Volume
  // Buzzer #(.waveform("Triangle")) buzzer_344: pin names not known; wires that end beside it: rom_87_data, demultiplexer_87_out2, Volume
  // Buzzer #(.waveform("Square")) buzzer_345: pin names not known; wires that end beside it: rom_87_data, demultiplexer_87_out1, Volume
  // Buzzer #(.waveform("Triangle")) buzzer_346: pin names not known; wires that end beside it: rom_88_data, demultiplexer_88_out2, Volume
  // Buzzer #(.waveform("Square")) buzzer_347: pin names not known; wires that end beside it: rom_88_data, demultiplexer_88_out1, Volume
  // Buzzer #(.waveform("Triangle")) buzzer_348: pin names not known; wires that end beside it: rom_89_data, demultiplexer_89_out2, Volume
  // Buzzer #(.waveform("Square")) buzzer_349: pin names not known; wires that end beside it: rom_89_data, demultiplexer_89_out1, Volume
  // Buzzer #(.waveform("Triangle")) buzzer_350: pin names not known; wires that end beside it: rom_90_data, demultiplexer_90_out2, Volume
  // Buzzer #(.waveform("Square")) buzzer_351: pin names not known; wires that end beside it: rom_90_data, demultiplexer_90_out1, Volume
  // Buzzer #(.waveform("Sawtooth")) buzzer_352: pin names not known; wires that end beside it: rom_82_data, demultiplexer_82_out3, Volume
  // Buzzer #(.waveform("Sawtooth")) buzzer_353: pin names not known; wires that end beside it: rom_83_data, demultiplexer_83_out3, Volume
  // Buzzer #(.waveform("Sawtooth")) buzzer_354: pin names not known; wires that end beside it: rom_84_data, demultiplexer_84_out3, Volume
  // Buzzer #(.waveform("Sawtooth")) buzzer_355: pin names not known; wires that end beside it: rom_85_data, demultiplexer_85_out3, Volume
  // Buzzer #(.waveform("Sawtooth")) buzzer_356: pin names not known; wires that end beside it: rom_86_data, demultiplexer_86_out3, Volume
  // Buzzer #(.waveform("Sawtooth")) buzzer_357: pin names not known; wires that end beside it: rom_87_data, demultiplexer_87_out3, Volume
  // Buzzer #(.waveform("Sawtooth")) buzzer_358: pin names not known; wires that end beside it: rom_88_data, demultiplexer_88_out3, Volume
  // Buzzer #(.waveform("Sawtooth")) buzzer_359: pin names not known; wires that end beside it: rom_89_data, demultiplexer_89_out3, Volume
  // Buzzer #(.waveform("Sawtooth")) buzzer_360: pin names not known; wires that end beside it: rom_90_data, demultiplexer_90_out3, Volume
  Button button_91 (.out(button_91_out));
  xor xor_91 (xor_91_out, in_13, button_91_out);
  Demultiplexer #(.select(2)) demultiplexer_91 (
    .out0(demultiplexer_91_out0), .out1(demultiplexer_91_out1), .out2(demultiplexer_91_out2),
    .out3(demultiplexer_91_out3), .in(xor_91_out), .sel(Waveform));
  ROM #(.addrWidth(2), .dataWidth(14)) rom_91 (.addr(2'b00), .data(rom_91_data));
  Button button_92 (.out(button_92_out));
  xor xor_92 (xor_92_out, in_25, button_92_out);
  Demultiplexer #(.select(2)) demultiplexer_92 (
    .out0(demultiplexer_92_out0), .out1(demultiplexer_92_out1), .out2(demultiplexer_92_out2),
    .out3(demultiplexer_92_out3), .in(xor_92_out), .sel(Waveform));
  ROM #(.addrWidth(2), .dataWidth(14)) rom_92 (.addr(2'b00), .data(rom_92_data));
  Button button_93 (.out(button_93_out));
  xor xor_93 (xor_93_out, in_37, button_93_out);
  Demultiplexer #(.select(2)) demultiplexer_93 (
    .out0(demultiplexer_93_out0), .out1(demultiplexer_93_out1), .out2(demultiplexer_93_out2),
    .out3(demultiplexer_93_out3), .in(xor_93_out), .sel(Waveform));
  ROM #(.addrWidth(2), .dataWidth(14)) rom_93 (.addr(2'b00), .data(rom_93_data));
  Button button_94 (.out(button_94_out));
  xor xor_94 (xor_94_out, in_49, button_94_out);
  Demultiplexer #(.select(2)) demultiplexer_94 (
    .out0(demultiplexer_94_out0), .out1(demultiplexer_94_out1), .out2(demultiplexer_94_out2),
    .out3(demultiplexer_94_out3), .in(xor_94_out), .sel(Waveform));
  ROM #(.addrWidth(2), .dataWidth(14)) rom_94 (.addr(2'b00), .data(rom_94_data));
  Button button_95 (.out(button_95_out));
  xor xor_95 (xor_95_out, in_61, button_95_out);
  Demultiplexer #(.select(2)) demultiplexer_95 (
    .out0(demultiplexer_95_out0), .out1(demultiplexer_95_out1), .out2(demultiplexer_95_out2),
    .out3(demultiplexer_95_out3), .in(xor_95_out), .sel(Waveform));
  ROM #(.addrWidth(2), .dataWidth(14)) rom_95 (.addr(2'b00), .data(rom_95_data));
  Button button_96 (.out(button_96_out));
  xor xor_96 (xor_96_out, in_73, button_96_out);
  Demultiplexer #(.select(2)) demultiplexer_96 (
    .out0(demultiplexer_96_out0), .out1(demultiplexer_96_out1), .out2(demultiplexer_96_out2),
    .out3(demultiplexer_96_out3), .in(xor_96_out), .sel(Waveform));
  ROM #(.addrWidth(2), .dataWidth(14)) rom_96 (.addr(2'b00), .data(rom_96_data));
  Button button_97 (.out(button_97_out));
  xor xor_97 (xor_97_out, in_85, button_97_out);
  Demultiplexer #(.select(2)) demultiplexer_97 (
    .out0(demultiplexer_97_out0), .out1(demultiplexer_97_out1), .out2(demultiplexer_97_out2),
    .out3(demultiplexer_97_out3), .in(xor_97_out), .sel(Waveform));
  ROM #(.addrWidth(2), .dataWidth(14)) rom_97 (.addr(2'b00), .data(rom_97_data));
  Button button_98 (.out(button_98_out));
  xor xor_98 (xor_98_out, in_97, button_98_out);
  Demultiplexer #(.select(2)) demultiplexer_98 (
    .out0(demultiplexer_98_out0), .out1(demultiplexer_98_out1), .out2(demultiplexer_98_out2),
    .out3(demultiplexer_98_out3), .in(xor_98_out), .sel(Waveform));
  ROM #(.addrWidth(2), .dataWidth(14)) rom_98 (.addr(2'b00), .data(rom_98_data));
  Button button_99 (.out(button_99_out));
  xor xor_99 (xor_99_out, in_109, button_99_out);
  Demultiplexer #(.select(2)) demultiplexer_99 (
    .out0(demultiplexer_99_out0), .out1(demultiplexer_99_out1), .out2(demultiplexer_99_out2),
    .out3(demultiplexer_99_out3), .in(xor_99_out), .sel(Waveform));
  ROM #(.addrWidth(2), .dataWidth(14)) rom_99 (.addr(2'b00), .data(rom_99_data));
  // Buzzer #(.waveform("Square")) buzzer_361: pin names not known; wires that end beside it: rom_91_data, demultiplexer_91_out1, Volume
  // Buzzer buzzer_362: pin names not known; wires that end beside it: rom_91_data, demultiplexer_91_out0, Volume
  // Buzzer #(.waveform("Square")) buzzer_363: pin names not known; wires that end beside it: rom_92_data, demultiplexer_92_out1, Volume
  // Buzzer buzzer_364: pin names not known; wires that end beside it: rom_92_data, demultiplexer_92_out0, Volume
  // Buzzer #(.waveform("Square")) buzzer_365: pin names not known; wires that end beside it: rom_93_data, demultiplexer_93_out1, Volume
  // Buzzer buzzer_366: pin names not known; wires that end beside it: rom_93_data, demultiplexer_93_out0, Volume
  // Buzzer #(.waveform("Square")) buzzer_367: pin names not known; wires that end beside it: rom_94_data, demultiplexer_94_out1, Volume
  // Buzzer buzzer_368: pin names not known; wires that end beside it: rom_94_data, demultiplexer_94_out0, Volume
  // Buzzer #(.waveform("Square")) buzzer_369: pin names not known; wires that end beside it: rom_95_data, demultiplexer_95_out1, Volume
  // Buzzer buzzer_370: pin names not known; wires that end beside it: rom_95_data, demultiplexer_95_out0, Volume
  // Buzzer #(.waveform("Square")) buzzer_371: pin names not known; wires that end beside it: rom_96_data, demultiplexer_96_out1, Volume
  // Buzzer buzzer_372: pin names not known; wires that end beside it: rom_96_data, demultiplexer_96_out0, Volume
  // Buzzer #(.waveform("Square")) buzzer_373: pin names not known; wires that end beside it: rom_97_data, demultiplexer_97_out1, Volume
  // Buzzer buzzer_374: pin names not known; wires that end beside it: rom_97_data, demultiplexer_97_out0, Volume
  // Buzzer #(.waveform("Square")) buzzer_375: pin names not known; wires that end beside it: rom_98_data, demultiplexer_98_out1, Volume
  // Buzzer buzzer_376: pin names not known; wires that end beside it: rom_98_data, demultiplexer_98_out0, Volume
  // Buzzer #(.waveform("Square")) buzzer_377: pin names not known; wires that end beside it: rom_99_data, demultiplexer_99_out1, Volume
  // Buzzer buzzer_378: pin names not known; wires that end beside it: rom_99_data, demultiplexer_99_out0, Volume
  // Buzzer #(.waveform("Sawtooth")) buzzer_379: pin names not known; wires that end beside it: rom_91_data, demultiplexer_91_out3, Volume
  // Buzzer #(.waveform("Triangle")) buzzer_380: pin names not known; wires that end beside it: rom_91_data, demultiplexer_91_out2, Volume
  // Buzzer #(.waveform("Sawtooth")) buzzer_381: pin names not known; wires that end beside it: rom_92_data, demultiplexer_92_out3, Volume
  // Buzzer #(.waveform("Triangle")) buzzer_382: pin names not known; wires that end beside it: rom_92_data, demultiplexer_92_out2, Volume
  // Buzzer #(.waveform("Sawtooth")) buzzer_383: pin names not known; wires that end beside it: rom_93_data, demultiplexer_93_out3, Volume
  // Buzzer #(.waveform("Triangle")) buzzer_384: pin names not known; wires that end beside it: rom_93_data, demultiplexer_93_out2, Volume
  // Buzzer #(.waveform("Sawtooth")) buzzer_385: pin names not known; wires that end beside it: rom_94_data, demultiplexer_94_out3, Volume
  // Buzzer #(.waveform("Triangle")) buzzer_386: pin names not known; wires that end beside it: rom_94_data, demultiplexer_94_out2, Volume
  // Buzzer #(.waveform("Sawtooth")) buzzer_387: pin names not known; wires that end beside it: rom_95_data, demultiplexer_95_out3, Volume
  // Buzzer #(.waveform("Triangle")) buzzer_388: pin names not known; wires that end beside it: rom_95_data, demultiplexer_95_out2, Volume
  // Buzzer #(.waveform("Sawtooth")) buzzer_389: pin names not known; wires that end beside it: rom_96_data, demultiplexer_96_out3, Volume
  // Buzzer #(.waveform("Triangle")) buzzer_390: pin names not known; wires that end beside it: rom_96_data, demultiplexer_96_out2, Volume
  // Buzzer #(.waveform("Sawtooth")) buzzer_391: pin names not known; wires that end beside it: rom_97_data, demultiplexer_97_out3, Volume
  // Buzzer #(.waveform("Triangle")) buzzer_392: pin names not known; wires that end beside it: rom_97_data, demultiplexer_97_out2, Volume
  // Buzzer #(.waveform("Sawtooth")) buzzer_393: pin names not known; wires that end beside it: rom_98_data, demultiplexer_98_out3, Volume
  // Buzzer #(.waveform("Triangle")) buzzer_394: pin names not known; wires that end beside it: rom_98_data, demultiplexer_98_out2, Volume
  // Buzzer #(.waveform("Sawtooth")) buzzer_395: pin names not known; wires that end beside it: rom_99_data, demultiplexer_99_out3, Volume
  // Buzzer #(.waveform("Triangle")) buzzer_396: pin names not known; wires that end beside it: rom_99_data, demultiplexer_99_out2, Volume
  Button button_100 (.out(button_100_out));
  xor xor_100 (xor_100_out, in_14, button_100_out);
  Demultiplexer #(.select(2)) demultiplexer_100 (
    .out0(demultiplexer_100_out0), .out1(demultiplexer_100_out1), .out2(demultiplexer_100_out2),
    .out3(demultiplexer_100_out3), .in(xor_100_out), .sel(Waveform));
  ROM #(.addrWidth(2), .dataWidth(14)) rom_100 (.addr(2'b00), .data(rom_100_data));
  Button button_101 (.out(button_101_out));
  xor xor_101 (xor_101_out, in_26, button_101_out);
  Demultiplexer #(.select(2)) demultiplexer_101 (
    .out0(demultiplexer_101_out0), .out1(demultiplexer_101_out1), .out2(demultiplexer_101_out2),
    .out3(demultiplexer_101_out3), .in(xor_101_out), .sel(Waveform));
  ROM #(.addrWidth(2), .dataWidth(14)) rom_101 (.addr(2'b00), .data(rom_101_data));
  Button button_102 (.out(button_102_out));
  xor xor_102 (xor_102_out, in_38, button_102_out);
  Demultiplexer #(.select(2)) demultiplexer_102 (
    .out0(demultiplexer_102_out0), .out1(demultiplexer_102_out1), .out2(demultiplexer_102_out2),
    .out3(demultiplexer_102_out3), .in(xor_102_out), .sel(Waveform));
  ROM #(.addrWidth(2), .dataWidth(14)) rom_102 (.addr(2'b00), .data(rom_102_data));
  Button button_103 (.out(button_103_out));
  xor xor_103 (xor_103_out, in_50, button_103_out);
  Demultiplexer #(.select(2)) demultiplexer_103 (
    .out0(demultiplexer_103_out0), .out1(demultiplexer_103_out1), .out2(demultiplexer_103_out2),
    .out3(demultiplexer_103_out3), .in(xor_103_out), .sel(Waveform));
  ROM #(.addrWidth(2), .dataWidth(14)) rom_103 (.addr(2'b00), .data(rom_103_data));
  Button button_104 (.out(button_104_out));
  xor xor_104 (xor_104_out, in_62, button_104_out);
  Demultiplexer #(.select(2)) demultiplexer_104 (
    .out0(demultiplexer_104_out0), .out1(demultiplexer_104_out1), .out2(demultiplexer_104_out2),
    .out3(demultiplexer_104_out3), .in(xor_104_out), .sel(Waveform));
  ROM #(.addrWidth(2), .dataWidth(14)) rom_104 (.addr(2'b00), .data(rom_104_data));
  Button button_105 (.out(button_105_out));
  xor xor_105 (xor_105_out, in_74, button_105_out);
  Demultiplexer #(.select(2)) demultiplexer_105 (
    .out0(demultiplexer_105_out0), .out1(demultiplexer_105_out1), .out2(demultiplexer_105_out2),
    .out3(demultiplexer_105_out3), .in(xor_105_out), .sel(Waveform));
  ROM #(.addrWidth(2), .dataWidth(14)) rom_105 (.addr(2'b00), .data(rom_105_data));
  Button button_106 (.out(button_106_out));
  xor xor_106 (xor_106_out, in_86, button_106_out);
  Demultiplexer #(.select(2)) demultiplexer_106 (
    .out0(demultiplexer_106_out0), .out1(demultiplexer_106_out1), .out2(demultiplexer_106_out2),
    .out3(demultiplexer_106_out3), .in(xor_106_out), .sel(Waveform));
  ROM #(.addrWidth(2), .dataWidth(14)) rom_106 (.addr(2'b00), .data(rom_106_data));
  Button button_107 (.out(button_107_out));
  xor xor_107 (xor_107_out, in_98, button_107_out);
  Demultiplexer #(.select(2)) demultiplexer_107 (
    .out0(demultiplexer_107_out0), .out1(demultiplexer_107_out1), .out2(demultiplexer_107_out2),
    .out3(demultiplexer_107_out3), .in(xor_107_out), .sel(Waveform));
  ROM #(.addrWidth(2), .dataWidth(14)) rom_107 (.addr(2'b00), .data(rom_107_data));
  Button button_108 (.out(button_108_out));
  xor xor_108 (xor_108_out, in_110, button_108_out);
  Demultiplexer #(.select(2)) demultiplexer_108 (
    .out0(demultiplexer_108_out0), .out1(demultiplexer_108_out1), .out2(demultiplexer_108_out2),
    .out3(demultiplexer_108_out3), .in(xor_108_out), .sel(Waveform));
  ROM #(.addrWidth(2), .dataWidth(14)) rom_108 (.addr(2'b00), .data(rom_108_data));
  // Buzzer buzzer_397: pin names not known; wires that end beside it: rom_100_data, demultiplexer_100_out0, Volume
  // Buzzer buzzer_398: pin names not known; wires that end beside it: rom_101_data, demultiplexer_101_out0, Volume
  // Buzzer buzzer_399: pin names not known; wires that end beside it: rom_102_data, demultiplexer_102_out0, Volume
  // Buzzer buzzer_400: pin names not known; wires that end beside it: rom_103_data, demultiplexer_103_out0, Volume
  // Buzzer buzzer_401: pin names not known; wires that end beside it: rom_104_data, demultiplexer_104_out0, Volume
  // Buzzer buzzer_402: pin names not known; wires that end beside it: rom_105_data, demultiplexer_105_out0, Volume
  // Buzzer buzzer_403: pin names not known; wires that end beside it: rom_106_data, demultiplexer_106_out0, Volume
  // Buzzer buzzer_404: pin names not known; wires that end beside it: rom_107_data, demultiplexer_107_out0, Volume
  // Buzzer buzzer_405: pin names not known; wires that end beside it: rom_108_data, demultiplexer_108_out0, Volume
  // Buzzer #(.waveform("Triangle")) buzzer_406: pin names not known; wires that end beside it: rom_100_data, demultiplexer_100_out2, Volume
  // Buzzer #(.waveform("Square")) buzzer_407: pin names not known; wires that end beside it: rom_100_data, demultiplexer_100_out1, Volume
  // Buzzer #(.waveform("Triangle")) buzzer_408: pin names not known; wires that end beside it: rom_101_data, demultiplexer_101_out2, Volume
  // Buzzer #(.waveform("Square")) buzzer_409: pin names not known; wires that end beside it: rom_101_data, demultiplexer_101_out1, Volume
  // Buzzer #(.waveform("Triangle")) buzzer_410: pin names not known; wires that end beside it: rom_102_data, demultiplexer_102_out2, Volume
  // Buzzer #(.waveform("Square")) buzzer_411: pin names not known; wires that end beside it: rom_102_data, demultiplexer_102_out1, Volume
  // Buzzer #(.waveform("Triangle")) buzzer_412: pin names not known; wires that end beside it: rom_103_data, demultiplexer_103_out2, Volume
  // Buzzer #(.waveform("Square")) buzzer_413: pin names not known; wires that end beside it: rom_103_data, demultiplexer_103_out1, Volume
  // Buzzer #(.waveform("Triangle")) buzzer_414: pin names not known; wires that end beside it: rom_104_data, demultiplexer_104_out2, Volume
  // Buzzer #(.waveform("Square")) buzzer_415: pin names not known; wires that end beside it: rom_104_data, demultiplexer_104_out1, Volume
  // Buzzer #(.waveform("Triangle")) buzzer_416: pin names not known; wires that end beside it: rom_105_data, demultiplexer_105_out2, Volume
  // Buzzer #(.waveform("Square")) buzzer_417: pin names not known; wires that end beside it: rom_105_data, demultiplexer_105_out1, Volume
  // Buzzer #(.waveform("Triangle")) buzzer_418: pin names not known; wires that end beside it: rom_106_data, demultiplexer_106_out2, Volume
  // Buzzer #(.waveform("Square")) buzzer_419: pin names not known; wires that end beside it: rom_106_data, demultiplexer_106_out1, Volume
  // Buzzer #(.waveform("Triangle")) buzzer_420: pin names not known; wires that end beside it: rom_107_data, demultiplexer_107_out2, Volume
  // Buzzer #(.waveform("Square")) buzzer_421: pin names not known; wires that end beside it: rom_107_data, demultiplexer_107_out1, Volume
  // Buzzer #(.waveform("Triangle")) buzzer_422: pin names not known; wires that end beside it: rom_108_data, demultiplexer_108_out2, Volume
  // Buzzer #(.waveform("Square")) buzzer_423: pin names not known; wires that end beside it: rom_108_data, demultiplexer_108_out1, Volume
  // Buzzer #(.waveform("Sawtooth")) buzzer_424: pin names not known; wires that end beside it: rom_100_data, demultiplexer_100_out3, Volume
  // Buzzer #(.waveform("Sawtooth")) buzzer_425: pin names not known; wires that end beside it: rom_101_data, demultiplexer_101_out3, Volume
  // Buzzer #(.waveform("Sawtooth")) buzzer_426: pin names not known; wires that end beside it: rom_102_data, demultiplexer_102_out3, Volume
  // Buzzer #(.waveform("Sawtooth")) buzzer_427: pin names not known; wires that end beside it: rom_103_data, demultiplexer_103_out3, Volume
  // Buzzer #(.waveform("Sawtooth")) buzzer_428: pin names not known; wires that end beside it: rom_104_data, demultiplexer_104_out3, Volume
  // Buzzer #(.waveform("Sawtooth")) buzzer_429: pin names not known; wires that end beside it: rom_105_data, demultiplexer_105_out3, Volume
  // Buzzer #(.waveform("Sawtooth")) buzzer_430: pin names not known; wires that end beside it: rom_106_data, demultiplexer_106_out3, Volume
  // Buzzer #(.waveform("Sawtooth")) buzzer_431: pin names not known; wires that end beside it: rom_107_data, demultiplexer_107_out3, Volume
  // Buzzer #(.waveform("Sawtooth")) buzzer_432: pin names not known; wires that end beside it: rom_108_data, demultiplexer_108_out3, Volume

  // Notes on the sheet:
  //   contents of rom_1 (hex, n*v repeats v):
  //   37
  //   contents of rom_2 (hex, n*v repeats v):
  //   6e
  //   contents of rom_3 (hex, n*v repeats v):
  //   dc
  //   contents of rom_4 (hex, n*v repeats v):
  //   1b8
  //   contents of rom_5 (hex, n*v repeats v):
  //   370
  //   contents of rom_6 (hex, n*v repeats v):
  //   6e0
  //   contents of rom_7 (hex, n*v repeats v):
  //   dc0
  //   contents of rom_8 (hex, n*v repeats v):
  //   1b80
  //   contents of rom_9 (hex, n*v repeats v):
  //   3700
  //   contents of rom_10 (hex, n*v repeats v):
  //   3a
  //   contents of rom_11 (hex, n*v repeats v):
  //   75
  //   contents of rom_12 (hex, n*v repeats v):
  //   e9
  //   contents of rom_13 (hex, n*v repeats v):
  //   1d2
  //   contents of rom_14 (hex, n*v repeats v):
  //   3a4
  //   contents of rom_15 (hex, n*v repeats v):
  //   749
  //   contents of rom_16 (hex, n*v repeats v):
  //   e91
  //   contents of rom_17 (hex, n*v repeats v):
  //   1d23
  //   contents of rom_18 (hex, n*v repeats v):
  //   3a45
  //   contents of rom_19 (hex, n*v repeats v):
  //   3e
  //   contents of rom_20 (hex, n*v repeats v):
  //   7b
  //   contents of rom_21 (hex, n*v repeats v):
  //   f7
  //   contents of rom_22 (hex, n*v repeats v):
  //   1ee
  //   contents of rom_23 (hex, n*v repeats v):
  //   3dc
  //   contents of rom_24 (hex, n*v repeats v):
  //   7b8
  //   contents of rom_25 (hex, n*v repeats v):
  //   f6f
  //   contents of rom_26 (hex, n*v repeats v):
  //   1ede
  //   contents of rom_27 (hex, n*v repeats v):
  //   3dbc
  //   contents of rom_28 (hex, n*v repeats v):
  //   41
  //   contents of rom_29 (hex, n*v repeats v):
  //   83
  //   contents of rom_30 (hex, n*v repeats v):
  //   106
  //   contents of rom_31 (hex, n*v repeats v):
  //   20b
  //   contents of rom_32 (hex, n*v repeats v):
  //   417
  //   contents of rom_33 (hex, n*v repeats v):
  //   82d
  //   contents of rom_34 (hex, n*v repeats v):
  //   105a
  //   contents of rom_35 (hex, n*v repeats v):
  //   20b4
  //   contents of rom_36 (hex, n*v repeats v):
  //   168
  //   contents of rom_37 (hex, n*v repeats v):
  //   45
  //   contents of rom_38 (hex, n*v repeats v):
  //   8b
  //   contents of rom_39 (hex, n*v repeats v):
  //   115
  //   contents of rom_40 (hex, n*v repeats v):
  //   22a
  //   contents of rom_41 (hex, n*v repeats v):
  //   455
  //   contents of rom_42 (hex, n*v repeats v):
  //   8a9
  //   contents of rom_43 (hex, n*v repeats v):
  //   1153
  //   contents of rom_44 (hex, n*v repeats v):
  //   22a6
  //   contents of rom_45 (hex, n*v repeats v):
  //   54c
  //   contents of rom_46 (hex, n*v repeats v):
  //   49
  //   contents of rom_47 (hex, n*v repeats v):
  //   93
  //   contents of rom_48 (hex, n*v repeats v):
  //   126
  //   contents of rom_49 (hex, n*v repeats v):
  //   24b
  //   contents of rom_50 (hex, n*v repeats v):
  //   497
  //   contents of rom_51 (hex, n*v repeats v):
  //   92d
  //   contents of rom_52 (hex, n*v repeats v):
  //   125b
  //   contents of rom_53 (hex, n*v repeats v):
  //   24b5
  //   contents of rom_54 (hex, n*v repeats v):
  //   96b
  //   contents of rom_55 (hex, n*v repeats v):
  //   4e
  //   contents of rom_56 (hex, n*v repeats v):
  //   9c
  //   contents of rom_57 (hex, n*v repeats v):
  //   137
  //   contents of rom_58 (hex, n*v repeats v):
  //   26e
  //   contents of rom_59 (hex, n*v repeats v):
  //   4dd
  //   contents of rom_60 (hex, n*v repeats v):
  //   9b9
  //   contents of rom_61 (hex, n*v repeats v):
  //   1372
  //   contents of rom_62 (hex, n*v repeats v):
  //   26e4
  //   contents of rom_63 (hex, n*v repeats v):
  //   dc8
  //   contents of rom_64 (hex, n*v repeats v):
  //   52
  //   contents of rom_65 (hex, n*v repeats v):
  //   a5
  //   contents of rom_66 (hex, n*v repeats v):
  //   14a
  //   contents of rom_67 (hex, n*v repeats v):
  //   293
  //   contents of rom_68 (hex, n*v repeats v):
  //   527
  //   contents of rom_69 (hex, n*v repeats v):
  //   a4d
  //   contents of rom_70 (hex, n*v repeats v):
  //   149a
  //   contents of rom_71 (hex, n*v repeats v):
  //   2934
  //   contents of rom_72 (hex, n*v repeats v):
  //   1268
  //   contents of rom_73 (hex, n*v repeats v):
  //   57
  //   contents of rom_74 (hex, n*v repeats v):
  //   af
  //   contents of rom_75 (hex, n*v repeats v):
  //   15d
  //   contents of rom_76 (hex, n*v repeats v):
  //   2ba
  //   contents of rom_77 (hex, n*v repeats v):
  //   575
  //   contents of rom_78 (hex, n*v repeats v):
  //   aea
  //   contents of rom_79 (hex, n*v repeats v):
  //   15d4
  //   contents of rom_80 (hex, n*v repeats v):
  //   2ba7
  //   contents of rom_81 (hex, n*v repeats v):
  //   174f
  //   contents of rom_82 (hex, n*v repeats v):
  //   5c
  //   contents of rom_83 (hex, n*v repeats v):
  //   b9
  //   contents of rom_84 (hex, n*v repeats v):
  //   172
  //   contents of rom_85 (hex, n*v repeats v):
  //   2e4
  //   contents of rom_86 (hex, n*v repeats v):
  //   5c8
  //   contents of rom_87 (hex, n*v repeats v):
  //   b90
  //   contents of rom_88 (hex, n*v repeats v):
  //   1720
  //   contents of rom_89 (hex, n*v repeats v):
  //   2e40
  //   contents of rom_90 (hex, n*v repeats v):
  //   1c80
  //   contents of rom_91 (hex, n*v repeats v):
  //   62
  //   contents of rom_92 (hex, n*v repeats v):
  //   c4
  //   contents of rom_93 (hex, n*v repeats v):
  //   188
  //   contents of rom_94 (hex, n*v repeats v):
  //   310
  //   contents of rom_95 (hex, n*v repeats v):
  //   620
  //   contents of rom_96 (hex, n*v repeats v):
  //   c40
  //   contents of rom_97 (hex, n*v repeats v):
  //   1880
  //   contents of rom_98 (hex, n*v repeats v):
  //   3100
  //   contents of rom_99 (hex, n*v repeats v):
  //   2200
  //   contents of rom_100 (hex, n*v repeats v):
  //   68
  //   contents of rom_101 (hex, n*v repeats v):
  //   d0
  //   contents of rom_102 (hex, n*v repeats v):
  //   19f
  //   contents of rom_103 (hex, n*v repeats v):
  //   33f
  //   contents of rom_104 (hex, n*v repeats v):
  //   67d
  //   contents of rom_105 (hex, n*v repeats v):
  //   cfa
  //   contents of rom_106 (hex, n*v repeats v):
  //   19f5
  //   contents of rom_107 (hex, n*v repeats v):
  //   33ea
  //   contents of rom_108 (hex, n*v repeats v):
  //   27d4
endmodule

module Full_Synth_Buttons (
  input  [1:0] WaveForm,
  input  [6:0] Volume
);

  wire button_1_out, button_2_out, button_3_out, button_4_out, button_5_out, button_6_out, button_7_out,
       button_8_out, button_9_out, button_10_out, button_11_out, button_12_out, button_13_out, button_14_out,
       button_15_out, button_16_out, button_17_out, button_18_out, button_19_out, button_20_out,
       button_21_out, button_22_out, button_23_out, button_24_out, button_25_out, button_26_out,
       button_27_out, button_28_out, button_29_out, button_30_out, button_31_out, button_32_out,
       button_33_out, button_34_out, button_35_out, button_36_out, button_37_out, button_38_out,
       button_39_out, button_40_out, button_41_out, button_42_out, button_43_out, button_44_out,
       button_45_out, button_46_out, button_47_out, button_48_out, button_49_out, button_50_out,
       button_51_out, button_52_out, button_53_out, button_54_out, button_55_out, button_56_out,
       button_57_out, button_58_out, button_59_out, button_60_out, button_61_out, button_62_out,
       button_63_out, button_64_out, button_65_out, button_66_out, button_67_out, button_68_out,
       button_69_out, button_70_out, button_71_out, button_72_out, button_73_out, button_74_out,
       button_75_out, button_76_out, button_77_out, button_78_out, button_79_out, button_80_out,
       button_81_out, button_82_out, button_83_out, button_84_out, button_85_out, button_86_out,
       button_87_out, button_88_out, button_89_out, button_90_out, button_91_out, button_92_out,
       button_93_out, button_94_out, button_95_out, button_96_out, button_97_out, button_98_out,
       button_99_out, button_100_out, button_101_out, button_102_out, button_103_out, button_104_out,
       button_105_out, button_106_out, button_107_out, button_108_out;

  Button button_1 (.out(button_1_out));
  Button button_2 (.out(button_2_out));
  Button button_3 (.out(button_3_out));
  Button button_4 (.out(button_4_out));
  Button button_5 (.out(button_5_out));
  Button button_6 (.out(button_6_out));
  Button button_7 (.out(button_7_out));
  Button button_8 (.out(button_8_out));
  Button button_9 (.out(button_9_out));
  Button button_10 (.out(button_10_out));
  Button button_11 (.out(button_11_out));
  Button button_12 (.out(button_12_out));
  Synth_12TET_8_Octaves synth_12tet_8_octaves_1 (
    .in_17(button_15_out), .in_5(button_2_out), .in_29(button_27_out), .in_41(button_39_out),
    .in_53(button_51_out), .in_65(button_63_out), .in_77(button_75_out), .in_89(button_87_out),
    .in_101(button_99_out), .A1(button_14_out), .A0(button_4_out), .A2(button_26_out), .A3(button_38_out),
    .A4(button_50_out), .A5(button_62_out), .A6(button_74_out), .A7(button_86_out), .A8(button_98_out),
    .in_18(button_16_out), .in_6(button_3_out), .in_30(button_28_out), .in_42(button_40_out),
    .in_54(button_52_out), .in_66(button_64_out), .in_78(button_76_out), .in_90(button_88_out),
    .in_102(button_100_out), .Waveform(WaveForm), .in_19(button_17_out), .in_7(button_5_out),
    .in_31(button_29_out), .in_43(button_41_out), .in_55(button_53_out), .in_67(button_65_out),
    .in_79(button_77_out), .in_91(button_89_out), .in_103(button_101_out), .in_20(button_19_out),
    .in_8(button_7_out), .in_32(button_31_out), .in_44(button_43_out), .in_56(button_55_out),
    .in_68(button_67_out), .in_80(button_79_out), .in_92(button_91_out), .in_104(button_103_out),
    .in_21(button_18_out), .in_9(button_6_out), .in_33(button_30_out), .in_45(button_42_out),
    .in_57(button_54_out), .in_69(button_66_out), .in_81(button_78_out), .in_93(button_90_out),
    .in_105(button_102_out), .in_22(button_20_out), .in_10(button_8_out), .in_34(button_32_out),
    .in_46(button_44_out), .in_58(button_56_out), .in_70(button_68_out), .in_82(button_80_out),
    .in_94(button_92_out), .in_106(button_104_out), .in_23(button_23_out), .in_11(button_11_out),
    .in_35(button_35_out), .in_47(button_48_out), .in_59(button_59_out), .in_71(button_71_out),
    .in_83(button_83_out), .in_95(button_95_out), .in_107(button_107_out), .Volume(Volume),
    .in_24(button_21_out), .in_12(button_9_out), .in_36(button_33_out), .in_48(button_46_out),
    .in_60(button_57_out), .in_72(button_69_out), .in_84(button_81_out), .in_96(button_93_out),
    .in_108(button_105_out), .in_25(button_24_out), .in_13(button_12_out), .in_37(button_36_out),
    .in_49(button_47_out), .in_61(button_60_out), .in_73(button_72_out), .in_85(button_84_out),
    .in_97(button_96_out), .in_109(button_108_out), .in_26(button_22_out), .in_14(button_10_out),
    .in_38(button_34_out), .in_50(button_45_out), .in_62(button_58_out), .in_74(button_70_out),
    .in_86(button_82_out), .in_98(button_94_out), .in_110(button_106_out), .in_16(button_13_out),
    .in_4(button_1_out), .in_28(button_25_out), .in_40(button_37_out), .in_52(button_49_out),
    .in_64(button_61_out), .in_76(button_73_out), .in_88(button_85_out), .in_100(button_97_out));
  Button button_13 (.out(button_13_out));
  Button button_14 (.out(button_14_out));
  Button button_15 (.out(button_15_out));
  Button button_16 (.out(button_16_out));
  Button button_17 (.out(button_17_out));
  Button button_18 (.out(button_18_out));
  Button button_19 (.out(button_19_out));
  Button button_20 (.out(button_20_out));
  Button button_21 (.out(button_21_out));
  Button button_22 (.out(button_22_out));
  Button button_23 (.out(button_23_out));
  Button button_24 (.out(button_24_out));
  Button button_25 (.out(button_25_out));
  Button button_26 (.out(button_26_out));
  Button button_27 (.out(button_27_out));
  Button button_28 (.out(button_28_out));
  Button button_29 (.out(button_29_out));
  Button button_30 (.out(button_30_out));
  Button button_31 (.out(button_31_out));
  Button button_32 (.out(button_32_out));
  Button button_33 (.out(button_33_out));
  Button button_34 (.out(button_34_out));
  Button button_35 (.out(button_35_out));
  Button button_36 (.out(button_36_out));
  Button button_37 (.out(button_37_out));
  Button button_38 (.out(button_38_out));
  Button button_39 (.out(button_39_out));
  Button button_40 (.out(button_40_out));
  Button button_41 (.out(button_41_out));
  Button button_42 (.out(button_42_out));
  Button button_43 (.out(button_43_out));
  Button button_44 (.out(button_44_out));
  Button button_45 (.out(button_45_out));
  Button button_46 (.out(button_46_out));
  Button button_47 (.out(button_47_out));
  Button button_48 (.out(button_48_out));
  Button button_49 (.out(button_49_out));
  Button button_50 (.out(button_50_out));
  Button button_51 (.out(button_51_out));
  Button button_52 (.out(button_52_out));
  Button button_53 (.out(button_53_out));
  Button button_54 (.out(button_54_out));
  Button button_55 (.out(button_55_out));
  Button button_56 (.out(button_56_out));
  Button button_57 (.out(button_57_out));
  Button button_58 (.out(button_58_out));
  Button button_59 (.out(button_59_out));
  Button button_60 (.out(button_60_out));
  Button button_61 (.out(button_61_out));
  Button button_62 (.out(button_62_out));
  Button button_63 (.out(button_63_out));
  Button button_64 (.out(button_64_out));
  Button button_65 (.out(button_65_out));
  Button button_66 (.out(button_66_out));
  Button button_67 (.out(button_67_out));
  Button button_68 (.out(button_68_out));
  Button button_69 (.out(button_69_out));
  Button button_70 (.out(button_70_out));
  Button button_71 (.out(button_71_out));
  Button button_72 (.out(button_72_out));
  Button button_73 (.out(button_73_out));
  Button button_74 (.out(button_74_out));
  Button button_75 (.out(button_75_out));
  Button button_76 (.out(button_76_out));
  Button button_77 (.out(button_77_out));
  Button button_78 (.out(button_78_out));
  Button button_79 (.out(button_79_out));
  Button button_80 (.out(button_80_out));
  Button button_81 (.out(button_81_out));
  Button button_82 (.out(button_82_out));
  Button button_83 (.out(button_83_out));
  Button button_84 (.out(button_84_out));
  Button button_85 (.out(button_85_out));
  Button button_86 (.out(button_86_out));
  Button button_87 (.out(button_87_out));
  Button button_88 (.out(button_88_out));
  Button button_89 (.out(button_89_out));
  Button button_90 (.out(button_90_out));
  Button button_91 (.out(button_91_out));
  Button button_92 (.out(button_92_out));
  Button button_93 (.out(button_93_out));
  Button button_94 (.out(button_94_out));
  Button button_95 (.out(button_95_out));
  Button button_96 (.out(button_96_out));
  Button button_97 (.out(button_97_out));
  Button button_98 (.out(button_98_out));
  Button button_99 (.out(button_99_out));
  Button button_100 (.out(button_100_out));
  Button button_101 (.out(button_101_out));
  Button button_102 (.out(button_102_out));
  Button button_103 (.out(button_103_out));
  Button button_104 (.out(button_104_out));
  Button button_105 (.out(button_105_out));
  Button button_106 (.out(button_106_out));
  Button button_107 (.out(button_107_out));
  Button button_108 (.out(button_108_out));

  // Notes on the sheet:
  //   0,0 Sine
  //   0,1 Square
  //   1,0 Triangle
  //   1,1 Saw
  //   0,0
  //   Waveform
  //   0,1
  //   1,0
  //   1,1
  //   Volume
endmodule

module Full_Synth_Pins (
  input  [1:0] in_1,
  input  [6:0] in_2,
  input  in_3,
  input  in_4,
  input  in_5,
  input  in_6,
  input  in_7,
  input  in_8,
  input  in_9,
  input  in_10,
  input  in_11,
  input  in_12,
  input  in_13,
  input  in_14,
  input  in_15,
  input  in_16,
  input  in_17,
  input  in_18,
  input  in_19,
  input  in_20,
  input  in_21,
  input  in_22,
  input  in_23,
  input  in_24,
  input  in_25,
  input  in_26,
  input  in_27,
  input  in_28,
  input  in_29,
  input  in_30,
  input  in_31,
  input  in_32,
  input  in_33,
  input  in_34,
  input  in_35,
  input  in_36,
  input  in_37,
  input  in_38,
  input  in_39,
  input  in_40,
  input  in_41,
  input  in_42,
  input  in_43,
  input  in_44,
  input  in_45,
  input  in_46,
  input  in_47,
  input  in_48,
  input  in_49,
  input  in_50,
  input  in_51,
  input  in_52,
  input  in_53,
  input  in_54,
  input  in_55,
  input  in_56,
  input  in_57,
  input  in_58,
  input  in_59,
  input  in_60,
  input  in_61,
  input  in_62,
  input  in_63,
  input  in_64,
  input  in_65,
  input  in_66,
  input  in_67,
  input  in_68,
  input  in_69,
  input  in_70,
  input  in_71,
  input  in_72,
  input  in_73,
  input  in_74,
  input  in_75,
  input  in_76,
  input  in_77,
  input  in_78,
  input  in_79,
  input  in_80,
  input  in_81,
  input  in_82,
  input  in_83,
  input  in_84,
  input  in_85,
  input  in_86,
  input  in_87,
  input  in_88,
  input  in_89,
  input  in_90,
  input  in_91,
  input  in_92,
  input  in_93,
  input  in_94,
  input  in_95,
  input  in_96,
  input  in_97,
  input  in_98,
  input  in_99,
  input  in_100,
  input  in_101,
  input  in_102,
  input  in_103,
  input  in_104,
  input  in_105,
  input  in_106,
  input  in_107,
  input  in_108,
  input  in_109,
  input  in_110
);

  Synth_12TET_8_Octaves synth_12tet_8_octaves_1 (
    .in_17(in_56), .in_5(in_49), .in_29(in_63), .in_41(in_70), .in_53(in_77), .in_65(in_84), .in_77(in_91),
    .in_89(in_98), .in_101(in_105), .A1(in_55), .A0(in_48), .A2(in_62), .A3(in_69), .A4(in_76), .A5(in_83),
    .A6(in_90), .A7(in_97), .A8(in_104), .in_18(in_57), .in_6(in_50), .in_30(in_64), .in_42(in_71),
    .in_54(in_78), .in_66(in_85), .in_78(in_92), .in_90(in_99), .in_102(in_106), .Waveform(in_1),
    .in_19(in_9), .in_7(in_4), .in_31(in_14), .in_43(in_19), .in_55(in_24), .in_67(in_29), .in_79(in_34),
    .in_91(in_39), .in_103(in_44), .in_20(in_58), .in_8(in_51), .in_32(in_65), .in_44(in_72), .in_56(in_79),
    .in_68(in_86), .in_80(in_93), .in_92(in_100), .in_104(in_107), .in_21(in_10), .in_9(in_5), .in_33(in_15),
    .in_45(in_20), .in_57(in_25), .in_69(in_30), .in_81(in_35), .in_93(in_40), .in_105(in_45), .in_22(in_59),
    .in_10(in_52), .in_34(in_66), .in_46(in_73), .in_58(in_80), .in_70(in_87), .in_82(in_94), .in_94(in_101),
    .in_106(in_108), .in_23(in_60), .in_11(in_53), .in_35(in_67), .in_47(in_74), .in_59(in_81),
    .in_71(in_88), .in_83(in_95), .in_95(in_102), .in_107(in_109), .Volume(in_2), .in_24(in_11),
    .in_12(in_6), .in_36(in_16), .in_48(in_21), .in_60(in_26), .in_72(in_31), .in_84(in_36), .in_96(in_41),
    .in_108(in_46), .in_25(in_61), .in_13(in_54), .in_37(in_68), .in_49(in_75), .in_61(in_82), .in_73(in_89),
    .in_85(in_96), .in_97(in_103), .in_109(in_110), .in_26(in_12), .in_14(in_7), .in_38(in_17),
    .in_50(in_22), .in_62(in_27), .in_74(in_32), .in_86(in_37), .in_98(in_42), .in_110(in_47), .in_16(in_8),
    .in_4(in_3), .in_28(in_13), .in_40(in_18), .in_52(in_23), .in_64(in_28), .in_76(in_33), .in_88(in_38),
    .in_100(in_43));

  // Notes on the sheet:
  //   0,0
  //   Waveform
  //   0,1
  //   1,0
  //   1,1
  //   Volume
endmodule

module Test_Bend (
  input  [1:0] in_1,
  input  [6:0] in_2,
  input  in_3,
  input  in_4,
  input  in_5,
  input  in_6,
  input  in_7,
  input  in_8,
  input  in_9,
  input  in_10,
  input  in_11,
  input  in_12,
  input  in_13,
  input  in_14,
  input  in_15,
  input  in_16,
  input  in_17,
  input  in_18,
  input  in_19,
  input  in_20,
  input  in_21,
  input  in_22,
  input  in_23,
  input  in_24,
  input  in_25,
  input  in_26,
  input  in_27,
  input  in_28,
  input  in_29,
  input  in_30,
  input  in_31,
  input  in_32,
  input  in_33,
  input  in_34,
  input  in_35,
  input  in_36,
  input  in_37,
  input  in_38
);

  wire button_1_out, button_2_out, button_3_out, button_4_out, button_5_out, button_6_out, button_7_out,
       button_8_out, button_9_out, button_10_out, button_11_out, button_12_out, button_13_out, button_14_out,
       button_15_out, button_16_out, button_17_out, button_18_out, button_19_out, button_20_out,
       button_21_out, button_22_out, button_23_out, button_24_out, button_25_out, button_26_out,
       button_27_out, button_28_out, button_29_out, button_30_out, button_31_out, button_32_out,
       button_33_out, button_34_out, button_35_out, button_36_out, demultiplexer_1_out0,
       demultiplexer_1_out1, demultiplexer_1_out2, demultiplexer_1_out3, demultiplexer_2_out0,
       demultiplexer_2_out1, demultiplexer_2_out2, demultiplexer_2_out3, demultiplexer_3_out0,
       demultiplexer_3_out1, demultiplexer_3_out2, demultiplexer_3_out3, demultiplexer_4_out0,
       demultiplexer_4_out1, demultiplexer_4_out2, demultiplexer_4_out3, demultiplexer_5_out0,
       demultiplexer_5_out1, demultiplexer_5_out2, demultiplexer_5_out3, demultiplexer_6_out0,
       demultiplexer_6_out1, demultiplexer_6_out2, demultiplexer_6_out3, demultiplexer_7_out0,
       demultiplexer_7_out1, demultiplexer_7_out2, demultiplexer_7_out3, demultiplexer_8_out0,
       demultiplexer_8_out1, demultiplexer_8_out2, demultiplexer_8_out3, demultiplexer_9_out0,
       demultiplexer_9_out1, demultiplexer_9_out2, demultiplexer_9_out3, demultiplexer_10_out0,
       demultiplexer_10_out1, demultiplexer_10_out2, demultiplexer_10_out3, demultiplexer_11_out0,
       demultiplexer_11_out1, demultiplexer_11_out2, demultiplexer_11_out3, demultiplexer_12_out0,
       demultiplexer_12_out1, demultiplexer_12_out2, demultiplexer_12_out3, demultiplexer_13_out0,
       demultiplexer_13_out1, demultiplexer_13_out2, demultiplexer_13_out3, demultiplexer_14_out0,
       demultiplexer_14_out1, demultiplexer_14_out2, demultiplexer_14_out3, demultiplexer_15_out0,
       demultiplexer_15_out1, demultiplexer_15_out2, demultiplexer_15_out3, demultiplexer_16_out0,
       demultiplexer_16_out1, demultiplexer_16_out2, demultiplexer_16_out3, demultiplexer_17_out0,
       demultiplexer_17_out1, demultiplexer_17_out2, demultiplexer_17_out3, demultiplexer_18_out0,
       demultiplexer_18_out1, demultiplexer_18_out2, demultiplexer_18_out3, demultiplexer_19_out0,
       demultiplexer_19_out1, demultiplexer_19_out2, demultiplexer_19_out3, demultiplexer_20_out0,
       demultiplexer_20_out1, demultiplexer_20_out2, demultiplexer_20_out3, demultiplexer_21_out0,
       demultiplexer_21_out1, demultiplexer_21_out2, demultiplexer_21_out3, demultiplexer_22_out0,
       demultiplexer_22_out1, demultiplexer_22_out2, demultiplexer_22_out3, demultiplexer_23_out0,
       demultiplexer_23_out1, demultiplexer_23_out2, demultiplexer_23_out3, demultiplexer_24_out0,
       demultiplexer_24_out1, demultiplexer_24_out2, demultiplexer_24_out3, demultiplexer_25_out0,
       demultiplexer_25_out1, demultiplexer_25_out2, demultiplexer_25_out3, demultiplexer_26_out0,
       demultiplexer_26_out1, demultiplexer_26_out2, demultiplexer_26_out3, demultiplexer_27_out0,
       demultiplexer_27_out1, demultiplexer_27_out2, demultiplexer_27_out3, demultiplexer_28_out0,
       demultiplexer_28_out1, demultiplexer_28_out2, demultiplexer_28_out3, demultiplexer_29_out0,
       demultiplexer_29_out1, demultiplexer_29_out2, demultiplexer_29_out3, demultiplexer_30_out0,
       demultiplexer_30_out1, demultiplexer_30_out2, demultiplexer_30_out3, demultiplexer_31_out0,
       demultiplexer_31_out1, demultiplexer_31_out2, demultiplexer_31_out3, demultiplexer_32_out0,
       demultiplexer_32_out1, demultiplexer_32_out2, demultiplexer_32_out3, demultiplexer_33_out0,
       demultiplexer_33_out1, demultiplexer_33_out2, demultiplexer_33_out3, demultiplexer_34_out0,
       demultiplexer_34_out1, demultiplexer_34_out2, demultiplexer_34_out3, demultiplexer_35_out0,
       demultiplexer_35_out1, demultiplexer_35_out2, demultiplexer_35_out3, demultiplexer_36_out0,
       demultiplexer_36_out1, demultiplexer_36_out2, demultiplexer_36_out3, xor_1_out, xor_2_out, xor_3_out,
       xor_4_out, xor_5_out, xor_6_out, xor_7_out, xor_8_out, xor_9_out, xor_10_out, xor_11_out, xor_12_out,
       xor_13_out, xor_14_out, xor_15_out, xor_16_out, xor_17_out, xor_18_out, xor_19_out, xor_20_out,
       xor_21_out, xor_22_out, xor_23_out, xor_24_out, xor_25_out, xor_26_out, xor_27_out, xor_28_out,
       xor_29_out, xor_30_out, xor_31_out, xor_32_out, xor_33_out, xor_34_out, xor_35_out, xor_36_out;
  wire [3:0] slider_1_out;
  wire [13:0] rom_1_data, rom_2_data, rom_3_data, rom_4_data, rom_5_data, rom_6_data, rom_7_data, rom_8_data,
       rom_9_data, rom_10_data, rom_11_data, rom_12_data, rom_13_data, rom_14_data, rom_15_data, rom_16_data,
       rom_17_data, rom_18_data, rom_19_data, rom_20_data, rom_21_data, rom_22_data, rom_23_data,
       rom_24_data, rom_25_data, rom_26_data, rom_27_data, rom_28_data, rom_29_data, rom_30_data,
       rom_31_data, rom_32_data, rom_33_data, rom_34_data, rom_35_data, rom_36_data;

  Button button_1 (.out(button_1_out));
  xor xor_1 (xor_1_out, in_3, button_1_out);
  Demultiplexer #(.select(2)) demultiplexer_1 (
    .out0(demultiplexer_1_out0), .out1(demultiplexer_1_out1), .out2(demultiplexer_1_out2),
    .out3(demultiplexer_1_out3), .in(xor_1_out), .sel(in_1));
  ROM #(.addrWidth(4), .dataWidth(14)) rom_1 (.addr(slider_1_out), .data(rom_1_data));
  Button button_2 (.out(button_2_out));
  xor xor_2 (xor_2_out, in_15, button_2_out);
  Demultiplexer #(.select(2)) demultiplexer_2 (
    .out0(demultiplexer_2_out0), .out1(demultiplexer_2_out1), .out2(demultiplexer_2_out2),
    .out3(demultiplexer_2_out3), .in(xor_2_out), .sel(in_1));
  ROM #(.addrWidth(4), .dataWidth(14)) rom_2 (.addr(slider_1_out), .data(rom_2_data));
  Button button_3 (.out(button_3_out));
  xor xor_3 (xor_3_out, in_27, button_3_out);
  Demultiplexer #(.select(2)) demultiplexer_3 (
    .out0(demultiplexer_3_out0), .out1(demultiplexer_3_out1), .out2(demultiplexer_3_out2),
    .out3(demultiplexer_3_out3), .in(xor_3_out), .sel(in_1));
  ROM #(.addrWidth(4), .dataWidth(14)) rom_3 (.addr(slider_1_out), .data(rom_3_data));
  // Buzzer #(.waveform("Square")) buzzer_1: pin names not known; wires that end beside it: rom_1_data, demultiplexer_1_out1, in_2
  // Buzzer buzzer_2: pin names not known; wires that end beside it: rom_1_data, demultiplexer_1_out0, in_2
  // Buzzer #(.waveform("Square")) buzzer_3: pin names not known; wires that end beside it: rom_2_data, demultiplexer_2_out1, in_2
  // Buzzer buzzer_4: pin names not known; wires that end beside it: rom_2_data, demultiplexer_2_out0, in_2
  // Buzzer #(.waveform("Square")) buzzer_5: pin names not known; wires that end beside it: rom_3_data, demultiplexer_3_out1, in_2
  // Buzzer buzzer_6: pin names not known; wires that end beside it: rom_3_data, demultiplexer_3_out0, in_2
  // Buzzer #(.waveform("Sawtooth")) buzzer_7: pin names not known; wires that end beside it: rom_1_data, demultiplexer_1_out3, in_2
  // Buzzer #(.waveform("Triangle")) buzzer_8: pin names not known; wires that end beside it: rom_1_data, demultiplexer_1_out2, in_2
  // Buzzer #(.waveform("Sawtooth")) buzzer_9: pin names not known; wires that end beside it: rom_2_data, demultiplexer_2_out3, in_2
  // Buzzer #(.waveform("Triangle")) buzzer_10: pin names not known; wires that end beside it: rom_2_data, demultiplexer_2_out2, in_2
  // Buzzer #(.waveform("Sawtooth")) buzzer_11: pin names not known; wires that end beside it: rom_3_data, demultiplexer_3_out3, in_2
  // Buzzer #(.waveform("Triangle")) buzzer_12: pin names not known; wires that end beside it: rom_3_data, demultiplexer_3_out2, in_2
  Button button_4 (.out(button_4_out));
  xor xor_4 (xor_4_out, in_4, button_4_out);
  Demultiplexer #(.select(2)) demultiplexer_4 (
    .out0(demultiplexer_4_out0), .out1(demultiplexer_4_out1), .out2(demultiplexer_4_out2),
    .out3(demultiplexer_4_out3), .in(xor_4_out), .sel(in_1));
  ROM #(.addrWidth(4), .dataWidth(14)) rom_4 (.addr(slider_1_out), .data(rom_4_data));
  Button button_5 (.out(button_5_out));
  xor xor_5 (xor_5_out, in_16, button_5_out);
  Demultiplexer #(.select(2)) demultiplexer_5 (
    .out0(demultiplexer_5_out0), .out1(demultiplexer_5_out1), .out2(demultiplexer_5_out2),
    .out3(demultiplexer_5_out3), .in(xor_5_out), .sel(in_1));
  ROM #(.addrWidth(4), .dataWidth(14)) rom_5 (.addr(slider_1_out), .data(rom_5_data));
  Button button_6 (.out(button_6_out));
  xor xor_6 (xor_6_out, in_28, button_6_out);
  Demultiplexer #(.select(2)) demultiplexer_6 (
    .out0(demultiplexer_6_out0), .out1(demultiplexer_6_out1), .out2(demultiplexer_6_out2),
    .out3(demultiplexer_6_out3), .in(xor_6_out), .sel(in_1));
  ROM #(.addrWidth(4), .dataWidth(14)) rom_6 (.addr(slider_1_out), .data(rom_6_data));
  // Buzzer buzzer_13: pin names not known; wires that end beside it: rom_4_data, demultiplexer_4_out0, in_2
  // Buzzer buzzer_14: pin names not known; wires that end beside it: rom_5_data, demultiplexer_5_out0, in_2
  // Buzzer buzzer_15: pin names not known; wires that end beside it: rom_6_data, demultiplexer_6_out0, in_2
  // Buzzer #(.waveform("Triangle")) buzzer_16: pin names not known; wires that end beside it: rom_4_data, demultiplexer_4_out2, in_2
  // Buzzer #(.waveform("Square")) buzzer_17: pin names not known; wires that end beside it: rom_4_data, demultiplexer_4_out1, in_2
  // Buzzer #(.waveform("Triangle")) buzzer_18: pin names not known; wires that end beside it: rom_5_data, demultiplexer_5_out2, in_2
  // Buzzer #(.waveform("Square")) buzzer_19: pin names not known; wires that end beside it: rom_5_data, demultiplexer_5_out1, in_2
  // Buzzer #(.waveform("Triangle")) buzzer_20: pin names not known; wires that end beside it: rom_6_data, demultiplexer_6_out2, in_2
  // Buzzer #(.waveform("Square")) buzzer_21: pin names not known; wires that end beside it: rom_6_data, demultiplexer_6_out1, in_2
  // Buzzer #(.waveform("Sawtooth")) buzzer_22: pin names not known; wires that end beside it: rom_4_data, demultiplexer_4_out3, in_2
  // Buzzer #(.waveform("Sawtooth")) buzzer_23: pin names not known; wires that end beside it: rom_5_data, demultiplexer_5_out3, in_2
  // Buzzer #(.waveform("Sawtooth")) buzzer_24: pin names not known; wires that end beside it: rom_6_data, demultiplexer_6_out3, in_2
  Button button_7 (.out(button_7_out));
  xor xor_7 (xor_7_out, in_5, button_7_out);
  Demultiplexer #(.select(2)) demultiplexer_7 (
    .out0(demultiplexer_7_out0), .out1(demultiplexer_7_out1), .out2(demultiplexer_7_out2),
    .out3(demultiplexer_7_out3), .in(xor_7_out), .sel(in_1));
  ROM #(.addrWidth(4), .dataWidth(14)) rom_7 (.addr(slider_1_out), .data(rom_7_data));
  Button button_8 (.out(button_8_out));
  xor xor_8 (xor_8_out, in_17, button_8_out);
  Demultiplexer #(.select(2)) demultiplexer_8 (
    .out0(demultiplexer_8_out0), .out1(demultiplexer_8_out1), .out2(demultiplexer_8_out2),
    .out3(demultiplexer_8_out3), .in(xor_8_out), .sel(in_1));
  ROM #(.addrWidth(4), .dataWidth(14)) rom_8 (.addr(slider_1_out), .data(rom_8_data));
  Button button_9 (.out(button_9_out));
  xor xor_9 (xor_9_out, in_29, button_9_out);
  Demultiplexer #(.select(2)) demultiplexer_9 (
    .out0(demultiplexer_9_out0), .out1(demultiplexer_9_out1), .out2(demultiplexer_9_out2),
    .out3(demultiplexer_9_out3), .in(xor_9_out), .sel(in_1));
  ROM #(.addrWidth(4), .dataWidth(14)) rom_9 (.addr(slider_1_out), .data(rom_9_data));
  // Buzzer #(.waveform("Square")) buzzer_25: pin names not known; wires that end beside it: rom_7_data, demultiplexer_7_out1, in_2
  // Buzzer buzzer_26: pin names not known; wires that end beside it: rom_7_data, demultiplexer_7_out0, in_2
  // Buzzer #(.waveform("Square")) buzzer_27: pin names not known; wires that end beside it: rom_8_data, demultiplexer_8_out1, in_2
  // Buzzer buzzer_28: pin names not known; wires that end beside it: rom_8_data, demultiplexer_8_out0, in_2
  // Buzzer #(.waveform("Square")) buzzer_29: pin names not known; wires that end beside it: rom_9_data, demultiplexer_9_out1, in_2
  // Buzzer buzzer_30: pin names not known; wires that end beside it: rom_9_data, demultiplexer_9_out0, in_2
  // Buzzer #(.waveform("Sawtooth")) buzzer_31: pin names not known; wires that end beside it: rom_7_data, demultiplexer_7_out3, in_2
  // Buzzer #(.waveform("Triangle")) buzzer_32: pin names not known; wires that end beside it: rom_7_data, demultiplexer_7_out2, in_2
  // Buzzer #(.waveform("Sawtooth")) buzzer_33: pin names not known; wires that end beside it: rom_8_data, demultiplexer_8_out3, in_2
  // Buzzer #(.waveform("Triangle")) buzzer_34: pin names not known; wires that end beside it: rom_8_data, demultiplexer_8_out2, in_2
  // Buzzer #(.waveform("Sawtooth")) buzzer_35: pin names not known; wires that end beside it: rom_9_data, demultiplexer_9_out3, in_2
  // Buzzer #(.waveform("Triangle")) buzzer_36: pin names not known; wires that end beside it: rom_9_data, demultiplexer_9_out2, in_2
  Slider #(.width(4)) slider_1 (.out(slider_1_out));
  Button button_10 (.out(button_10_out));
  xor xor_10 (xor_10_out, in_6, button_10_out);
  Demultiplexer #(.select(2)) demultiplexer_10 (
    .out0(demultiplexer_10_out0), .out1(demultiplexer_10_out1), .out2(demultiplexer_10_out2),
    .out3(demultiplexer_10_out3), .in(xor_10_out), .sel(in_1));
  ROM #(.addrWidth(4), .dataWidth(14)) rom_10 (.addr(slider_1_out), .data(rom_10_data));
  Button button_11 (.out(button_11_out));
  xor xor_11 (xor_11_out, in_18, button_11_out);
  Demultiplexer #(.select(2)) demultiplexer_11 (
    .out0(demultiplexer_11_out0), .out1(demultiplexer_11_out1), .out2(demultiplexer_11_out2),
    .out3(demultiplexer_11_out3), .in(xor_11_out), .sel(in_1));
  ROM #(.addrWidth(4), .dataWidth(14)) rom_11 (.addr(slider_1_out), .data(rom_11_data));
  Button button_12 (.out(button_12_out));
  xor xor_12 (xor_12_out, in_30, button_12_out);
  Demultiplexer #(.select(2)) demultiplexer_12 (
    .out0(demultiplexer_12_out0), .out1(demultiplexer_12_out1), .out2(demultiplexer_12_out2),
    .out3(demultiplexer_12_out3), .in(xor_12_out), .sel(in_1));
  ROM #(.addrWidth(4), .dataWidth(14)) rom_12 (.addr(slider_1_out), .data(rom_12_data));
  // Buzzer buzzer_37: pin names not known; wires that end beside it: rom_10_data, demultiplexer_10_out0, in_2
  // Buzzer buzzer_38: pin names not known; wires that end beside it: rom_11_data, demultiplexer_11_out0, in_2
  // Buzzer buzzer_39: pin names not known; wires that end beside it: rom_12_data, demultiplexer_12_out0, in_2
  // Buzzer #(.waveform("Triangle")) buzzer_40: pin names not known; wires that end beside it: rom_10_data, demultiplexer_10_out2, in_2
  // Buzzer #(.waveform("Square")) buzzer_41: pin names not known; wires that end beside it: rom_10_data, demultiplexer_10_out1, in_2
  // Buzzer #(.waveform("Triangle")) buzzer_42: pin names not known; wires that end beside it: rom_11_data, demultiplexer_11_out2, in_2
  // Buzzer #(.waveform("Square")) buzzer_43: pin names not known; wires that end beside it: rom_11_data, demultiplexer_11_out1, in_2
  // Buzzer #(.waveform("Triangle")) buzzer_44: pin names not known; wires that end beside it: rom_12_data, demultiplexer_12_out2, in_2
  // Buzzer #(.waveform("Square")) buzzer_45: pin names not known; wires that end beside it: rom_12_data, demultiplexer_12_out1, in_2
  // Buzzer #(.waveform("Sawtooth")) buzzer_46: pin names not known; wires that end beside it: rom_10_data, demultiplexer_10_out3, in_2
  // Buzzer #(.waveform("Sawtooth")) buzzer_47: pin names not known; wires that end beside it: rom_11_data, demultiplexer_11_out3, in_2
  // Buzzer #(.waveform("Sawtooth")) buzzer_48: pin names not known; wires that end beside it: rom_12_data, demultiplexer_12_out3, in_2
  Button button_13 (.out(button_13_out));
  xor xor_13 (xor_13_out, in_7, button_13_out);
  Demultiplexer #(.select(2)) demultiplexer_13 (
    .out0(demultiplexer_13_out0), .out1(demultiplexer_13_out1), .out2(demultiplexer_13_out2),
    .out3(demultiplexer_13_out3), .in(xor_13_out), .sel(in_1));
  ROM #(.addrWidth(4), .dataWidth(14)) rom_13 (.addr(slider_1_out), .data(rom_13_data));
  Button button_14 (.out(button_14_out));
  xor xor_14 (xor_14_out, in_19, button_14_out);
  Demultiplexer #(.select(2)) demultiplexer_14 (
    .out0(demultiplexer_14_out0), .out1(demultiplexer_14_out1), .out2(demultiplexer_14_out2),
    .out3(demultiplexer_14_out3), .in(xor_14_out), .sel(in_1));
  ROM #(.addrWidth(4), .dataWidth(14)) rom_14 (.addr(slider_1_out), .data(rom_14_data));
  Button button_15 (.out(button_15_out));
  xor xor_15 (xor_15_out, in_31, button_15_out);
  Demultiplexer #(.select(2)) demultiplexer_15 (
    .out0(demultiplexer_15_out0), .out1(demultiplexer_15_out1), .out2(demultiplexer_15_out2),
    .out3(demultiplexer_15_out3), .in(xor_15_out), .sel(in_1));
  ROM #(.addrWidth(4), .dataWidth(14)) rom_15 (.addr(slider_1_out), .data(rom_15_data));
  // Buzzer #(.waveform("Square")) buzzer_49: pin names not known; wires that end beside it: rom_13_data, demultiplexer_13_out1, in_2
  // Buzzer buzzer_50: pin names not known; wires that end beside it: rom_13_data, demultiplexer_13_out0, in_2
  // Buzzer #(.waveform("Square")) buzzer_51: pin names not known; wires that end beside it: rom_14_data, demultiplexer_14_out1, in_2
  // Buzzer buzzer_52: pin names not known; wires that end beside it: rom_14_data, demultiplexer_14_out0, in_2
  // Buzzer #(.waveform("Square")) buzzer_53: pin names not known; wires that end beside it: rom_15_data, demultiplexer_15_out1, in_2
  // Buzzer buzzer_54: pin names not known; wires that end beside it: rom_15_data, demultiplexer_15_out0, in_2
  // Buzzer #(.waveform("Sawtooth")) buzzer_55: pin names not known; wires that end beside it: rom_13_data, demultiplexer_13_out3, in_2
  // Buzzer #(.waveform("Triangle")) buzzer_56: pin names not known; wires that end beside it: rom_13_data, demultiplexer_13_out2, in_2
  // Buzzer #(.waveform("Sawtooth")) buzzer_57: pin names not known; wires that end beside it: rom_14_data, demultiplexer_14_out3, in_2
  // Buzzer #(.waveform("Triangle")) buzzer_58: pin names not known; wires that end beside it: rom_14_data, demultiplexer_14_out2, in_2
  // Buzzer #(.waveform("Sawtooth")) buzzer_59: pin names not known; wires that end beside it: rom_15_data, demultiplexer_15_out3, in_2
  // Buzzer #(.waveform("Triangle")) buzzer_60: pin names not known; wires that end beside it: rom_15_data, demultiplexer_15_out2, in_2
  Button button_16 (.out(button_16_out));
  xor xor_16 (xor_16_out, in_8, button_16_out);
  Demultiplexer #(.select(2)) demultiplexer_16 (
    .out0(demultiplexer_16_out0), .out1(demultiplexer_16_out1), .out2(demultiplexer_16_out2),
    .out3(demultiplexer_16_out3), .in(xor_16_out), .sel(in_1));
  ROM #(.addrWidth(4), .dataWidth(14)) rom_16 (.addr(slider_1_out), .data(rom_16_data));
  Button button_17 (.out(button_17_out));
  xor xor_17 (xor_17_out, in_20, button_17_out);
  Demultiplexer #(.select(2)) demultiplexer_17 (
    .out0(demultiplexer_17_out0), .out1(demultiplexer_17_out1), .out2(demultiplexer_17_out2),
    .out3(demultiplexer_17_out3), .in(xor_17_out), .sel(in_1));
  ROM #(.addrWidth(4), .dataWidth(14)) rom_17 (.addr(slider_1_out), .data(rom_17_data));
  Button button_18 (.out(button_18_out));
  xor xor_18 (xor_18_out, in_32, button_18_out);
  Demultiplexer #(.select(2)) demultiplexer_18 (
    .out0(demultiplexer_18_out0), .out1(demultiplexer_18_out1), .out2(demultiplexer_18_out2),
    .out3(demultiplexer_18_out3), .in(xor_18_out), .sel(in_1));
  ROM #(.addrWidth(4), .dataWidth(14)) rom_18 (.addr(slider_1_out), .data(rom_18_data));
  // Buzzer buzzer_61: pin names not known; wires that end beside it: rom_16_data, demultiplexer_16_out0, in_2
  // Buzzer buzzer_62: pin names not known; wires that end beside it: rom_17_data, demultiplexer_17_out0, in_2
  // Buzzer buzzer_63: pin names not known; wires that end beside it: rom_18_data, demultiplexer_18_out0, in_2
  // Buzzer #(.waveform("Triangle")) buzzer_64: pin names not known; wires that end beside it: rom_16_data, demultiplexer_16_out2, in_2
  // Buzzer #(.waveform("Square")) buzzer_65: pin names not known; wires that end beside it: rom_16_data, demultiplexer_16_out1, in_2
  // Buzzer #(.waveform("Triangle")) buzzer_66: pin names not known; wires that end beside it: rom_17_data, demultiplexer_17_out2, in_2
  // Buzzer #(.waveform("Square")) buzzer_67: pin names not known; wires that end beside it: rom_17_data, demultiplexer_17_out1, in_2
  // Buzzer #(.waveform("Triangle")) buzzer_68: pin names not known; wires that end beside it: rom_18_data, demultiplexer_18_out2, in_2
  // Buzzer #(.waveform("Square")) buzzer_69: pin names not known; wires that end beside it: rom_18_data, demultiplexer_18_out1, in_2
  // Buzzer #(.waveform("Sawtooth")) buzzer_70: pin names not known; wires that end beside it: rom_16_data, demultiplexer_16_out3, in_2
  // Buzzer #(.waveform("Sawtooth")) buzzer_71: pin names not known; wires that end beside it: rom_17_data, demultiplexer_17_out3, in_2
  // Buzzer #(.waveform("Sawtooth")) buzzer_72: pin names not known; wires that end beside it: rom_18_data, demultiplexer_18_out3, in_2
  Button button_19 (.out(button_19_out));
  xor xor_19 (xor_19_out, in_9, button_19_out);
  Demultiplexer #(.select(2)) demultiplexer_19 (
    .out0(demultiplexer_19_out0), .out1(demultiplexer_19_out1), .out2(demultiplexer_19_out2),
    .out3(demultiplexer_19_out3), .in(xor_19_out), .sel(in_1));
  ROM #(.addrWidth(4), .dataWidth(14)) rom_19 (.addr(slider_1_out), .data(rom_19_data));
  Button button_20 (.out(button_20_out));
  xor xor_20 (xor_20_out, in_21, button_20_out);
  Demultiplexer #(.select(2)) demultiplexer_20 (
    .out0(demultiplexer_20_out0), .out1(demultiplexer_20_out1), .out2(demultiplexer_20_out2),
    .out3(demultiplexer_20_out3), .in(xor_20_out), .sel(in_1));
  ROM #(.addrWidth(4), .dataWidth(14)) rom_20 (.addr(slider_1_out), .data(rom_20_data));
  Button button_21 (.out(button_21_out));
  xor xor_21 (xor_21_out, in_33, button_21_out);
  Demultiplexer #(.select(2)) demultiplexer_21 (
    .out0(demultiplexer_21_out0), .out1(demultiplexer_21_out1), .out2(demultiplexer_21_out2),
    .out3(demultiplexer_21_out3), .in(xor_21_out), .sel(in_1));
  ROM #(.addrWidth(4), .dataWidth(14)) rom_21 (.addr(slider_1_out), .data(rom_21_data));
  // Buzzer #(.waveform("Square")) buzzer_73: pin names not known; wires that end beside it: rom_19_data, demultiplexer_19_out1, in_2
  // Buzzer buzzer_74: pin names not known; wires that end beside it: rom_19_data, demultiplexer_19_out0, in_2
  // Buzzer #(.waveform("Square")) buzzer_75: pin names not known; wires that end beside it: rom_20_data, demultiplexer_20_out1, in_2
  // Buzzer buzzer_76: pin names not known; wires that end beside it: rom_20_data, demultiplexer_20_out0, in_2
  // Buzzer #(.waveform("Square")) buzzer_77: pin names not known; wires that end beside it: rom_21_data, demultiplexer_21_out1, in_2
  // Buzzer buzzer_78: pin names not known; wires that end beside it: rom_21_data, demultiplexer_21_out0, in_2
  // Buzzer #(.waveform("Sawtooth")) buzzer_79: pin names not known; wires that end beside it: rom_19_data, demultiplexer_19_out3, in_2
  // Buzzer #(.waveform("Triangle")) buzzer_80: pin names not known; wires that end beside it: rom_19_data, demultiplexer_19_out2, in_2
  // Buzzer #(.waveform("Sawtooth")) buzzer_81: pin names not known; wires that end beside it: rom_20_data, demultiplexer_20_out3, in_2
  // Buzzer #(.waveform("Triangle")) buzzer_82: pin names not known; wires that end beside it: rom_20_data, demultiplexer_20_out2, in_2
  // Buzzer #(.waveform("Sawtooth")) buzzer_83: pin names not known; wires that end beside it: rom_21_data, demultiplexer_21_out3, in_2
  // Buzzer #(.waveform("Triangle")) buzzer_84: pin names not known; wires that end beside it: rom_21_data, demultiplexer_21_out2, in_2
  Button button_22 (.out(button_22_out));
  xor xor_22 (xor_22_out, in_10, button_22_out);
  Demultiplexer #(.select(2)) demultiplexer_22 (
    .out0(demultiplexer_22_out0), .out1(demultiplexer_22_out1), .out2(demultiplexer_22_out2),
    .out3(demultiplexer_22_out3), .in(xor_22_out), .sel(in_1));
  ROM #(.addrWidth(4), .dataWidth(14)) rom_22 (.addr(slider_1_out), .data(rom_22_data));
  Button button_23 (.out(button_23_out));
  xor xor_23 (xor_23_out, in_22, button_23_out);
  Demultiplexer #(.select(2)) demultiplexer_23 (
    .out0(demultiplexer_23_out0), .out1(demultiplexer_23_out1), .out2(demultiplexer_23_out2),
    .out3(demultiplexer_23_out3), .in(xor_23_out), .sel(in_1));
  ROM #(.addrWidth(4), .dataWidth(14)) rom_23 (.addr(slider_1_out), .data(rom_23_data));
  Button button_24 (.out(button_24_out));
  xor xor_24 (xor_24_out, in_34, button_24_out);
  Demultiplexer #(.select(2)) demultiplexer_24 (
    .out0(demultiplexer_24_out0), .out1(demultiplexer_24_out1), .out2(demultiplexer_24_out2),
    .out3(demultiplexer_24_out3), .in(xor_24_out), .sel(in_1));
  ROM #(.addrWidth(4), .dataWidth(14)) rom_24 (.addr(slider_1_out), .data(rom_24_data));
  // Buzzer buzzer_85: pin names not known; wires that end beside it: rom_22_data, demultiplexer_22_out0, in_2
  // Buzzer buzzer_86: pin names not known; wires that end beside it: rom_23_data, demultiplexer_23_out0, in_2
  // Buzzer buzzer_87: pin names not known; wires that end beside it: rom_24_data, demultiplexer_24_out0, in_2
  // Buzzer #(.waveform("Triangle")) buzzer_88: pin names not known; wires that end beside it: rom_22_data, demultiplexer_22_out2, in_2
  // Buzzer #(.waveform("Square")) buzzer_89: pin names not known; wires that end beside it: rom_22_data, demultiplexer_22_out1, in_2
  // Buzzer #(.waveform("Triangle")) buzzer_90: pin names not known; wires that end beside it: rom_23_data, demultiplexer_23_out2, in_2
  // Buzzer #(.waveform("Square")) buzzer_91: pin names not known; wires that end beside it: rom_23_data, demultiplexer_23_out1, in_2
  // Buzzer #(.waveform("Triangle")) buzzer_92: pin names not known; wires that end beside it: rom_24_data, demultiplexer_24_out2, in_2
  // Buzzer #(.waveform("Square")) buzzer_93: pin names not known; wires that end beside it: rom_24_data, demultiplexer_24_out1, in_2
  // Buzzer #(.waveform("Sawtooth")) buzzer_94: pin names not known; wires that end beside it: rom_22_data, demultiplexer_22_out3, in_2
  // Buzzer #(.waveform("Sawtooth")) buzzer_95: pin names not known; wires that end beside it: rom_23_data, demultiplexer_23_out3, in_2
  // Buzzer #(.waveform("Sawtooth")) buzzer_96: pin names not known; wires that end beside it: rom_24_data, demultiplexer_24_out3, in_2
  Button button_25 (.out(button_25_out));
  xor xor_25 (xor_25_out, in_11, button_25_out);
  Demultiplexer #(.select(2)) demultiplexer_25 (
    .out0(demultiplexer_25_out0), .out1(demultiplexer_25_out1), .out2(demultiplexer_25_out2),
    .out3(demultiplexer_25_out3), .in(xor_25_out), .sel(in_1));
  ROM #(.addrWidth(4), .dataWidth(14)) rom_25 (.addr(slider_1_out), .data(rom_25_data));
  Button button_26 (.out(button_26_out));
  xor xor_26 (xor_26_out, in_23, button_26_out);
  Demultiplexer #(.select(2)) demultiplexer_26 (
    .out0(demultiplexer_26_out0), .out1(demultiplexer_26_out1), .out2(demultiplexer_26_out2),
    .out3(demultiplexer_26_out3), .in(xor_26_out), .sel(in_1));
  ROM #(.addrWidth(4), .dataWidth(14)) rom_26 (.addr(slider_1_out), .data(rom_26_data));
  Button button_27 (.out(button_27_out));
  xor xor_27 (xor_27_out, in_35, button_27_out);
  Demultiplexer #(.select(2)) demultiplexer_27 (
    .out0(demultiplexer_27_out0), .out1(demultiplexer_27_out1), .out2(demultiplexer_27_out2),
    .out3(demultiplexer_27_out3), .in(xor_27_out), .sel(in_1));
  ROM #(.addrWidth(4), .dataWidth(14)) rom_27 (.addr(slider_1_out), .data(rom_27_data));
  // Buzzer #(.waveform("Square")) buzzer_97: pin names not known; wires that end beside it: rom_25_data, demultiplexer_25_out1, in_2
  // Buzzer buzzer_98: pin names not known; wires that end beside it: rom_25_data, demultiplexer_25_out0, in_2
  // Buzzer #(.waveform("Square")) buzzer_99: pin names not known; wires that end beside it: rom_26_data, demultiplexer_26_out1, in_2
  // Buzzer buzzer_100: pin names not known; wires that end beside it: rom_26_data, demultiplexer_26_out0, in_2
  // Buzzer #(.waveform("Square")) buzzer_101: pin names not known; wires that end beside it: rom_27_data, demultiplexer_27_out1, in_2
  // Buzzer buzzer_102: pin names not known; wires that end beside it: rom_27_data, demultiplexer_27_out0, in_2
  // Buzzer #(.waveform("Sawtooth")) buzzer_103: pin names not known; wires that end beside it: rom_25_data, demultiplexer_25_out3, in_2
  // Buzzer #(.waveform("Triangle")) buzzer_104: pin names not known; wires that end beside it: rom_25_data, demultiplexer_25_out2, in_2
  // Buzzer #(.waveform("Sawtooth")) buzzer_105: pin names not known; wires that end beside it: rom_26_data, demultiplexer_26_out3, in_2
  // Buzzer #(.waveform("Triangle")) buzzer_106: pin names not known; wires that end beside it: rom_26_data, demultiplexer_26_out2, in_2
  // Buzzer #(.waveform("Sawtooth")) buzzer_107: pin names not known; wires that end beside it: rom_27_data, demultiplexer_27_out3, in_2
  // Buzzer #(.waveform("Triangle")) buzzer_108: pin names not known; wires that end beside it: rom_27_data, demultiplexer_27_out2, in_2
  Button button_28 (.out(button_28_out));
  xor xor_28 (xor_28_out, in_12, button_28_out);
  Demultiplexer #(.select(2)) demultiplexer_28 (
    .out0(demultiplexer_28_out0), .out1(demultiplexer_28_out1), .out2(demultiplexer_28_out2),
    .out3(demultiplexer_28_out3), .in(xor_28_out), .sel(in_1));
  ROM #(.addrWidth(4), .dataWidth(14)) rom_28 (.addr(slider_1_out), .data(rom_28_data));
  Button button_29 (.out(button_29_out));
  xor xor_29 (xor_29_out, in_24, button_29_out);
  Demultiplexer #(.select(2)) demultiplexer_29 (
    .out0(demultiplexer_29_out0), .out1(demultiplexer_29_out1), .out2(demultiplexer_29_out2),
    .out3(demultiplexer_29_out3), .in(xor_29_out), .sel(in_1));
  ROM #(.addrWidth(4), .dataWidth(14)) rom_29 (.addr(slider_1_out), .data(rom_29_data));
  Button button_30 (.out(button_30_out));
  xor xor_30 (xor_30_out, in_36, button_30_out);
  Demultiplexer #(.select(2)) demultiplexer_30 (
    .out0(demultiplexer_30_out0), .out1(demultiplexer_30_out1), .out2(demultiplexer_30_out2),
    .out3(demultiplexer_30_out3), .in(xor_30_out), .sel(in_1));
  ROM #(.addrWidth(4), .dataWidth(14)) rom_30 (.addr(slider_1_out), .data(rom_30_data));
  // Buzzer buzzer_109: pin names not known; wires that end beside it: rom_28_data, demultiplexer_28_out0, in_2
  // Buzzer buzzer_110: pin names not known; wires that end beside it: rom_29_data, demultiplexer_29_out0, in_2
  // Buzzer buzzer_111: pin names not known; wires that end beside it: rom_30_data, demultiplexer_30_out0, in_2
  // Buzzer #(.waveform("Triangle")) buzzer_112: pin names not known; wires that end beside it: rom_28_data, demultiplexer_28_out2, in_2
  // Buzzer #(.waveform("Square")) buzzer_113: pin names not known; wires that end beside it: rom_28_data, demultiplexer_28_out1, in_2
  // Buzzer #(.waveform("Triangle")) buzzer_114: pin names not known; wires that end beside it: rom_29_data, demultiplexer_29_out2, in_2
  // Buzzer #(.waveform("Square")) buzzer_115: pin names not known; wires that end beside it: rom_29_data, demultiplexer_29_out1, in_2
  // Buzzer #(.waveform("Triangle")) buzzer_116: pin names not known; wires that end beside it: rom_30_data, demultiplexer_30_out2, in_2
  // Buzzer #(.waveform("Square")) buzzer_117: pin names not known; wires that end beside it: rom_30_data, demultiplexer_30_out1, in_2
  // Buzzer #(.waveform("Sawtooth")) buzzer_118: pin names not known; wires that end beside it: rom_28_data, demultiplexer_28_out3, in_2
  // Buzzer #(.waveform("Sawtooth")) buzzer_119: pin names not known; wires that end beside it: rom_29_data, demultiplexer_29_out3, in_2
  // Buzzer #(.waveform("Sawtooth")) buzzer_120: pin names not known; wires that end beside it: rom_30_data, demultiplexer_30_out3, in_2
  Button button_31 (.out(button_31_out));
  xor xor_31 (xor_31_out, in_13, button_31_out);
  Demultiplexer #(.select(2)) demultiplexer_31 (
    .out0(demultiplexer_31_out0), .out1(demultiplexer_31_out1), .out2(demultiplexer_31_out2),
    .out3(demultiplexer_31_out3), .in(xor_31_out), .sel(in_1));
  ROM #(.addrWidth(4), .dataWidth(14)) rom_31 (.addr(slider_1_out), .data(rom_31_data));
  Button button_32 (.out(button_32_out));
  xor xor_32 (xor_32_out, in_25, button_32_out);
  Demultiplexer #(.select(2)) demultiplexer_32 (
    .out0(demultiplexer_32_out0), .out1(demultiplexer_32_out1), .out2(demultiplexer_32_out2),
    .out3(demultiplexer_32_out3), .in(xor_32_out), .sel(in_1));
  ROM #(.addrWidth(4), .dataWidth(14)) rom_32 (.addr(slider_1_out), .data(rom_32_data));
  Button button_33 (.out(button_33_out));
  xor xor_33 (xor_33_out, in_37, button_33_out);
  Demultiplexer #(.select(2)) demultiplexer_33 (
    .out0(demultiplexer_33_out0), .out1(demultiplexer_33_out1), .out2(demultiplexer_33_out2),
    .out3(demultiplexer_33_out3), .in(xor_33_out), .sel(in_1));
  ROM #(.addrWidth(4), .dataWidth(14)) rom_33 (.addr(slider_1_out), .data(rom_33_data));
  // Buzzer #(.waveform("Square")) buzzer_121: pin names not known; wires that end beside it: rom_31_data, demultiplexer_31_out1, in_2
  // Buzzer buzzer_122: pin names not known; wires that end beside it: rom_31_data, demultiplexer_31_out0, in_2
  // Buzzer #(.waveform("Square")) buzzer_123: pin names not known; wires that end beside it: rom_32_data, demultiplexer_32_out1, in_2
  // Buzzer buzzer_124: pin names not known; wires that end beside it: rom_32_data, demultiplexer_32_out0, in_2
  // Buzzer #(.waveform("Square")) buzzer_125: pin names not known; wires that end beside it: rom_33_data, demultiplexer_33_out1, in_2
  // Buzzer buzzer_126: pin names not known; wires that end beside it: rom_33_data, demultiplexer_33_out0, in_2
  // Buzzer #(.waveform("Sawtooth")) buzzer_127: pin names not known; wires that end beside it: rom_31_data, demultiplexer_31_out3, in_2
  // Buzzer #(.waveform("Triangle")) buzzer_128: pin names not known; wires that end beside it: rom_31_data, demultiplexer_31_out2, in_2
  // Buzzer #(.waveform("Sawtooth")) buzzer_129: pin names not known; wires that end beside it: rom_32_data, demultiplexer_32_out3, in_2
  // Buzzer #(.waveform("Triangle")) buzzer_130: pin names not known; wires that end beside it: rom_32_data, demultiplexer_32_out2, in_2
  // Buzzer #(.waveform("Sawtooth")) buzzer_131: pin names not known; wires that end beside it: rom_33_data, demultiplexer_33_out3, in_2
  // Buzzer #(.waveform("Triangle")) buzzer_132: pin names not known; wires that end beside it: rom_33_data, demultiplexer_33_out2, in_2
  Button button_34 (.out(button_34_out));
  xor xor_34 (xor_34_out, in_14, button_34_out);
  Demultiplexer #(.select(2)) demultiplexer_34 (
    .out0(demultiplexer_34_out0), .out1(demultiplexer_34_out1), .out2(demultiplexer_34_out2),
    .out3(demultiplexer_34_out3), .in(xor_34_out), .sel(in_1));
  ROM #(.addrWidth(4), .dataWidth(14)) rom_34 (.addr(slider_1_out), .data(rom_34_data));
  Button button_35 (.out(button_35_out));
  xor xor_35 (xor_35_out, in_26, button_35_out);
  Demultiplexer #(.select(2)) demultiplexer_35 (
    .out0(demultiplexer_35_out0), .out1(demultiplexer_35_out1), .out2(demultiplexer_35_out2),
    .out3(demultiplexer_35_out3), .in(xor_35_out), .sel(in_1));
  ROM #(.addrWidth(4), .dataWidth(14)) rom_35 (.addr(slider_1_out), .data(rom_35_data));
  Button button_36 (.out(button_36_out));
  xor xor_36 (xor_36_out, in_38, button_36_out);
  Demultiplexer #(.select(2)) demultiplexer_36 (
    .out0(demultiplexer_36_out0), .out1(demultiplexer_36_out1), .out2(demultiplexer_36_out2),
    .out3(demultiplexer_36_out3), .in(xor_36_out), .sel(in_1));
  ROM #(.addrWidth(4), .dataWidth(14)) rom_36 (.addr(slider_1_out), .data(rom_36_data));
  // Buzzer buzzer_133: pin names not known; wires that end beside it: rom_34_data, demultiplexer_34_out0, in_2
  // Buzzer buzzer_134: pin names not known; wires that end beside it: rom_35_data, demultiplexer_35_out0, in_2
  // Buzzer buzzer_135: pin names not known; wires that end beside it: rom_36_data, demultiplexer_36_out0, in_2
  // Buzzer #(.waveform("Triangle")) buzzer_136: pin names not known; wires that end beside it: rom_34_data, demultiplexer_34_out2, in_2
  // Buzzer #(.waveform("Square")) buzzer_137: pin names not known; wires that end beside it: rom_34_data, demultiplexer_34_out1, in_2
  // Buzzer #(.waveform("Triangle")) buzzer_138: pin names not known; wires that end beside it: rom_35_data, demultiplexer_35_out2, in_2
  // Buzzer #(.waveform("Square")) buzzer_139: pin names not known; wires that end beside it: rom_35_data, demultiplexer_35_out1, in_2
  // Buzzer #(.waveform("Triangle")) buzzer_140: pin names not known; wires that end beside it: rom_36_data, demultiplexer_36_out2, in_2
  // Buzzer #(.waveform("Square")) buzzer_141: pin names not known; wires that end beside it: rom_36_data, demultiplexer_36_out1, in_2
  // Buzzer #(.waveform("Sawtooth")) buzzer_142: pin names not known; wires that end beside it: rom_34_data, demultiplexer_34_out3, in_2
  // Buzzer #(.waveform("Sawtooth")) buzzer_143: pin names not known; wires that end beside it: rom_35_data, demultiplexer_35_out3, in_2
  // Buzzer #(.waveform("Sawtooth")) buzzer_144: pin names not known; wires that end beside it: rom_36_data, demultiplexer_36_out3, in_2

  // Notes on the sheet:
  //   contents of rom_1 (hex, n*v repeats v):
  //   2c 2d 2e 30 31 32 34 35 37 39 3a 3c 3e 40 41 43
  //   contents of rom_2 (hex, n*v repeats v):
  //   57 5a 5c 5f 62 65 68 6b 6e 71 75 78 7b 7f 83 87
  //   contents of rom_3 (hex, n*v repeats v):
  //   af b4 b9 be c4 ca d0 d6 dc e2 e9 f0 f7 fe 106 10d
  //   contents of rom_4 (hex, n*v repeats v):
  //   2e 30 31 32 34 35 37 39 3a 3c 3e 40 41 43 45 47
  //   contents of rom_5 (hex, n*v repeats v):
  //   5c 5f 62 65 68 6b 6e 71 75 78 7b 7f 83 87 8b 8f
  //   contents of rom_6 (hex, n*v repeats v):
  //   b9 be c4 ca d0 d6 dc e2 e9 f0 f7 fe 106 10d 115 11d
  //   contents of rom_7 (hex, n*v repeats v):
  //   31 32 34 35 37 39 3a 3c 3e 40 41 43 45 47 49 4c
  //   contents of rom_8 (hex, n*v repeats v):
  //   62 65 68 6b 6e 71 75 78 7b 7f 83 87 8b 8f 93 97
  //   contents of rom_9 (hex, n*v repeats v):
  //   c4 ca d0 d6 dc e2 e9 f0 f7 fe 106 10d 115 11d 126 12e
  //   contents of rom_10 (hex, n*v repeats v):
  //   34 35 37 39 3a 3c 3e 40 41 43 45 47 49 4c 4e 50
  //   contents of rom_11 (hex, n*v repeats v):
  //   68 6b 6e 71 75 78 7b 7f 83 87 8b 8f 93 97 9c a0
  //   contents of rom_12 (hex, n*v repeats v):
  //   d0 d6 dc e2 e9 f0 f7 fe 106 10d 115 11d 126 12e 137 140
  //   contents of rom_13 (hex, n*v repeats v):
  //   37 39 3a 3c 3e 40 41 43 45 47 49 4c 4e 50 52 55
  //   contents of rom_14 (hex, n*v repeats v):
  //   6e 71 75 78 7b 7f 83 87 8b 8f 93 97 9c a0 a5 aa
  //   contents of rom_15 (hex, n*v repeats v):
  //   dc e2 e9 f0 f7 fe 106 10d 115 11d 126 12e 137 140 14a 153
  //   contents of rom_16 (hex, n*v repeats v):
  //   3a 3c 3e 40 41 43 45 47 49 4c 4e 50 52 55 57 5a
  //   contents of rom_17 (hex, n*v repeats v):
  //   75 78 7b 7f 83 87 8b 8f 93 97 9c a0 a5 aa af b4
  //   contents of rom_18 (hex, n*v repeats v):
  //   e9 f0 f7 fe 106 10d 115 11d 126 12e 137 140 14a 153 15d 167
  //   contents of rom_19 (hex, n*v repeats v):
  //   3e 40 41 43 45 47 49 4c 4e 50 52 55 57 5a 5c 5f
  //   contents of rom_20 (hex, n*v repeats v):
  //   7b 7f 83 87 8b 8f 93 97 9c a0 a5 aa af b4 b9 be
  //   contents of rom_21 (hex, n*v repeats v):
  //   f7 fe 106 10d 115 11d 126 12e 137 140 14a 153 15d 167 172 17d
  //   contents of rom_22 (hex, n*v repeats v):
  //   41 43 45 47 49 4c 4e 50 52 55 57 5a 5c 5f 62 65
  //   contents of rom_23 (hex, n*v repeats v):
  //   83 87 8b 8f 93 97 9c a0 a5 aa af b4 b9 be c4 ca
  //   contents of rom_24 (hex, n*v repeats v):
  //   106 10d 115 11d 126 12e 137 140 14a 153 15d 167 172 17d 188 193
  //   contents of rom_25 (hex, n*v repeats v):
  //   45 47 49 4c 4e 50 52 55 57 5a 5c 5f 62 65 68 6b
  //   contents of rom_26 (hex, n*v repeats v):
  //   8b 8f 93 97 9c a0 a5 aa af b4 b9 be c4 ca d0 d6
  //   contents of rom_27 (hex, n*v repeats v):
  //   115 11d 126 12e 137 140 14a 153 15d 167 172 17d 188 193 19f 1ab
  //   contents of rom_28 (hex, n*v repeats v):
  //   49 4c 4e 50 52 55 57 5a 5c 5f 62 65 68 6b 6e 71
  //   contents of rom_29 (hex, n*v repeats v):
  //   93 97 9c a0 a5 aa af b4 b9 be c4 ca d0 d6 dc e2
  //   contents of rom_30 (hex, n*v repeats v):
  //   126 12e 137 140 14a 153 15d 167 172 17d 188 193 19f 1ab 1b8 1c5
  //   contents of rom_31 (hex, n*v repeats v):
  //   4e 50 52 55 57 5a 5c 5f 62 65 68 6b 6e 71 75 78
  //   contents of rom_32 (hex, n*v repeats v):
  //   9c a0 a5 aa af b4 b9 be c4 ca d0 d6 dc e2 e9 f0
  //   contents of rom_33 (hex, n*v repeats v):
  //   137 140 14a 153 15d 167 172 17d 188 193 19f 1ab 1b8 1c5 1d2 1e0
  //   contents of rom_34 (hex, n*v repeats v):
  //   52 55 57 5a 5c 5f 62 65 68 6b 6e 71 75 78 7b 7f
  //   contents of rom_35 (hex, n*v repeats v):
  //   a5 aa af b4 b9 be c4 ca d0 d6 dc e2 e9 f0 f7 fe
  //   contents of rom_36 (hex, n*v repeats v):
  //   14a 153 15d 167 172 17d 188 193 19f 1ab 1b8 1c5 1d2 1e0 1ee 1fc
endmodule

module Ear_Trainer_circ (
  input  Unison,
  input  mi2,
  input  Ma2,
  input  mi3,
  input  Ascending_Decending,
  input  Ma3,
  input  P4,
  input  Replay,
  input  Tritone,
  input  P5,
  input  mi6,
  input  Ma6,
  input  mi7,
  input  [6:0] Volume,
  input  Ma7,
  input  Octave,
  input  Reset_Score,
  output [7:0] Score
);

  wire and_1_out, and_2_out, clock_1_out, comparator_1_gt, comparator_2_eq, or_1_out, priority_encoder_1_gs,
       t_ff_1_q, t_ff_2_q, t_ff_3_qn, t_ff_4_qn;
  wire [0:0] multiplexer_1_out;
  wire [1:0] t_ff_3_q;
  wire [3:0] multiplexer_2_out, priority_encoder_1_out, rom_2_data;
  wire [7:0] adder_1_out;
  wire [13:0] random_1_out, rom_1_data;

  Clock clock_1 (.out(clock_1_out));
  or or_1 (or_1_out, Replay, priority_encoder_1_gs);
  T_Flip_Flop #(.trigger("falling")) t_ff_1 (
    .T(t_ff_2_q), .clk(clock_1_out), .Q(t_ff_1_q), .preset(or_1_out));  // open: Qn, reset
  Random #(.width(14)) random_1 (.clk(priority_encoder_1_gs), .out(random_1_out));  // open: clr, next
  T_Flip_Flop #(.trigger("falling")) t_ff_2 (.T(t_ff_1_q), .clk(clock_1_out), .Q(t_ff_2_q));  // open: Qn, reset, preset
  and and_1 (and_1_out, comparator_1_gt, 1'b1);
  T_Flip_Flop #(.trigger("falling")) t_ff_3 (
    .T(and_1_out), .clk(clock_1_out), .Q(t_ff_3_q[0]), .Qn(t_ff_3_qn), .reset(t_ff_2_q));  // open: preset
  T_Flip_Flop #(.trigger("falling")) t_ff_4 (
    .T(and_2_out), .clk(clock_1_out), .Q(t_ff_3_q[1]), .Qn(t_ff_4_qn), .reset(t_ff_2_q));  // open: preset
  and and_2 (and_2_out, 1'b1, t_ff_3_q[0]);
  Comparator #(.mode("unsigned"), .width(2)) comparator_1 (
    .a(2'b10), .b(t_ff_3_q), .gt(comparator_1_gt));  // open: eq, lt
  Multiplexer multiplexer_1 (.in0(t_ff_3_q[0]), .in1(t_ff_3_qn), .out(multiplexer_1_out[0]), .sel(Ascending_Decending));
  ROM #(.addrWidth(14), .dataWidth(14)) rom_1 (.addr({random_1_out[13:1], multiplexer_1_out[0]}), .data(rom_1_data));
  // Buzzer buzzer_1: pin names not known; wires that end beside it: rom_1_data, t_ff_4_qn, Volume
  ROM #(.addrWidth(14), .dataWidth(4)) rom_2 (.addr({random_1_out[13:1], multiplexer_1_out[0]}), .data(rom_2_data));
  Priority_Encoder #(.select(4)) priority_encoder_1 (
    .in0(Unison), .in1(mi2), .in2(Ma2), .in3(mi3), .in4(Ma3), .in5(P4), .in6(Tritone), .in7(P5), .in8(mi6),
    .in9(Ma6), .in10(mi7), .in11(Ma7), .in12(Octave), .in13(1'b0), .in14(1'b0), .in15(1'b0),
    .out(priority_encoder_1_out), .gs(priority_encoder_1_gs));  // open: en_out, en_in
  Multiplexer #(.width(4)) multiplexer_2 (
    .in0(4'b1100), .in1(priority_encoder_1_out), .out(multiplexer_2_out), .sel(priority_encoder_1_gs));
  Comparator #(.width(4)) comparator_2 (.a(multiplexer_2_out), .b(rom_2_data), .eq(comparator_2_eq));  // open: gt, lt
  Adder adder_1 (.a({8{1'b0}}), .b(Score), .out(adder_1_out), .cin(comparator_2_eq));  // open: cout
  Register #(.trigger("falling")) register_1 (
    .D(adder_1_out), .en(1'b1), .clk(comparator_2_eq), .Q(Score), .clr(Reset_Score));

  // Notes on the sheet:
  //   contents of rom_1 (hex, n*v repeats v):
  //   370 455 370 67d 575 8a9 417 527 20b 370 3dc 7b8 1d2 3a4 575 620 749 8a9 4dd 92d 455 4dd 620 c40 2e4
  //   4dd 5c8 b90 22a 26e 1b8 2ba 6e0 9b9 1b8 2e4 67d c40 24b 455 575 aea 82d aea 620 c40 a4d cfa 8a9 cfa
  //   455 620 417 67d 527 a4d 2e4 33f 497 6e0 24b 310 aea c40 749 7b8 370 527 5c8 7b8 22a 2ba 92d c40 1ee
  //   310 575 67d 310 575 20b 293 3a4 620 417 5c8 1b8 22a 749 82d 7b8 aea 575 67d 575 620 5c8 82d 1d2 2e4
  //   620 9b9 7b8 aea 749 aea 33f 370 310 3a4 575 8a9 749 9b9 749 cfa 455 82d 4dd 749 497 7b8 6e0 b90 455
  //   497 6e0 c40 7b8 a4d 575 9b9 26e 4dd 1ee 26e 3dc 575 33f 5c8 67d cfa 4dd 7b8 1b8 24b aea cfa 5c8 aea
  //   575 aea 3dc 67d 26e 3a4 4dd 9b9 82d 82d aea c40 527 9b9 3a4 749 8a9 b90 310 527 1d2 2e4 575 749 92d
  //   a4d 575 aea 497 5c8 293 497 4dd 8a9 3dc 497 3a4 749 4dd 620 4dd 7b8 293 497 1ee 310 527 8a9 82d aea
  //   6e0 b90 6e0 cfa 417 4dd 9b9 b90 575 82d 527 8a9 26e 33f 1d2 33f 6e0 9b9 20b 2ba 7b8 92d 2e4 575 67d
  //   7b8 20b 20b 67d b90 26e 370 8a9 aea b90 c40 455 82d 417 455 92d aea 67d 9b9 20b 2e4 20b 2e4 2ba 3a4
  //   24b 3dc 370 455 370 620 82d a4d 1d2 1ee 7b8 c40 3a4 5c8 417 5c8 1ee 3a4 6e0 82d 455 4dd 527 82d 24b
  //   417 3a4 5c8 7b8 cfa aea aea 417 455 575 8a9 67d a4d 527 82d 33f 3dc 3a4 4dd 33f 527 67d aea 417 5c8
  //   33f 455 6e0 b90 2e4 2e4 82d aea 1d2 22a 293 527 417 5c8 417 749 417 82d 455 82d 3dc 5c8 310 3dc 4dd
  //   67d 2e4 527 3a4 5c8 4dd 92d 9b9 cfa 293 455 7b8 b90 2e4 33f 1b8 1ee 22a 24b 2ba 33f 24b 24b 2e4 455
  //   92d c40 2ba 33f 22a 3dc 497 82d 22a 2ba cfa cfa 3a4 4dd 2ba 4dd 8a9 aea 1b8 370 1b8 2e4 2e4 3a4 2e4
  //   5c8 2ba 2ba 749 b90 92d 9b9 749 82d 82d b90 7b8 cfa 82d aea 6e0 7b8 92d b90 370 417 26e 455 82d 92d
  //   749 c40 455 7b8 417 4dd 22a 3a4 1ee 22a 417 527 1b8 310 5c8 a4d 33f 527 1b8 2e4 7b8 cfa 370 67d 310
  //   620 293 455 2e4 3a4 575 a4d 497 6e0 497 82d 497 8a9 7b8 cfa 417 417 24b 370 67d a4d 7b8 82d 67d 9b9
  //   22a 455 749 aea 527 575 497 67d 2ba 310 6e0 aea 4dd 67d 527 7b8 5c8 82d 6e0 b90 2ba 527 5c8 92d 370
  //   67d 497 620 6e0 9b9 1b8 1d2 26e 370 497 82d 1ee 24b 67d 92d 2e4 497 620 a4d 4dd 8a9 a4d b90 aea aea
  //   1ee 370 26e 2e4 92d c40 22a 3dc 1ee 3a4 2ba 33f 26e 370 575 8a9 497 92d 3dc 6e0 1b8 2e4 82d aea 20b
  //   2e4 26e 3dc 749 b90 aea b90 2ba 370 26e 2e4 a4d b90 497 575 4dd 82d 22a 2ba 82d c40 33f 3a4 6e0 aea
  //   455 527 575 7b8 497 749 1b8 24b 3dc 749 24b 455 527 8a9 24b 26e 527 8a9 2ba 417 6e0 6e0 aea cfa 9b9
  //   cfa 620 620 22a 24b 3dc 417 620 749 24b 2e4 4dd 620 b90 b90 82d 8a9 1d2 20b 749 7b8 575 67d 26e 4dd
  //   67d 92d 1b8 2ba 497 527 417 527 293 455 5c8 aea 3dc 7b8 527 82d 67d a4d 5c8 a4d 575 82d 26e 4dd 67d
  //   aea 1ee 1ee 575 92d 6e0 c40 67d b90 455 575 9b9 b90 417 417 310 417 5c8 9b9 527 67d 417 527 26e 2e4
  //   455 4dd 310 5c8 417 4dd 9b9 cfa 26e 2ba 575 9b9 620 c40 310 33f 1d2 26e 3dc 4dd 22a 2e4 575 8a9 4dd
  //   620 8a9 b90 aea b90 497 8a9 527 527 82d cfa 5c8 92d 620 b90 8a9 b90 6e0 b90 26e 4dd 3a4 4dd 92d c40
  //   310 455 527 6e0 749 c40 293 417 67d 7b8 3a4 4dd 5c8 5c8 6e0 92d 749 8a9 417 6e0 575 6e0 24b 2ba 370
  //   67d 1d2 293 92d c40 455 8a9 92d b90 1ee 3dc 4dd 749 575 aea 24b 310 620 92d 455 455 620 9b9 370 527
  //   2e4 33f 9b9 cfa 3a4 3dc 620 92d 2e4 497 1d2 20b 6e0 8a9 24b 2ba 20b 310 67d cfa 293 455 20b 293 b90
  //   c40 92d cfa 1b8 2e4 4dd 8a9 67d 8a9 293 527 20b 3a4 310 33f 3dc 749 33f 3dc 67d a4d a4d a4d 4dd 7b8
  //   620 67d 2ba 417 370 6e0 5c8 82d 620 a4d 6e0 8a9 2ba 2ba 82d c40 1d2 20b 92d b90 5c8 aea 20b 24b 6e0
  //   6e0 1d2 24b 26e 4dd 2e4 370 620 7b8 310 3dc 20b 417 82d 82d 9b9 aea 3dc 417 6e0 c40 370 3a4 749 cfa
  //   370 3a4 370 620 575 575 2ba 370 2e4 497 92d b90 33f 67d 1ee 26e 9b9 cfa 9b9 b90 4dd 8a9 2ba 2ba 6e0
  //   9b9 20b 370 8a9 a4d 749 b90 5c8 82d 2ba 3a4 20b 417 8a9 cfa 1b8 1b8 5c8 92d 20b 3dc 497 92d 5c8 b90
  //   293 497 3a4 749 20b 370 8a9 cfa 2ba 3dc 4dd 9b9 575 aea 4dd 67d 3dc 749 cfa cfa 749 a4d 67d cfa 67d
  //   aea 67d 9b9 293 2e4 2e4 3dc 3dc 749 575 749 a4d cfa 293 33f 67d aea 293 417 24b 455 417 417 3a4 620
  //   3a4 620 82d 92d 24b 2e4 575 9b9 620 7b8 22a 3dc 92d b90 26e 2ba c40 cfa 20b 2e4 417 455 67d aea 20b
  //   22a 1d2 33f 1d2 1ee 20b 3dc 33f 497 20b 22a 20b 2e4 26e 26e 82d aea 417 7b8 310 3dc 67d 92d 749 92d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
  //   contents of rom_2 (hex, n*v repeats v):
  //   4 4 b b 8 8 4 4 9 9 4*c 2 2 3 3 b b 2 2 c c 9 9 c c 2 2 8 8 6 6 9 9 4*b c c 5 5 c c 4 4 7 7 6 6 8 8
  //   c c 2 2 7 7 5 5 2 2 1 1 7 7 5 5 4 4 5 5 8 8 3 3 a a 4 4 9 9 6 6 4 4 2 2 6 6 3 3 2 2 6 6 4*8 6 6 7 7
  //   1 1 3 3 8 8 5 5 a a b b 7 7 4*9 1 1 a a 5 5 a a c c 4 4 6 6 a a c c 8 8 5 5 3 3 b b c c 9 9 7 7 c c
  //   0 0 2 2 b b c c 5 5 9 9 8 8 5 5 2 2 c c 4 4 4*a 3 3 c c 4 4 8 8 a a 8 8 9 9 5 5 9 9 b b 4*3 7 7 9 9
  //   5 5 a a 6 6 5 5 3 3 b b 3 3 0 0 a a 6 6 4 4 1 1 b b 1 1 3 3 7 7 4*6 5 5 9 9 4 4 a a 4 4 1 1 4*8 6 6
  //   b b 3 3 2 2 8 8 a a 8 8 9 9 0 0 1 1 6*8 3 3 5 5 8 8 9 9 6 6 5 5 9 9 0 0 5 5 3 3 c c 6 6 a a c c b b
  //   7 7 4 4 5 5 a a 8 8 b b 5 5 9 9 7 7 4*2 1 1 3 3 0 0 7 7 5 5 3 3 4*a 4 4 0 0 5 5 a a 4 4 c c 9 9 4 4
  //   c c 0 0 8 8 1 1 2 2 6 6 9 9 5 5 2 2 4 4 3 3 a a 2 2 9 9 a a 3 3 9 9 2 2 4 4 4*a 8 8 4*9 b b c c 9 9
  //   4 4 b b 7 7 a a b b 9 9 0 0 7 7 8 8 1 1 7 7 c c 7 7 1 1 6 6 2 2 8 8 5 5 7 7 6 6 9 9 b b 8 8 b b 5 5
  //   6 6 1 1 6 6 a a 3 3 6 6 8 8 9 9 a a 2 2 0 0 a a 3 3 5 5 a a b b 3 3 6 6 8 8 c c a a 9 9 5 5 6 6 4*8
  //   1 1 4 4 3 3 2 2 3 3 9 9 4 4 7 7 2 2 8 8 3 3 6 6 8 8 5 5 4*b 9 9 1 1 9 9 7 7 0 0 3 3 5 5 0 0 4*1 3 3
  //   4*4 0 0 1 1 2 2 1 1 3 3 c c 6 6 8 8 2 2 4 4 9 9 b b c c 4*8 a a 7 7 c c 9 9 0 0 9 9 4*a 4 4 3 3 0 0
  //   5 5 9 9 4*4 3 3 2 2 b b 3 3 5 5 2 2 a a c c 1 1 5 5 4 4 5 5 8 8 4 4 5 5 1 1 b b 0 0 4*8 b b 5 5 9 9
  //   c c 4*5 6 6 5 5 9 9 8 8 3 3 5 5 0 0 5 5 3 3 9 9 4 4 3 3 b b 6 6 5 5 c c 4 4 c c 7 7 c c 5 5 7 7 0 0
  //   8 8 7 7 2 2 5 5 1 1 7 7 8 8 2 2 4 4 3 3 7 7 c c 9 9 4 4 1 1 6 6 9 9 a a 5 5 c c a a 1 1 b b 3 3 8 8
  //   0 0 8 8 1 1 7 7 c c 6 6 9 9 4 4 0 0 7 7 2 2 4 4 b b 2 2 0 0 4 4 c c 3 3 4*4 c c 0 0 2 2 1 1 a a 1 1
  //   a a 1 1 a a 0 0 4 4 8 8 4 4 c c 4 4 5 5 3 3 a a 0 0 6 6 9 9 3 3 8 8 6 6 5 5 c c 7 7 0 0 8 8 b b 4*c
  //   a a c c 9 9 7 7 6 6 4*c 5 5 b b 0 0 6 6 c c 9 9 7 7 2 2 5 5 b b 5 5 4*4 9 9 8 8 b b 0 0 4*9 2 2 4 4
  //   a a 4 4 a a 4 4 2 2 1 1 6 6 1 1 9 9 1 1 a a 1 1 b b 6 6 1 1 6 6 0 0 5 5 b b 4 4 6 6 4 4 9 9 4*b 2 2
  //   7 7 3 3 c c 2 2 4 4 c c 8 8 2 2 0 0 3 3 b b 9 9 2 2 3 3 4 4 2 2 9 9 5 5 7 7 6 6 5 5 c c 2 2 1 1 8 8
  //   6 6 5 5 4 4 0 0 b b 6 6 c c b b 4 4 4*1 0 0 4 4 3 3 5 5 1 1 6 6 a a 9 9 a a 0 0 b b 4 4 5 5 8 8 c c
  //   b b 9 9 5 5 b b 2 2 8 8 6 6 4 4 3 3 5 5 0 0 a a 8 8 3 3 6 6 2 2 4 4 2 2 a a 5 5 4 4 4*0 8 8 5 5 c c
  //   a a b b c c b b 0 0 2 2 a a 0 0 c c 4 4 2 2 7 7 4*9 a a 8 8 2 2 b b 9 9 c c 3 3 4 4 c c 2 2 5 5 7 7
  //   8 8 a a b b c c 7 7 0 0 c c a a 8 8 5 5 3 3 a a c c 5 5 6 6 4 4 0 0 5 5 0 0 3 3 c c b b 3 3 b b 7 7
  //   1 1 c c 9 9 1 1 a a 1 1 7 7 4*6 7 7 3 3 1 1 3 3 1 1 3 3 7 7 4 4 0 0 1 1 a a 5 5 9 9 6 6 7 7 4 4 b b
  //   4 4 1 1 5 5 8 8 3 3 4 4 4*1 8 8 b b 8 8 c c 5 5 4*9 8 8 4*b 1 1 7 7 3 3 7 7 3 3 0 0 a a 8 8 0 0 b b
  //   9 9 7 7 5 5 2 2 a a 6 6 8 8 2 2 7 7 5 5 3 3 6*2 1 1 5 5 0 0 6 6 5 5 4*7 9 9 c c 6 6 4*a 3 3 1 1 5 5
  //   4 4 7 7 a a 6 6 b b 8 8 2 2 8 8 b b 5 5 4*3 4 4 6 6 b b 8 8 0 0 3 3 b b 8 8 0 0 2 2 4 4 2 2 0 0 4*6
  //   3 3 8 8 2 2 b b 1 1 c c 5 5 0 0 b b 4 4 2 2 b b 0 0 1 1 c c 4 4 1 1 4 4 4*9 6 6 4*5 3 3 5 5 4*0 4 4
  //   8 8 2 2 7 7 b b 1 1 7 7 4 4 3 3 5 5 1 1 5 5 2 2 a a 4*c 8 8 1 1 8 8 b b 5 5 9 9 7 7 0 0 b b a a 5 5
  //   9 9 3 3 4 4 1 1 9 9 6 6 3 3 a a c c 9 9 4 4 3 3 4*6 9 9 3 3 1 1 9 9 4*c 1 1 2 2 a a 1 1 7 7 4*9 a a
  //   b b 4 4 a a c c 5 5 6 6 b b c c 5 5 4 4 1 1 9 9 3 3 9 9 6 6 3 3 5 5 7 7 4 4 7 7 c c 4*4 7 7 3 3 4*c
  //   2 2 b b c c 4*6 b b 0 0 3 3 1 1 a a 0 0 8 8 4*1 c c 3 3 a a 3 3 6 6 b b 3 3 4*a 3 3 c c b b a a 1 1
  //   4 4 8 8 b b 6 6 3 3 9 9 c c 6 6 9 9 8 8 0 0 3 3 2 2 0 0 1 1 2 2 5 5 0 0 5 5 6 6 8 8 2 2 4 4 3 3 4*4
  //   0 0 4 4 3 3 c c 8 8 1 1 3 3 9 9 5 5 1 1 a a 3 3 8 8 7 7 a a 4*4 7 7 4 4 b b a a 8 8 c c 3 3 9 9 a a
  //   4*6 5 5 2 2 c c 4 4 8 8 6 6 a a b b 3 3 a a 0 0 6 6 1 1 2 2 9 9 b b 3 3 1 1 9 9 4 4 b b c c 8 8 4 4
  //   0 0 5 5 9 9 8 8 6 6 1 1 4*6 9 9 7 7 0 0 b b 0 0 a a 6 6 a a 5 5 4*2 b b 6 6 b b 4*5 b b 0 0 a a 9 9
  //   7 7 9 9 4*b 6 6 8 8 0 0 a a 6 6 9 9 8 8 3 3 b b 4 4 9 9 4*6 b b 2 2 c c a a 9 9 7 7 6 6 7 7 4 4 2 2
  //   7 7 9 9 c c 4 4 8 8 7 7 a a 3 3 c c 4*8 4*5 a a 2 2 9 9 6 6 9 9 0 0 7 7 1 1 9 9 c c b b c c 2 2 5 5
  //   9 9 a a 7 7 b b 3 3 8 8 a a 0 0 7 7 9 9 4*8 2 2 7 7 6 6 b b 1 1 6 6 9 9 a a 0 0 b b 5 5 1 1 2 2 a a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
endmodule

module Note_Trainer_circ (
  input  C,
  input  Db,
  input  D,
  input  Eb,
  input  E,
  input  F,
  input  Gb,
  input  G,
  input  Ab,
  input  A,
  input  [6:0] Volume,
  input  Bb,
  input  B,
  input  Reset_Score,
  output C2,
  output C3,
  output C4,
  output C5,
  output C6,
  output Db2,
  output Db3,
  output Db4,
  output Db5,
  output D2,
  output D3,
  output D4,
  output D5,
  output Eb2,
  output Eb3,
  output Eb4,
  output Eb5,
  output E2,
  output E3,
  output E4,
  output E5,
  output F2,
  output F3,
  output F4,
  output F5,
  output Gb2,
  output Gb3,
  output Gb4,
  output Gb5,
  output G2,
  output G3,
  output G4,
  output G5,
  output Ab2,
  output Ab3,
  output Ab4,
  output Ab5,
  output A2,
  output A3,
  output A4,
  output A5,
  output Bb2,
  output Bb3,
  output Bb4,
  output Bb5,
  output B2,
  output B3,
  output B4,
  output B5,
  output [7:0] Score
);

  wire and_1_out, and_14_out, and_27_out, and_40_out, clock_1_out, comparator_1_eq, demultiplexer_1_out0,
       demultiplexer_1_out1, demultiplexer_1_out2, demultiplexer_1_out3, demultiplexer_1_out4,
       demultiplexer_1_out5, demultiplexer_1_out6, demultiplexer_1_out7, demultiplexer_1_out8,
       demultiplexer_1_out9, demultiplexer_1_out10, demultiplexer_1_out11, not_1_out, not_2_out, not_3_out,
       priority_encoder_1_gs, t_ff_1_q, t_ff_2_q;
  wire [3:0] multiplexer_1_out, priority_encoder_1_out;
  wire [5:0] divider_1_rem, divider_2_out, divider_2_rem, random_1_out, rom_2_data;
  wire [7:0] adder_1_out;
  wire [13:0] rom_1_data;

  Random #(.width(6)) random_1 (.clk(priority_encoder_1_gs), .out(random_1_out));  // open: clr, next
  Clock clock_1 (.out(clock_1_out));
  T_Flip_Flop t_ff_1 (
    .T(t_ff_2_q), .clk(clock_1_out), .Q(t_ff_1_q), .preset(priority_encoder_1_gs));  // open: Qn, reset
  Divider #(.width(6)) divider_1 (.a(random_1_out), .b(6'b110001), .rem(divider_1_rem));  // open: out, upper
  ROM #(.addrWidth(6), .dataWidth(14)) rom_1 (.addr(divider_1_rem), .data(rom_1_data));
  T_Flip_Flop t_ff_2 (.T(t_ff_1_q), .clk(clock_1_out), .Q(t_ff_2_q));  // open: Qn, reset, preset
  // Buzzer buzzer_1: pin names not known; wires that end beside it: rom_1_data, t_ff_2_q, Volume
  ROM #(.addrWidth(6), .dataWidth(6)) rom_2 (.addr(divider_1_rem), .data(rom_2_data));
  Divider #(.width(6)) divider_2 (
    .a(rom_2_data), .b(6'b001100), .out(divider_2_out), .rem(divider_2_rem));  // open: upper
  Priority_Encoder #(.select(4)) priority_encoder_1 (
    .in0(C), .in1(Db), .in2(D), .in3(Eb), .in4(E), .in5(F), .in6(Gb), .in7(G), .in8(Ab), .in9(A), .in10(Bb),
    .in11(B), .in12(1'b0), .in13(1'b0), .in14(1'b0), .in15(1'b0), .out(priority_encoder_1_out),
    .gs(priority_encoder_1_gs));  // open: en_out, en_in
  Comparator #(.width(4)) comparator_1 (
    .a(multiplexer_1_out), .b(divider_2_rem[3:0]), .eq(comparator_1_eq));  // open: gt, lt
  Multiplexer #(.width(4)) multiplexer_1 (
    .in0(4'b1111), .in1(priority_encoder_1_out), .out(multiplexer_1_out), .sel(priority_encoder_1_gs));
  Adder adder_1 (.a({8{1'b0}}), .b(Score), .out(adder_1_out), .cin(comparator_1_eq));  // open: cout
  Demultiplexer #(.select(4)) demultiplexer_1 (
    .out0(demultiplexer_1_out0), .out1(demultiplexer_1_out1), .out2(demultiplexer_1_out2),
    .out3(demultiplexer_1_out3), .out4(demultiplexer_1_out4), .out5(demultiplexer_1_out5),
    .out6(demultiplexer_1_out6), .out7(demultiplexer_1_out7), .out8(demultiplexer_1_out8),
    .out9(demultiplexer_1_out9), .out10(demultiplexer_1_out10), .out11(demultiplexer_1_out11), .in(1'b1),
    .sel(divider_2_rem[3:0]));  // open: out12, out13, out14, out15
  Register #(.trigger("falling")) register_1 (
    .D(adder_1_out), .en(1'b1), .clk(comparator_1_eq), .Q(Score), .clr(Reset_Score));
  and and_1 (and_1_out, not_1_out, not_2_out);
  not not_1 (not_1_out, divider_2_out[0]);
  and and_2 (C2, demultiplexer_1_out0, and_1_out);
  and and_3 (Db2, demultiplexer_1_out1, and_1_out);
  and and_4 (D2, demultiplexer_1_out2, and_1_out);
  and and_5 (Eb2, demultiplexer_1_out3, and_1_out);
  and and_6 (E2, demultiplexer_1_out4, and_1_out);
  and and_7 (F2, demultiplexer_1_out5, and_1_out);
  and and_8 (Gb2, demultiplexer_1_out6, and_1_out);
  and and_9 (G2, demultiplexer_1_out7, and_1_out);
  and and_10 (Ab2, demultiplexer_1_out8, and_1_out);
  and and_11 (A2, demultiplexer_1_out9, and_1_out);
  and and_12 (Bb2, demultiplexer_1_out10, and_1_out);
  and and_13 (B2, demultiplexer_1_out11, and_1_out);
  not not_2 (not_2_out, divider_2_out[1]);
  and and_14 (and_14_out, divider_2_out[0], not_2_out);
  and and_15 (C3, demultiplexer_1_out0, and_14_out);
  and and_16 (Db3, demultiplexer_1_out1, and_14_out);
  and and_17 (D3, demultiplexer_1_out2, and_14_out);
  and and_18 (Eb3, demultiplexer_1_out3, and_14_out);
  and and_19 (E3, demultiplexer_1_out4, and_14_out);
  and and_20 (F3, demultiplexer_1_out5, and_14_out);
  and and_21 (Gb3, demultiplexer_1_out6, and_14_out);
  and and_22 (G3, demultiplexer_1_out7, and_14_out);
  and and_23 (Ab3, demultiplexer_1_out8, and_14_out);
  and and_24 (A3, demultiplexer_1_out9, and_14_out);
  and and_25 (Bb3, demultiplexer_1_out10, and_14_out);
  and and_26 (B3, demultiplexer_1_out11, and_14_out);
  and and_27 (and_27_out, not_3_out, divider_2_out[1]);
  not not_3 (not_3_out, divider_2_out[0]);
  and and_28 (C4, demultiplexer_1_out0, and_27_out);
  and and_29 (Db4, demultiplexer_1_out1, and_27_out);
  and and_30 (D4, demultiplexer_1_out2, and_27_out);
  and and_31 (Eb4, demultiplexer_1_out3, and_27_out);
  and and_32 (E4, demultiplexer_1_out4, and_27_out);
  and and_33 (F4, demultiplexer_1_out5, and_27_out);
  and and_34 (Gb4, demultiplexer_1_out6, and_27_out);
  and and_35 (G4, demultiplexer_1_out7, and_27_out);
  and and_36 (Ab4, demultiplexer_1_out8, and_27_out);
  and and_37 (A4, demultiplexer_1_out9, and_27_out);
  and and_38 (Bb4, demultiplexer_1_out10, and_27_out);
  and and_39 (B4, demultiplexer_1_out11, and_27_out);
  and and_40 (and_40_out, divider_2_out[0], divider_2_out[1]);
  and and_41 (C5, demultiplexer_1_out0, and_40_out);
  and and_42 (Db5, demultiplexer_1_out1, and_40_out);
  and and_43 (D5, demultiplexer_1_out2, and_40_out);
  and and_44 (Eb5, demultiplexer_1_out3, and_40_out);
  and and_45 (E5, demultiplexer_1_out4, and_40_out);
  and and_46 (F5, demultiplexer_1_out5, and_40_out);
  and and_47 (Gb5, demultiplexer_1_out6, and_40_out);
  and and_48 (G5, demultiplexer_1_out7, and_40_out);
  and and_49 (Ab5, demultiplexer_1_out8, and_40_out);
  and and_50 (A5, demultiplexer_1_out9, and_40_out);
  and and_51 (Bb5, demultiplexer_1_out10, and_40_out);
  and and_52 (B5, demultiplexer_1_out11, and_40_out);
  and and_53 (C6, demultiplexer_1_out0, divider_2_out[2]);

  // Notes on the sheet:
  //   contents of rom_1 (hex, n*v repeats v):
  //   41 45 49 4e 52 57 5c 62 68 6e 75 7b 83 8b 93 9c a5 af b9 c4 d0 dc e9 f7 106 115 126 137 14a 15d 172
  //   188 19f 1b8 1d2 1ee 20b 22a 24b 26e 293 2ba 2e4 310 33f 370 3a4 3dc 416
  //   contents of rom_2 (hex, n*v repeats v):
  //   0 1 2 3 4 5 6 7 8 9 a b c d e f 10 11 12 13 14 15 16 17 18 19 1a 1b 1c 1d 1e 1f 20 21 22 23 24 25 26
  //   27 28 29 2a 2b 2c 2d 2e 2f 30
endmodule
module Game (
  input  Ascending_Descending,
  input  [6:0] Volume,
  input  [1:0] in_3,
  output [7:0] out_4,
  output [7:0] Score
);

  wire A_out, Ab_out, B_out, Bb_out, button_1_out, button_2_out, button_3_out, button_4_out, button_5_out,
       button_6_out, button_7_out, button_8_out, button_9_out, button_10_out, button_11_out, button_12_out,
       button_13_out, button_14_out, button_15_out, button_16_out, button_17_out, button_18_out,
       button_19_out, button_20_out, button_21_out, button_22_out, button_23_out, button_24_out,
       button_25_out, button_26_out, button_27_out, button_28_out, button_29_out, button_30_out,
       button_31_out, button_32_out, button_33_out, button_34_out, button_35_out, button_36_out,
       button_37_out, button_38_out, button_39_out, button_40_out, button_41_out, button_42_out,
       button_43_out, button_44_out, button_45_out, button_46_out, button_47_out, button_48_out,
       button_49_out, button_50_out, button_51_out, button_52_out, button_53_out, button_54_out,
       button_55_out, button_56_out, button_57_out, button_58_out, button_59_out, button_60_out,
       button_61_out, button_62_out, button_63_out, button_64_out, button_65_out, button_66_out,
       button_67_out, button_68_out, button_69_out, button_70_out, button_71_out, button_72_out,
       button_73_out, button_74_out, button_75_out, button_76_out, button_77_out, button_78_out,
       button_79_out, button_80_out, button_81_out, button_82_out, button_83_out, button_84_out,
       button_85_out, button_86_out, button_87_out, button_88_out, button_89_out, button_90_out,
       button_91_out, button_92_out, button_93_out, button_94_out, button_95_out, button_96_out,
       button_97_out, button_98_out, button_99_out, button_100_out, button_101_out, button_102_out,
       button_103_out, button_104_out, button_105_out, button_106_out, button_107_out, button_108_out, C_out,
       D_out, Db_out, E_out, Eb_out, F_out, G_out, Gb_out, Ma2_out, Ma3_out, Ma6_out, Ma7_out, mi2_out,
       mi3_out, mi6_out, mi7_out, Oct_out, P4_out, P5_out, Replay_out, Reset_Score_out, rgbled_1_p1,
       rgbled_1_p2, rgbled_2_p1, rgbled_3_p1, rgbled_3_p2, rgbled_4_p1, rgbled_4_p2, rgbled_5_p1,
       rgbled_6_p1, rgbled_6_p2, rgbled_7_p1, rgbled_8_p1, rgbled_9_p1, rgbled_9_p2, rgbled_10_p1,
       rgbled_10_p2, rgbled_11_p1, rgbled_11_p2, rgbled_12_p1, rgbled_13_p1, rgbled_13_p2, rgbled_14_p1,
       rgbled_14_p2, rgbled_15_p1, rgbled_15_p2, rgbled_16_p1, rgbled_17_p1, rgbled_17_p2, rgbled_18_p1,
       rgbled_18_p2, rgbled_19_p1, rgbled_20_p1, rgbled_20_p2, rgbled_21_p1, rgbled_21_p2, rgbled_22_p1,
       rgbled_23_p1, rgbled_23_p2, rgbled_24_p1, rgbled_24_p2, rgbled_25_p1, rgbled_26_p1, rgbled_26_p2,
       rgbled_27_p1, rgbled_28_p1, rgbled_28_p2, rgbled_29_p1, rgbled_29_p2, Tritone_out, Unison_out;

  Button button_1 (.out(button_1_out));
  Button button_2 (.out(button_2_out));
  Button Replay (.out(Replay_out));
  Button button_3 (.out(button_3_out));
  Button button_4 (.out(button_4_out));
  Button button_5 (.out(button_5_out));
  Button button_6 (.out(button_6_out));
  Button Unison (.out(Unison_out));
  Button button_7 (.out(button_7_out));
  Button button_8 (.out(button_8_out));
  Button button_9 (.out(button_9_out));
  Button button_10 (.out(button_10_out));
  Button mi2 (.out(mi2_out));
  Button Ma2 (.out(Ma2_out));
  Synth_12TET_8_Octaves synth_12tet_8_octaves_1 (
    .in_17(button_16_out), .in_5(button_6_out), .in_29(button_28_out), .in_41(button_40_out),
    .in_53(button_52_out), .in_65(button_64_out), .in_77(button_76_out), .in_89(button_88_out),
    .in_101(button_100_out), .A1(button_14_out), .A0(button_2_out), .A2(button_26_out), .A3(button_38_out),
    .A4(button_49_out), .A5(button_62_out), .A6(button_74_out), .A7(button_86_out), .A8(button_98_out),
    .in_18(button_17_out), .in_6(button_4_out), .in_30(button_29_out), .in_42(button_41_out),
    .in_54(button_53_out), .in_66(button_65_out), .in_78(button_77_out), .in_90(button_89_out),
    .in_102(button_101_out), .Waveform(in_3), .in_19(button_15_out), .in_7(button_3_out),
    .in_31(button_27_out), .in_43(button_39_out), .in_55(button_51_out), .in_67(button_63_out),
    .in_79(button_75_out), .in_91(button_87_out), .in_103(button_99_out), .in_20(button_18_out),
    .in_8(button_5_out), .in_32(button_30_out), .in_44(button_42_out), .in_56(button_54_out),
    .in_68(button_66_out), .in_80(button_78_out), .in_92(button_90_out), .in_104(button_102_out),
    .in_21(button_19_out), .in_9(button_7_out), .in_33(button_31_out), .in_45(button_43_out),
    .in_57(button_55_out), .in_69(button_67_out), .in_81(button_79_out), .in_93(button_91_out),
    .in_105(button_103_out), .in_22(button_21_out), .in_10(button_9_out), .in_34(button_33_out),
    .in_46(button_45_out), .in_58(button_57_out), .in_70(button_69_out), .in_82(button_81_out),
    .in_94(button_93_out), .in_106(button_105_out), .in_23(button_22_out), .in_11(button_10_out),
    .in_35(button_34_out), .in_47(button_46_out), .in_59(button_58_out), .in_71(button_70_out),
    .in_83(button_82_out), .in_95(button_94_out), .in_107(button_106_out), .Volume(Volume),
    .in_24(button_20_out), .in_12(button_8_out), .in_36(button_32_out), .in_48(button_44_out),
    .in_60(button_56_out), .in_72(button_68_out), .in_84(button_80_out), .in_96(button_92_out),
    .in_108(button_104_out), .in_25(button_25_out), .in_13(button_13_out), .in_37(button_37_out),
    .in_49(button_50_out), .in_61(button_61_out), .in_73(button_73_out), .in_85(button_85_out),
    .in_97(button_97_out), .in_109(button_108_out), .in_26(button_23_out), .in_14(button_11_out),
    .in_38(button_35_out), .in_50(button_48_out), .in_62(button_59_out), .in_74(button_71_out),
    .in_86(button_83_out), .in_98(button_95_out), .in_110(button_107_out), .in_16(button_12_out),
    .in_4(button_1_out), .in_28(button_24_out), .in_40(button_36_out), .in_52(button_47_out),
    .in_64(button_60_out), .in_76(button_72_out), .in_88(button_84_out), .in_100(button_96_out));
  Button button_11 (.out(button_11_out));
  Button button_12 (.out(button_12_out));
  Button button_13 (.out(button_13_out));
  Button button_14 (.out(button_14_out));
  Button mi3 (.out(mi3_out));
  Button Ma3 (.out(Ma3_out));
  Button button_15 (.out(button_15_out));
  Button button_16 (.out(button_16_out));
  Button button_17 (.out(button_17_out));
  Button button_18 (.out(button_18_out));
  Button P4 (.out(P4_out));
  Button Tritone (.out(Tritone_out));
  Button button_19 (.out(button_19_out));
  Button button_20 (.out(button_20_out));
  Button button_21 (.out(button_21_out));
  Button button_22 (.out(button_22_out));
  Button P5 (.out(P5_out));
  Button mi6 (.out(mi6_out));
  Button button_23 (.out(button_23_out));
  Button button_24 (.out(button_24_out));
  Button button_25 (.out(button_25_out));
  Button button_26 (.out(button_26_out));
  Button Ma6 (.out(Ma6_out));
  Button mi7 (.out(mi7_out));
  Button button_27 (.out(button_27_out));
  Button button_28 (.out(button_28_out));
  Button button_29 (.out(button_29_out));
  Button button_30 (.out(button_30_out));
  Ear_Trainer_circ ear_trainer_circ_1 (
    .mi3(mi3_out), .Ma2(Ma2_out), .Ma7(Ma7_out), .mi2(mi2_out), .Unison(Unison_out), .Octave(Oct_out),
    .Reset_Score(Reset_Score_out), .Replay(Replay_out), .Volume(Volume),
    .Ascending_Decending(Ascending_Descending), .Ma6(Ma6_out), .Tritone(Tritone_out), .P5(P5_out),
    .mi6(mi6_out), .P4(P4_out), .mi7(mi7_out), .Ma3(Ma3_out), .Score(Score));
  Button Ma7 (.out(Ma7_out));
  Button Oct (.out(Oct_out));
  Button button_31 (.out(button_31_out));
  Button button_32 (.out(button_32_out));
  Button button_33 (.out(button_33_out));
  Button button_34 (.out(button_34_out));
  Button button_35 (.out(button_35_out));
  Button button_36 (.out(button_36_out));
  Button button_37 (.out(button_37_out));
  Button button_38 (.out(button_38_out));
  Button button_39 (.out(button_39_out));
  Button button_40 (.out(button_40_out));
  Button button_41 (.out(button_41_out));
  Button button_42 (.out(button_42_out));
  Button button_43 (.out(button_43_out));
  Button button_44 (.out(button_44_out));
  Button button_45 (.out(button_45_out));
  Button button_46 (.out(button_46_out));
  Button Reset_Score (.out(Reset_Score_out));
  Button button_47 (.out(button_47_out));
  Button button_48 (.out(button_48_out));
  Button button_49 (.out(button_49_out));
  Button button_50 (.out(button_50_out));
  Button button_51 (.out(button_51_out));
  Button button_52 (.out(button_52_out));
  Button button_53 (.out(button_53_out));
  Button button_54 (.out(button_54_out));
  // RGBLED rgbled_1: pin names not known; wires that end beside it: rgbled_1_p1, rgbled_1_p2
  // RGBLED rgbled_2: pin names not known; wires that end beside it: rgbled_2_p1
  // RGBLED rgbled_3: pin names not known; wires that end beside it: rgbled_3_p1, rgbled_3_p2
  // RGBLED rgbled_4: pin names not known; wires that end beside it: rgbled_4_p1, rgbled_4_p2
  // RGBLED rgbled_5: pin names not known; wires that end beside it: rgbled_5_p1
  // RGBLED rgbled_6: pin names not known; wires that end beside it: rgbled_6_p1, rgbled_6_p2
  // RGBLED rgbled_7: pin names not known; wires that end beside it: rgbled_7_p1
  // RGBLED rgbled_8: pin names not known; wires that end beside it: rgbled_8_p1
  Button Ab (.out(Ab_out));
  Button A (.out(A_out));
  Button Eb (.out(Eb_out));
  Button button_55 (.out(button_55_out));
  Button button_56 (.out(button_56_out));
  Button button_57 (.out(button_57_out));
  Button button_58 (.out(button_58_out));
  // RGBLED rgbled_9: pin names not known; wires that end beside it: rgbled_9_p1, rgbled_9_p2
  // RGBLED rgbled_10: pin names not known; wires that end beside it: rgbled_10_p1, rgbled_10_p2
  // RGBLED rgbled_11: pin names not known; wires that end beside it: rgbled_11_p1, rgbled_11_p2
  // RGBLED rgbled_12: pin names not known; wires that end beside it: rgbled_12_p1
  // RGBLED rgbled_13: pin names not known; wires that end beside it: rgbled_13_p1, rgbled_13_p2
  // RGBLED rgbled_14: pin names not known; wires that end beside it: rgbled_14_p1, rgbled_14_p2
  // RGBLED rgbled_15: pin names not known; wires that end beside it: rgbled_15_p1, rgbled_15_p2
  Button Bb (.out(Bb_out));
  Button B (.out(B_out));
  Button E (.out(E_out));
  Button F (.out(F_out));
  Button button_59 (.out(button_59_out));
  Button button_60 (.out(button_60_out));
  Button button_61 (.out(button_61_out));
  Button button_62 (.out(button_62_out));
  // RGBLED rgbled_16: pin names not known; wires that end beside it: rgbled_16_p1
  // RGBLED rgbled_17: pin names not known; wires that end beside it: rgbled_17_p1, rgbled_17_p2
  // RGBLED rgbled_18: pin names not known; wires that end beside it: rgbled_18_p1, rgbled_18_p2
  // RGBLED rgbled_19: pin names not known; wires that end beside it: rgbled_19_p1
  // RGBLED rgbled_20: pin names not known; wires that end beside it: rgbled_20_p1, rgbled_20_p2
  // RGBLED rgbled_21: pin names not known; wires that end beside it: rgbled_21_p1, rgbled_21_p2
  // RGBLED rgbled_22: pin names not known; wires that end beside it: rgbled_22_p1
  // RGBLED rgbled_23: pin names not known; wires that end beside it: rgbled_23_p1, rgbled_23_p2
  // RGBLED rgbled_24: pin names not known; wires that end beside it: rgbled_24_p1, rgbled_24_p2
  // RGBLED rgbled_25: pin names not known; wires that end beside it: rgbled_25_p1
  Button C (.out(C_out));
  Button Gb (.out(Gb_out));
  Button G (.out(G_out));
  Button button_63 (.out(button_63_out));
  Button button_64 (.out(button_64_out));
  Button button_65 (.out(button_65_out));
  Button button_66 (.out(button_66_out));
  // RGBLED rgbled_26: pin names not known; wires that end beside it: rgbled_26_p1, rgbled_26_p2
  // RGBLED rgbled_27: pin names not known; wires that end beside it: rgbled_27_p1
  // RGBLED rgbled_28: pin names not known; wires that end beside it: rgbled_28_p1, rgbled_28_p2
  // RGBLED rgbled_29: pin names not known; wires that end beside it: rgbled_29_p1, rgbled_29_p2
  Button Db (.out(Db_out));
  Button D (.out(D_out));
  Button button_67 (.out(button_67_out));
  Button button_68 (.out(button_68_out));
  Button button_69 (.out(button_69_out));
  Button button_70 (.out(button_70_out));
  Button button_71 (.out(button_71_out));
  Button button_72 (.out(button_72_out));
  Button button_73 (.out(button_73_out));
  Button button_74 (.out(button_74_out));
  Note_Trainer_circ note_trainer_circ_1 (
    .C(C_out), .Db(Db_out), .D(D_out), .Eb(Eb_out), .E(E_out), .F(F_out), .Gb(Gb_out), .G(G_out),
    .Ab(Ab_out), .A(A_out), .Bb(Bb_out), .B(B_out), .Reset_Score(Reset_Score_out), .Volume(Volume),
    .Score(out_4), .C2(rgbled_8_p1), .Db2(rgbled_7_p1), .Eb2(rgbled_15_p2), .E2(rgbled_15_p1),
    .F2(rgbled_25_p1), .Gb2(rgbled_24_p2), .G2(rgbled_24_p1), .Ab2(rgbled_29_p2), .A2(rgbled_29_p1),
    .Bb2(rgbled_6_p2), .B2(rgbled_6_p1), .C3(rgbled_5_p1), .Db3(rgbled_14_p2), .D3(rgbled_14_p1),
    .Eb3(rgbled_23_p2), .E3(rgbled_23_p1), .F3(rgbled_22_p1), .Gb3(rgbled_28_p2), .G3(rgbled_28_p1),
    .Ab3(rgbled_4_p2), .A3(rgbled_4_p1), .Bb3(rgbled_13_p2), .B3(rgbled_13_p1), .C4(rgbled_12_p1),
    .Db4(rgbled_21_p2), .D4(rgbled_21_p1), .Eb4(rgbled_20_p2), .E4(rgbled_20_p1), .F4(rgbled_27_p1),
    .Gb4(rgbled_3_p2), .G4(rgbled_3_p1), .Ab4(rgbled_11_p2), .A4(rgbled_11_p1), .Bb4(rgbled_10_p2),
    .B4(rgbled_10_p1), .C5(rgbled_19_p1), .Db5(rgbled_18_p2), .D5(rgbled_18_p1), .Eb5(rgbled_26_p2),
    .E5(rgbled_26_p1), .F5(rgbled_2_p1), .Gb5(rgbled_1_p2), .G5(rgbled_1_p1), .Ab5(rgbled_9_p2),
    .A5(rgbled_9_p1), .Bb5(rgbled_17_p2), .B5(rgbled_17_p1), .C6(rgbled_16_p1));  // open: D2
  Button button_75 (.out(button_75_out));
  Button button_76 (.out(button_76_out));
  Button button_77 (.out(button_77_out));
  Button button_78 (.out(button_78_out));
  Button button_79 (.out(button_79_out));
  Button button_80 (.out(button_80_out));
  Button button_81 (.out(button_81_out));
  Button button_82 (.out(button_82_out));
  Button button_83 (.out(button_83_out));
  Button button_84 (.out(button_84_out));
  Button button_85 (.out(button_85_out));
  Button button_86 (.out(button_86_out));
  Button button_87 (.out(button_87_out));
  Button button_88 (.out(button_88_out));
  Button button_89 (.out(button_89_out));
  Button button_90 (.out(button_90_out));
  Button button_91 (.out(button_91_out));
  Button button_92 (.out(button_92_out));
  Button button_93 (.out(button_93_out));
  Button button_94 (.out(button_94_out));
  Button button_95 (.out(button_95_out));
  Button button_96 (.out(button_96_out));
  Button button_97 (.out(button_97_out));
  Button button_98 (.out(button_98_out));
  Button button_99 (.out(button_99_out));
  Button button_100 (.out(button_100_out));
  Button button_101 (.out(button_101_out));
  Button button_102 (.out(button_102_out));
  Button button_103 (.out(button_103_out));
  Button button_104 (.out(button_104_out));
  Button button_105 (.out(button_105_out));
  Button button_106 (.out(button_106_out));
  Button button_107 (.out(button_107_out));
  Button button_108 (.out(button_108_out));

  // Notes on the sheet:
  //   0,0 Sine
  //   1,1 Saw
  //   0,1 Square*
  //   1,0 Triangle
  //   Red is Natural
  //   Green is Flat
endmodule

module Listen (
  input  [6:0] in_1,
  input  A,
  input  Bb,
  input  B,
  input  C,
  input  Db,
  input  D,
  input  Eb,
  input  E,
  input  F,
  input  Gb,
  input  G,
  input  Ab
);

  wire Aeolian_out, Dorian_out, Harmonic_Minor_out, Ionian_out, Locrian_out, Lydian_out, Major_Blues_out,
       Major_Pentatonic_out, Melodic_Minor_out, Minor_Blues_out, Minor_Pentatonic_out, Mixolydian_out,
       Phrygian_out, Phyrgian_Dominant_out, priority_encoder_1_gs, scale_selector_1_buzz;
  wire [3:0] priority_encoder_1_out, register_1_q;
  wire [4:0] adder_1_out, scale_selector_1_out_15;
  wire [13:0] rom_1_data;

  Priority_Encoder #(.select(4)) priority_encoder_1 (
    .in0(A), .in1(Bb), .in2(B), .in3(C), .in4(Db), .in5(D), .in6(Eb), .in7(E), .in8(F), .in9(Gb), .in10(G),
    .in11(Ab), .in12(1'b0), .in13(1'b0), .in14(1'b0), .in15(1'b0), .out(priority_encoder_1_out),
    .gs(priority_encoder_1_gs));  // open: en_out, en_in
  Button Ionian (.out(Ionian_out));
  Button Dorian (.out(Dorian_out));
  Button Phrygian (.out(Phrygian_out));
  Button Lydian (.out(Lydian_out));
  Button Mixolydian (.out(Mixolydian_out));
  Button Aeolian (.out(Aeolian_out));
  Button Locrian (.out(Locrian_out));
  Button Harmonic_Minor (.out(Harmonic_Minor_out));
  Button Phyrgian_Dominant (.out(Phyrgian_Dominant_out));
  Button Major_Pentatonic (.out(Major_Pentatonic_out));
  Button Minor_Pentatonic (.out(Minor_Pentatonic_out));
  Button Major_Blues (.out(Major_Blues_out));
  Button Minor_Blues (.out(Minor_Blues_out));
  Button Melodic_Minor (.out(Melodic_Minor_out));
  Register #(.width(4)) register_1 (
    .D(priority_encoder_1_out), .en(1'b1), .clk(priority_encoder_1_gs), .Q(register_1_q));  // open: clr
  Scale_Selector scale_selector_1 (
    .Ionian(Ionian_out), .Dorian(Dorian_out), .Phyrgian(Phrygian_out), .Lydian(Lydian_out),
    .Mixolydian(Mixolydian_out), .Aeolian(Aeolian_out), .Locrian(Locrian_out),
    .Harmonic_Minor(Harmonic_Minor_out), .Phrygian_Dominant(Phyrgian_Dominant_out),
    .Major_Pentatonic(Major_Pentatonic_out), .Minor_Pentatonic(Minor_Pentatonic_out),
    .Major_Blues(Major_Blues_out), .Minor_Blues(Minor_Blues_out), .Melodic_Minor(Melodic_Minor_out),
    .out_15(scale_selector_1_out_15), .Buzz(scale_selector_1_buzz));
  Adder #(.width(5)) adder_1 (
    .a(scale_selector_1_out_15), .b({1'b0, register_1_q}), .out(adder_1_out));  // open: cin, cout
  ROM #(.addrWidth(5), .dataWidth(14)) rom_1 (.addr(adder_1_out), .data(rom_1_data));
  // Buzzer buzzer_1: pin names not known; wires that end beside it: rom_1_data, scale_selector_1_buzz, in_1

  // Notes on the sheet:
  //   contents of rom_1 (hex, n*v repeats v):
  //   1b8 1d2 1ee 20b 22a 24b 26e 293 2ba 2e4 310 33f 370 3a4 3dc 417 455 497 4dd 527 575 5c8 620 67d
endmodule

module Counter8 (
  input  in_1,
  output [3:0] out_2,
  output out_3
);

  wire and_1_out, and_2_out, and_3_out, clock_1_out, t_ff_5_q;

  Clock clock_1 (.out(clock_1_out));
  and and_1 (and_1_out, out_3, out_2[0]);
  and and_2 (and_2_out, and_1_out, out_2[1]);
  and and_3 (and_3_out, and_2_out, out_2[2]);
  T_Flip_Flop #(.trigger("falling")) t_ff_1 (
    .T(out_3), .clk(clock_1_out), .Q(out_2[0]), .reset(t_ff_5_q));  // open: Qn, preset
  T_Flip_Flop #(.trigger("falling")) t_ff_2 (
    .T(and_1_out), .clk(clock_1_out), .Q(out_2[1]), .reset(t_ff_5_q));  // open: Qn, preset
  T_Flip_Flop #(.trigger("falling")) t_ff_3 (
    .T(and_2_out), .clk(clock_1_out), .Q(out_2[2]), .reset(t_ff_5_q));  // open: Qn, preset
  T_Flip_Flop #(.trigger("falling")) t_ff_4 (
    .T(and_3_out), .clk(clock_1_out), .Q(out_2[3]), .reset(t_ff_5_q));  // open: Qn, preset
  T_Flip_Flop #(.trigger("falling")) t_ff_5 (
    .T(out_2[3]), .clk(clock_1_out), .Q(t_ff_5_q), .Qn(out_3), .reset(in_1));  // open: preset
endmodule

module Scale_Selector (
  input  Ionian,
  input  Dorian,
  input  Phyrgian,
  input  Lydian,
  input  Mixolydian,
  input  Aeolian,
  input  Locrian,
  input  Harmonic_Minor,
  input  Phrygian_Dominant,
  input  Major_Pentatonic,
  input  Minor_Pentatonic,
  input  Major_Blues,
  input  Minor_Blues,
  input  Melodic_Minor,
  output [4:0] out_15,
  output Buzz
);

  wire clock_1_out, comparator_1_eq, counter6_1_out_3, counter7_1_out_3, counter8_1_out_3, counter16_1_out_3,
       d_ff_1_q, priority_encoder_1_gs;
  wire [2:0] counter6_1_out_2, counter7_1_out_2;
  wire [3:0] counter8_1_out_2, priority_encoder_1_out, register_1_q;
  wire [4:0] adder_1_out, counter16_1_out_2, multiplexer_1_out, multiplexer_3_out, multiplexer_4_out,
       rom_1_data, rom_2_data, rom_3_data, rom_4_data, rom_5_data, rom_6_data, rom_7_data, rom_8_data,
       rom_9_data, rom_10_data, rom_11_data, rom_12_data, rom_13_data, rom_14_data, subtractor_1_out;

  Priority_Encoder #(.select(4)) priority_encoder_1 (
    .in0(Ionian), .in1(Dorian), .in2(Phyrgian), .in3(Lydian), .in4(Mixolydian), .in5(Aeolian), .in6(Locrian),
    .in7(Harmonic_Minor), .in8(Phrygian_Dominant), .in9(Major_Pentatonic), .in10(Minor_Pentatonic),
    .in11(Major_Blues), .in12(Minor_Blues), .in13(Melodic_Minor), .out(priority_encoder_1_out),
    .gs(priority_encoder_1_gs));  // open: in14, in15, en_out, en_in
  Counter7 counter7_1 (.in_1(priority_encoder_1_gs), .out_2(counter7_1_out_2), .out_3(counter7_1_out_3));
  Counter16 counter16_1 (.in_1(priority_encoder_1_gs), .out_2(counter16_1_out_2), .out_3(counter16_1_out_3));
  Register #(.width(4)) register_1 (
    .D(priority_encoder_1_out), .en(1'b1), .clk(priority_encoder_1_gs), .Q(register_1_q));  // open: clr
  Counter6 counter6_1 (.in_1(priority_encoder_1_gs), .out_2(counter6_1_out_2), .out_3(counter6_1_out_3));
  Counter8 counter8_1 (.in_1(priority_encoder_1_gs), .out_2(counter8_1_out_2), .out_3(counter8_1_out_3));
  Multiplexer #(.select(4), .width(5)) multiplexer_1 (
    .in0({1'b0, counter8_1_out_2}), .in1({1'b0, counter8_1_out_2}), .in2({1'b0, counter8_1_out_2}),
    .in3({1'b0, counter8_1_out_2}), .in4({1'b0, counter8_1_out_2}), .in5({1'b0, counter8_1_out_2}),
    .in6({1'b0, counter8_1_out_2}), .in7({1'b0, counter8_1_out_2}), .in8({1'b0, counter8_1_out_2}),
    .in9({2'b00, counter6_1_out_2}), .in10({2'b00, counter6_1_out_2}), .in11({2'b00, counter7_1_out_2}),
    .in12({2'b00, counter7_1_out_2}), .in13(counter16_1_out_2), .out(multiplexer_1_out), .sel(register_1_q));  // open: in14, in15
  Multiplexer #(.select(4)) multiplexer_2 (
    .in0(counter8_1_out_3), .in1(counter8_1_out_3), .in2(counter8_1_out_3), .in3(counter8_1_out_3),
    .in4(counter8_1_out_3), .in5(counter8_1_out_3), .in6(counter8_1_out_3), .in7(counter8_1_out_3),
    .in8(counter8_1_out_3), .in9(counter6_1_out_3), .in10(counter6_1_out_3), .in11(counter7_1_out_3),
    .in12(counter7_1_out_3), .in13(counter16_1_out_3), .out(Buzz), .sel(register_1_q));  // open: in14, in15
  ROM #(.addrWidth(5), .dataWidth(5)) rom_1 (.addr(multiplexer_1_out), .data(rom_1_data));
  ROM #(.addrWidth(5), .dataWidth(5)) rom_2 (.addr(multiplexer_1_out), .data(rom_2_data));
  ROM #(.addrWidth(5), .dataWidth(5)) rom_3 (.addr(multiplexer_1_out), .data(rom_3_data));
  ROM #(.addrWidth(5), .dataWidth(5)) rom_4 (.addr(multiplexer_1_out), .data(rom_4_data));
  ROM #(.addrWidth(5), .dataWidth(5)) rom_5 (.addr(multiplexer_1_out), .data(rom_5_data));
  ROM #(.addrWidth(5), .dataWidth(5)) rom_6 (.addr(multiplexer_1_out), .data(rom_6_data));
  ROM #(.addrWidth(5), .dataWidth(5)) rom_7 (.addr(multiplexer_1_out), .data(rom_7_data));
  ROM #(.addrWidth(5), .dataWidth(5)) rom_8 (.addr(multiplexer_1_out), .data(rom_8_data));
  ROM #(.addrWidth(5), .dataWidth(5)) rom_9 (.addr(multiplexer_1_out), .data(rom_9_data));
  ROM #(.addrWidth(5), .dataWidth(5)) rom_10 (.addr(multiplexer_1_out), .data(rom_10_data));
  ROM #(.addrWidth(5), .dataWidth(5)) rom_11 (.addr(multiplexer_1_out), .data(rom_11_data));
  ROM #(.addrWidth(5), .dataWidth(5)) rom_12 (.addr(multiplexer_1_out), .data(rom_12_data));
  ROM #(.addrWidth(5), .dataWidth(5)) rom_13 (.addr(multiplexer_1_out), .data(rom_13_data));
  ROM #(.addrWidth(5), .dataWidth(5)) rom_14 (.addr(multiplexer_1_out), .data(rom_14_data));
  Multiplexer #(.select(4), .width(5)) multiplexer_3 (
    .in0(rom_1_data), .in1(rom_2_data), .in2(rom_3_data), .in3(rom_4_data), .in4(rom_5_data),
    .in5(rom_6_data), .in6(rom_7_data), .in7(rom_8_data), .in8(rom_9_data), .in9(rom_10_data),
    .in10(rom_11_data), .in11(rom_12_data), .in12(rom_13_data), .in13(rom_14_data), .out(multiplexer_3_out),
    .sel(register_1_q));  // open: in14, in15
  Adder #(.width(5)) adder_1 (.a(multiplexer_3_out), .b(out_15), .out(adder_1_out));  // open: cin, cout
  Subtractor #(.width(5)) subtractor_1 (.a(out_15), .b(multiplexer_3_out), .out(subtractor_1_out));  // open: bin, bout
  Multiplexer #(.width(5)) multiplexer_4 (
    .in0(adder_1_out), .in1(subtractor_1_out), .out(multiplexer_4_out), .sel(d_ff_1_q));
  Comparator #(.mode("unsigned"), .width(5)) comparator_1 (
    .a(5'b01100), .b(out_15), .eq(comparator_1_eq));  // open: gt, lt
  Clock clock_1 (.out(clock_1_out));
  D_Flip_Flop d_ff_1 (
    .clk(clock_1_out), .Q(d_ff_1_q), .preset(comparator_1_eq), .reset(priority_encoder_1_gs));  // open: D, Qn
  Register #(.width(5)) register_2 (
    .D(multiplexer_4_out), .en(1'b1), .clk(clock_1_out), .Q(out_15), .clr(priority_encoder_1_gs));

  // Notes on the sheet:
  //   contents of rom_1 (hex, n*v repeats v):
  //   0 2 2 1 2 2 2 1
  //   contents of rom_2 (hex, n*v repeats v):
  //   0 2 1 2 2 2 1 2
  //   contents of rom_3 (hex, n*v repeats v):
  //   0 1 2 2 2 1 2 2
  //   contents of rom_4 (hex, n*v repeats v):
  //   0 2 2 2 1 2 2 1
  //   contents of rom_5 (hex, n*v repeats v):
  //   0 2 2 1 2 2 1 2
  //   contents of rom_6 (hex, n*v repeats v):
  //   0 2 1 2 2 1 2 2
  //   contents of rom_7 (hex, n*v repeats v):
  //   0 1 2 2 1 2 2 2
  //   contents of rom_8 (hex, n*v repeats v):
  //   0 2 1 2 2 1 3 1
  //   contents of rom_9 (hex, n*v repeats v):
  //   0 1 3 1 2 1 2 2
  //   contents of rom_10 (hex, n*v repeats v):
  //   0 2 2 3 2 3
  //   contents of rom_11 (hex, n*v repeats v):
  //   0 3 2 2 3 2
  //   contents of rom_12 (hex, n*v repeats v):
  //   0 2 1 1 3 2 3
  //   contents of rom_13 (hex, n*v repeats v):
  //   0 3 2 1 1 3 2
  //   contents of rom_14 (hex, n*v repeats v):
  //   0 2 1 4*2 1 2 2 1 2 2 1 2
endmodule

module Counter6 (
  input  in_1,
  output [2:0] out_2,
  output out_3
);

  wire and_1_out, and_2_out, and_3_out, clock_1_out, t_ff_4_q;

  and and_1 (and_1_out, out_3, out_2[0]);
  and and_2 (and_2_out, and_1_out, out_2[1]);
  Clock clock_1 (.out(clock_1_out));
  T_Flip_Flop #(.trigger("falling")) t_ff_1 (
    .T(out_3), .clk(clock_1_out), .Q(out_2[0]), .reset(t_ff_4_q));  // open: Qn, preset
  T_Flip_Flop #(.trigger("falling")) t_ff_2 (
    .T(and_1_out), .clk(clock_1_out), .Q(out_2[1]), .reset(t_ff_4_q));  // open: Qn, preset
  T_Flip_Flop #(.trigger("falling")) t_ff_3 (
    .T(and_2_out), .clk(clock_1_out), .Q(out_2[2]), .reset(t_ff_4_q));  // open: Qn, preset
  and and_3 (and_3_out, out_2[2], out_2[1]);
  T_Flip_Flop #(.trigger("falling")) t_ff_4 (
    .T(and_3_out), .clk(clock_1_out), .Q(t_ff_4_q), .Qn(out_3), .reset(in_1));  // open: preset
endmodule

module Counter7 (
  input  in_1,
  output [2:0] out_2,
  output out_3
);

  wire and_1_out, and_2_out, and_3_out, clock_1_out, t_ff_4_q;

  Clock clock_1 (.out(clock_1_out));
  and and_1 (and_1_out, out_3, out_2[0]);
  and and_2 (and_2_out, and_1_out, out_2[1]);
  T_Flip_Flop #(.trigger("falling")) t_ff_1 (
    .T(out_3), .clk(clock_1_out), .Q(out_2[0]), .reset(t_ff_4_q));  // open: Qn, preset
  T_Flip_Flop #(.trigger("falling")) t_ff_2 (
    .T(and_1_out), .clk(clock_1_out), .Q(out_2[1]), .reset(t_ff_4_q));  // open: Qn, preset
  T_Flip_Flop #(.trigger("falling")) t_ff_3 (
    .T(and_2_out), .clk(clock_1_out), .Q(out_2[2]), .reset(t_ff_4_q));  // open: Qn, preset
  and and_3 (and_3_out, out_2[2], out_2[1], out_2[0]);
  T_Flip_Flop #(.trigger("falling")) t_ff_4 (
    .T(and_3_out), .clk(clock_1_out), .Q(t_ff_4_q), .Qn(out_3), .reset(in_1));  // open: preset
endmodule

module Counter16 (
  input  in_1,
  output [4:0] out_2,
  output out_3
);

  wire and_1_out, and_2_out, and_3_out, and_4_out, clock_1_out, t_ff_6_q;

  Clock clock_1 (.out(clock_1_out));
  and and_1 (and_1_out, out_3, out_2[0]);
  and and_2 (and_2_out, and_1_out, out_2[1]);
  and and_3 (and_3_out, and_2_out, out_2[2]);
  and and_4 (and_4_out, and_3_out, out_2[3]);
  T_Flip_Flop #(.trigger("falling")) t_ff_1 (
    .T(and_4_out), .clk(clock_1_out), .Q(out_2[4]), .reset(t_ff_6_q));  // open: Qn, preset
  T_Flip_Flop #(.trigger("falling")) t_ff_2 (
    .T(out_3), .clk(clock_1_out), .Q(out_2[0]), .reset(t_ff_6_q));  // open: Qn, preset
  T_Flip_Flop #(.trigger("falling")) t_ff_3 (
    .T(and_1_out), .clk(clock_1_out), .Q(out_2[1]), .reset(t_ff_6_q));  // open: Qn, preset
  T_Flip_Flop #(.trigger("falling")) t_ff_4 (
    .T(and_2_out), .clk(clock_1_out), .Q(out_2[2]), .reset(t_ff_6_q));  // open: Qn, preset
  T_Flip_Flop #(.trigger("falling")) t_ff_5 (
    .T(and_3_out), .clk(clock_1_out), .Q(out_2[3]), .reset(t_ff_6_q));  // open: Qn, preset
  T_Flip_Flop #(.trigger("falling")) t_ff_6 (
    .T(out_2[4]), .clk(clock_1_out), .Q(t_ff_6_q), .Qn(out_3), .reset(in_1));  // open: preset
endmodule
